// Logisim project master.circ as structural Verilog: 32 circuits, main circuit main
module main (
);

  wire alumicrocoded_1_fc, alumicrocoded_1_fo, alumicrocoded_1_fs, alumicrocoded_1_fz, clock_1_out,
       clock_2_out, clock_3_out, clock_4_out, clock_5_out, clock_6_out, clock_7_out, control_1_mask_restore,
       control_1_mask_save, control_1_oregwe, io_1_ogpu_clear, io_1_okeyread, keyboard_1_avail,
       memory_controller_1_gpu_we, registerfile_1_busy, registerfile_1_int;
  wire [1:0] control_1_oioop;
  wire [2:0] control_1_oioaddr, control_1_omemop, registerfile_1_int_id;
  wire [3:0] control_1_oaluop, control_1_oregid;
  wire [6:0] keyboard_1_data, memory_controller_1_gpu_data;
  wire [7:0] io_1_obusyassert, io_1_ointasssert;
  wire [15:0] alumicrocoded_1_dout, control_1_oiobus, control_1_oregbus, io_1_oled,
       memory_controller_1_databusout;
  wire [15:7] memory_controller_1_gpu_data_2;

  Clock clock_1 (.out(clock_1_out));
  TTY tty_1 (
    .data(memory_controller_1_gpu_data), .clk(clock_1_out), .we(memory_controller_1_gpu_we),
    .clr(io_1_ogpu_clear));
  memory_controller memory_controller_1 (
    .DataBUSin(memory_controller_1_databusout), .CLK(clock_2_out), .MODE(control_1_omemop),
    .GPU_WE(memory_controller_1_gpu_we),
    .GPU_DATA({memory_controller_1_gpu_data_2, memory_controller_1_gpu_data}),
    .DataBUSout(memory_controller_1_databusout));  // open: GPU_ADDR
  Clock clock_2 (.out(clock_2_out));
  Clock clock_3 (.out(clock_3_out));
  Clock clock_4 (.out(clock_4_out));
  aluMICROCODED alumicrocoded_1 (
    .OP(control_1_oaluop), .CLK(clock_4_out), .Din(alumicrocoded_1_dout), .Dout(alumicrocoded_1_dout),
    .FS(alumicrocoded_1_fs), .FO(alumicrocoded_1_fo), .FC(alumicrocoded_1_fc), .FZ(alumicrocoded_1_fz));
  control control_1 (
    .ialubus(alumicrocoded_1_dout), .ifs(alumicrocoded_1_fs), .ifo(alumicrocoded_1_fo),
    .ifc(alumicrocoded_1_fc), .ifz(alumicrocoded_1_fz), .imembus(memory_controller_1_databusout),
    .iregbus(control_1_oregbus), .iint(registerfile_1_int), .iintid(registerfile_1_int_id),
    .ibusy(registerfile_1_busy), .iiobus(control_1_oiobus), .CLK(clock_3_out), .oregwe(control_1_oregwe),
    .omemop(control_1_omemop), .oioaddr(control_1_oioaddr), .oaluop(control_1_oaluop),
    .oalubus(alumicrocoded_1_dout), .omembus(memory_controller_1_databusout), .oregbus(control_1_oregbus),
    .oregid(control_1_oregid), .mask_save(control_1_mask_save), .mask_restore(control_1_mask_restore),
    .oioop(control_1_oioop), .oiobus(control_1_oiobus));
  IO io_1 (
    .ikeychar(keyboard_1_data), .CLK(clock_7_out), .ikeyaval(keyboard_1_avail), .iiobus(control_1_oiobus),
    .iioid(control_1_oioaddr), .iiocmd(control_1_oioop), .ointasssert(io_1_ointasssert),
    .obusyassert(io_1_obusyassert), .oiobus(control_1_oiobus), .ogpu_clear(io_1_ogpu_clear),
    .okeyread(io_1_okeyread), .oled(io_1_oled));
  Clock clock_5 (.out(clock_5_out));
  Keyboard keyboard_1 (
    .clk(clock_5_out), .re(io_1_okeyread), .clr(1'b0), .avail(keyboard_1_avail), .data(keyboard_1_data));
  Clock clock_6 (.out(clock_6_out));
  Clock clock_7 (.out(clock_7_out));
  registerfile registerfile_1 (
    .mask_save(control_1_mask_save), .mask_restore(control_1_mask_restore), .IO_BUSY(io_1_obusyassert),
    .IO_INT(io_1_ointasssert), .REG_SEL(control_1_oregid), .data(control_1_oregbus), .SET(control_1_oregwe),
    .CLK(clock_6_out), .BUSY(registerfile_1_busy), .REG_OUT(control_1_oregbus),
    .INT_ID(registerfile_1_int_id), .INT(registerfile_1_int));
  // LedBar #(.inputtype("row"), .matrixcols(16)) ledbar_1: pin names not known; wires that end beside it: io_1_oled
endmodule

module memory_controller (
  input  [15:0] DataBUSin,
  input  [2:0] MODE,
  input  CLK,
  output [14:0] GPU_ADDR,
  output [15:0] GPU_DATA,
  output [15:0] DataBUSout,
  output GPU_WE
);

  wire \bit , muxnOE_n, n7404_1_pin2, n7404_1_pin4, n7404_1_pin6, n7404_1_pin10, n7404_1_pin12, n7404_2_pin6,
       n7404_2_pin10, n7404_2_pin12, n7408_1_pin11, n7408_2_pin5, n7408_2_pin6, n7408_2_pin8, n7408_2_pin11,
       n74283_1_pin3, n74283_1_pin5, n74283_1_pin7, n74283_1_pin12, n74283_1_pin14, n74283_2_pin3,
       n74283_2_pin5, n74283_2_pin7, n74283_2_pin12, n74283_2_pin14, n74283_3_pin3, n74283_3_pin5,
       n74283_3_pin7, n74283_3_pin12, n74283_3_pin14, n74283_4_pin3, n74283_4_pin5, n74283_4_pin7,
       n74283_4_pin12, n74283_4_pin14, nOutput_enable, output_enable, t74245_9_b1out, t74245_9_b2out,
       t74245_9_b3out, t74245_9_b4out, t74245_9_b5out, t74245_9_b6out, t74245_9_b7out, t74245_9_b8out,
       t74245_11_a1out, t74245_11_a2out, t74245_11_a3out, t74245_11_a4out, t74245_11_a5out, t74245_11_a6out,
       t74245_11_a7out, t74245_11_a8out, write_enable;
  wire [15:0] at28c256_rom_1_1_o0, n74283_4_pin4, rom_1_data, t74245_3_b1out, t74245_7_b1out;

  T74245 t74245_1 (
    .A6in(DataBUSin[5]), .A7in(DataBUSin[6]), .A8in(DataBUSin[7]), .A1in(DataBUSin[0]), .A2in(DataBUSin[1]),
    .A3in(DataBUSin[2]), .A4in(DataBUSin[3]), .A5in(DataBUSin[4]), .DIR(1'b1), .nOE(output_enable),
    .B6in(GPU_DATA[5]), .B7in(GPU_DATA[6]), .B8in(GPU_DATA[7]), .B1in(GPU_DATA[0]), .B2in(GPU_DATA[1]),
    .B3in(GPU_DATA[2]), .B4in(GPU_DATA[3]), .B5in(GPU_DATA[4]), .B8out(GPU_DATA[7]), .B6out(GPU_DATA[5]),
    .B7out(GPU_DATA[6]), .B1out(GPU_DATA[0]), .B2out(GPU_DATA[1]), .B3out(GPU_DATA[2]), .B4out(GPU_DATA[3]),
    .B5out(GPU_DATA[4]));  // open: A6out, A7out, A8out, A1out, A2out, A3out, A4out, A5out
  T74245 t74245_2 (
    .A6in(DataBUSin[13]), .A7in(DataBUSin[14]), .A8in(DataBUSin[15]), .A1in(DataBUSin[8]),
    .A2in(DataBUSin[9]), .A3in(DataBUSin[10]), .A4in(DataBUSin[11]), .A5in(DataBUSin[12]), .DIR(1'b1),
    .nOE(output_enable), .B6in(GPU_DATA[13]), .B7in(GPU_DATA[14]), .B8in(GPU_DATA[15]), .B1in(GPU_DATA[8]),
    .B2in(GPU_DATA[9]), .B3in(GPU_DATA[10]), .B4in(GPU_DATA[11]), .B5in(GPU_DATA[12]), .B8out(GPU_DATA[15]),
    .B6out(GPU_DATA[13]), .B7out(GPU_DATA[14]), .B1out(GPU_DATA[8]), .B2out(GPU_DATA[9]),
    .B3out(GPU_DATA[10]), .B4out(GPU_DATA[11]), .B5out(GPU_DATA[12]));  // open: A6out, A7out, A8out, A1out, A2out, A3out, A4out, A5out
  _7404 u_7404_1 (
    .pin1(MODE[0]), .pin2(n7404_1_pin2), .pin3(MODE[1]), .pin4(n7404_1_pin4), .pin5(\bit ),
    .pin6(n7404_1_pin6), .pin13(MODE[1]), .pin12(n7404_1_pin12), .pin11(MODE[0]), .pin10(n7404_1_pin10),
    .pin9(output_enable), .pin8(nOutput_enable));
  _7408 u_7408_1 (
    .pin1(MODE[0]), .pin2(MODE[2]), .pin3(output_enable), .pin4(write_enable), .pin5(n7404_1_pin6),
    .pin6(GPU_WE), .pin13(n7404_1_pin2), .pin12(n7404_1_pin4), .pin11(n7408_1_pin11), .pin10(n7408_1_pin11),
    .pin9(MODE[2]), .pin8(write_enable));
  T74245 t74245_3 (
    .A6in(GPU_DATA[5]), .A7in(GPU_DATA[6]), .A8in(GPU_DATA[7]), .A1in(GPU_DATA[0]), .A2in(GPU_DATA[1]),
    .A3in(GPU_DATA[2]), .A4in(GPU_DATA[3]), .A5in(GPU_DATA[4]), .DIR(1'b1), .nOE(MODE[0]),
    .B6in(t74245_3_b1out[5]), .B7in(t74245_3_b1out[6]), .B8in(t74245_3_b1out[7]), .B1in(t74245_3_b1out[0]),
    .B2in(t74245_3_b1out[1]), .B3in(t74245_3_b1out[2]), .B4in(t74245_3_b1out[3]), .B5in(t74245_3_b1out[4]),
    .B8out(t74245_3_b1out[7]), .B6out(t74245_3_b1out[5]), .B7out(t74245_3_b1out[6]),
    .B1out(t74245_3_b1out[0]), .B2out(t74245_3_b1out[1]), .B3out(t74245_3_b1out[2]),
    .B4out(t74245_3_b1out[3]), .B5out(t74245_3_b1out[4]));  // open: A6out, A7out, A8out, A1out, A2out, A3out, A4out, A5out
  T74245 t74245_4 (
    .A6in(t74245_3_b1out[5]), .A7in(t74245_3_b1out[6]), .A8in(t74245_3_b1out[7]), .A1in(t74245_3_b1out[0]),
    .A2in(t74245_3_b1out[1]), .A3in(t74245_3_b1out[2]), .A4in(t74245_3_b1out[3]), .A5in(t74245_3_b1out[4]),
    .DIR(1'b0), .nOE(n7404_1_pin10), .B6in(n74283_4_pin4[5]), .B7in(n74283_4_pin4[6]),
    .B8in(n74283_4_pin4[7]), .B1in(n74283_4_pin4[0]), .B2in(n74283_4_pin4[1]), .B3in(n74283_4_pin4[2]),
    .B4in(n74283_4_pin4[3]), .B5in(n74283_4_pin4[4]), .A6out(t74245_3_b1out[5]), .A7out(t74245_3_b1out[6]),
    .A8out(t74245_3_b1out[7]), .A1out(t74245_3_b1out[0]), .A2out(t74245_3_b1out[1]),
    .A3out(t74245_3_b1out[2]), .A4out(t74245_3_b1out[3]), .A5out(t74245_3_b1out[4]));  // open: B8out, B6out, B7out, B1out, B2out, B3out, B4out, B5out
  T74245 t74245_5 (
    .A6in(t74245_3_b1out[13]), .A7in(t74245_3_b1out[14]), .A8in(t74245_3_b1out[15]),
    .A1in(t74245_3_b1out[8]), .A2in(t74245_3_b1out[9]), .A3in(t74245_3_b1out[10]), .A4in(t74245_3_b1out[11]),
    .A5in(t74245_3_b1out[12]), .DIR(1'b0), .nOE(n7404_1_pin10), .B6in(n74283_4_pin4[13]),
    .B7in(n74283_4_pin4[14]), .B8in(n74283_4_pin4[15]), .B1in(n74283_4_pin4[8]), .B2in(n74283_4_pin4[9]),
    .B3in(n74283_4_pin4[10]), .B4in(n74283_4_pin4[11]), .B5in(n74283_4_pin4[12]), .A6out(t74245_3_b1out[13]),
    .A7out(t74245_3_b1out[14]), .A8out(t74245_3_b1out[15]), .A1out(t74245_3_b1out[8]),
    .A2out(t74245_3_b1out[9]), .A3out(t74245_3_b1out[10]), .A4out(t74245_3_b1out[11]),
    .A5out(t74245_3_b1out[12]));  // open: B8out, B6out, B7out, B1out, B2out, B3out, B4out, B5out
  T74245 t74245_6 (
    .A6in(GPU_DATA[13]), .A7in(GPU_DATA[14]), .A8in(GPU_DATA[15]), .A1in(GPU_DATA[8]), .A2in(GPU_DATA[9]),
    .A3in(GPU_DATA[10]), .A4in(GPU_DATA[11]), .A5in(GPU_DATA[12]), .DIR(1'b1), .nOE(MODE[0]),
    .B6in(t74245_3_b1out[13]), .B7in(t74245_3_b1out[14]), .B8in(t74245_3_b1out[15]),
    .B1in(t74245_3_b1out[8]), .B2in(t74245_3_b1out[9]), .B3in(t74245_3_b1out[10]), .B4in(t74245_3_b1out[11]),
    .B5in(t74245_3_b1out[12]), .B8out(t74245_3_b1out[15]), .B6out(t74245_3_b1out[13]),
    .B7out(t74245_3_b1out[14]), .B1out(t74245_3_b1out[8]), .B2out(t74245_3_b1out[9]),
    .B3out(t74245_3_b1out[10]), .B4out(t74245_3_b1out[11]), .B5out(t74245_3_b1out[12]));  // open: A6out, A7out, A8out, A1out, A2out, A3out, A4out, A5out
  _74377 u_74377_1 (
    .pin1(n7404_1_pin12), .pin2(GPU_ADDR[0]), .pin3(t74245_3_b1out[0]), .pin4(t74245_3_b1out[1]),
    .pin5(GPU_ADDR[1]), .pin6(GPU_ADDR[2]), .pin7(t74245_3_b1out[2]), .pin8(t74245_3_b1out[3]),
    .pin9(GPU_ADDR[3]), .pin19(GPU_ADDR[7]), .pin18(t74245_3_b1out[7]), .pin17(t74245_3_b1out[6]),
    .pin16(GPU_ADDR[6]), .pin15(GPU_ADDR[5]), .pin14(t74245_3_b1out[5]), .pin13(t74245_3_b1out[4]),
    .pin12(GPU_ADDR[4]), .pin11(CLK));
  _74377 u_74377_2 (
    .pin1(n7404_1_pin12), .pin2(GPU_ADDR[8]), .pin3(t74245_3_b1out[8]), .pin4(t74245_3_b1out[9]),
    .pin5(GPU_ADDR[9]), .pin6(GPU_ADDR[10]), .pin7(t74245_3_b1out[10]), .pin8(t74245_3_b1out[11]),
    .pin9(GPU_ADDR[11]), .pin19(\bit ), .pin18(t74245_3_b1out[15]), .pin17(t74245_3_b1out[14]),
    .pin16(GPU_ADDR[14]), .pin15(GPU_ADDR[13]), .pin14(t74245_3_b1out[13]), .pin13(t74245_3_b1out[12]),
    .pin12(GPU_ADDR[12]), .pin11(CLK));
  _7408 u_7408_2 (
    .pin4(CLK), .pin5(n7408_2_pin5), .pin6(n7408_2_pin6), .pin13(write_enable), .pin12(\bit ),
    .pin11(n7408_2_pin11), .pin10(n7408_2_pin11), .pin9(n7408_2_pin6), .pin8(n7408_2_pin8));  // open: pin1, pin2, pin3
  _7404 u_7404_2 (
    .pin3(\bit ), .pin4(muxnOE_n), .pin5(n7408_2_pin8), .pin6(n7404_2_pin6), .pin13(CLK),
    .pin12(n7404_2_pin12), .pin11(n7404_2_pin12), .pin10(n7404_2_pin10), .pin9(n7404_2_pin10),
    .pin8(n7408_2_pin5));  // open: pin1, pin2
  _74283 u_74283_1 (
    .pin1(n74283_4_pin4[13]), .pin2(GPU_ADDR[13]), .pin3(n74283_1_pin3), .pin4(n74283_4_pin4[12]),
    .pin5(n74283_1_pin5), .pin6(GPU_ADDR[12]), .pin7(n74283_1_pin7), .pin15(GPU_ADDR[14]),
    .pin14(n74283_1_pin14), .pin13(n74283_4_pin4[14]), .pin12(n74283_1_pin12), .pin11(\bit ),
    .pin10(n74283_4_pin4[15]));  // open: pin9
  _74283 u_74283_2 (
    .pin1(n74283_4_pin4[9]), .pin2(GPU_ADDR[9]), .pin3(n74283_2_pin3), .pin4(n74283_4_pin4[8]),
    .pin5(n74283_2_pin5), .pin6(GPU_ADDR[8]), .pin7(n74283_2_pin7), .pin15(GPU_ADDR[10]),
    .pin14(n74283_2_pin14), .pin13(n74283_4_pin4[10]), .pin12(n74283_2_pin12), .pin11(GPU_ADDR[11]),
    .pin10(n74283_4_pin4[11]), .pin9(n74283_1_pin7));
  _74283 u_74283_3 (
    .pin1(n74283_4_pin4[5]), .pin2(GPU_ADDR[5]), .pin3(n74283_3_pin3), .pin4(n74283_4_pin4[4]),
    .pin5(n74283_3_pin5), .pin6(GPU_ADDR[4]), .pin7(n74283_3_pin7), .pin15(GPU_ADDR[6]),
    .pin14(n74283_3_pin14), .pin13(n74283_4_pin4[6]), .pin12(n74283_3_pin12), .pin11(GPU_ADDR[7]),
    .pin10(n74283_4_pin4[7]), .pin9(n74283_2_pin7));
  _74283 u_74283_4 (
    .pin1(n74283_4_pin4[1]), .pin2(GPU_ADDR[1]), .pin3(n74283_4_pin3), .pin4(n74283_4_pin4[0]),
    .pin5(n74283_4_pin5), .pin6(GPU_ADDR[0]), .pin7(n74283_4_pin7), .pin15(GPU_ADDR[2]),
    .pin14(n74283_4_pin14), .pin13(n74283_4_pin4[2]), .pin12(n74283_4_pin12), .pin11(GPU_ADDR[3]),
    .pin10(n74283_4_pin4[3]), .pin9(n74283_3_pin7));
  AS7C1026B_RAM_1 as7c1026b_ram_1_1 (
    .A14(GPU_ADDR[14]), .A13(GPU_ADDR[13]), .A12(GPU_ADDR[12]), .A11(GPU_ADDR[11]), .A10(GPU_ADDR[10]),
    .A9(GPU_ADDR[9]), .A8(GPU_ADDR[8]), .A7(GPU_ADDR[7]), .A6(GPU_ADDR[6]), .A5(GPU_ADDR[5]),
    .A4(GPU_ADDR[4]), .A3(GPU_ADDR[3]), .A2(GPU_ADDR[2]), .A1(GPU_ADDR[1]), .A0(GPU_ADDR[0]), .nCE(1'b0),
    .nWE(n7404_2_pin6), .nOE(nOutput_enable), .nLB(1'b0), .nUB(1'b0), .IO15(GPU_DATA[15]),
    .IO14(GPU_DATA[14]), .IO13(GPU_DATA[13]), .IO12(GPU_DATA[12]), .IO11(GPU_DATA[11]), .IO10(GPU_DATA[10]),
    .IO9(GPU_DATA[9]), .IO8(GPU_DATA[8]), .IO7(GPU_DATA[7]), .IO6(GPU_DATA[6]), .A15(\bit ),
    .IO5(GPU_DATA[5]), .IO4(GPU_DATA[4]), .IO3(GPU_DATA[3]), .IO2(GPU_DATA[2]), .IO1(GPU_DATA[1]),
    .IO0(GPU_DATA[0]), .O15(GPU_DATA[15]), .O14(GPU_DATA[14]), .O13(GPU_DATA[13]), .O12(GPU_DATA[12]),
    .O11(GPU_DATA[11]), .O10(GPU_DATA[10]), .O9(GPU_DATA[9]), .O8(GPU_DATA[8]), .O7(GPU_DATA[7]),
    .O6(GPU_DATA[6]), .O5(GPU_DATA[5]), .O4(GPU_DATA[4]), .O3(GPU_DATA[3]), .O2(GPU_DATA[2]),
    .O1(GPU_DATA[1]), .O0(GPU_DATA[0]));
  ROM #(.addrWidth(16), .dataWidth(16)) rom_1 (.addr({\bit , GPU_ADDR}), .data(rom_1_data));
  AT28C256_ROM_1 at28c256_rom_1_1 (
    .A2(GPU_ADDR[2]), .A3(GPU_ADDR[3]), .A4(GPU_ADDR[4]), .A5(GPU_ADDR[5]), .A6(GPU_ADDR[6]),
    .A7(GPU_ADDR[7]), .A8(GPU_ADDR[8]), .A9(GPU_ADDR[9]), .A10(GPU_ADDR[10]), .A11(GPU_ADDR[11]),
    .A12(GPU_ADDR[12]), .A13(GPU_ADDR[13]), .A14(GPU_ADDR[14]), .nOE(1'b0), .nCE(1'b0), .A0(GPU_ADDR[0]),
    .A1(GPU_ADDR[1]), .O0(at28c256_rom_1_1_o0[0]), .O1(at28c256_rom_1_1_o0[1]), .O2(at28c256_rom_1_1_o0[2]),
    .O3(at28c256_rom_1_1_o0[3]), .O4(at28c256_rom_1_1_o0[4]), .O5(at28c256_rom_1_1_o0[5]),
    .O6(at28c256_rom_1_1_o0[6]), .O7(at28c256_rom_1_1_o0[7]));  // open: nWE
  AT28C256_ROM_2 at28c256_rom_2_1 (
    .A2(GPU_ADDR[2]), .A3(GPU_ADDR[3]), .A4(GPU_ADDR[4]), .A5(GPU_ADDR[5]), .A6(GPU_ADDR[6]),
    .A7(GPU_ADDR[7]), .A8(GPU_ADDR[8]), .A9(GPU_ADDR[9]), .A10(GPU_ADDR[10]), .A11(GPU_ADDR[11]),
    .A12(GPU_ADDR[12]), .A13(GPU_ADDR[13]), .A14(GPU_ADDR[14]), .nOE(1'b0), .nCE(1'b0), .A0(GPU_ADDR[0]),
    .A1(GPU_ADDR[1]), .O0(at28c256_rom_1_1_o0[8]), .O1(at28c256_rom_1_1_o0[9]), .O2(at28c256_rom_1_1_o0[10]),
    .O3(at28c256_rom_1_1_o0[11]), .O4(at28c256_rom_1_1_o0[12]), .O5(at28c256_rom_1_1_o0[13]),
    .O6(at28c256_rom_1_1_o0[14]), .O7(at28c256_rom_1_1_o0[15]));  // open: nWE
  T74245 t74245_7 (
    .A6in(GPU_DATA[5]), .A7in(GPU_DATA[6]), .A8in(GPU_DATA[7]), .A1in(GPU_DATA[0]), .A2in(GPU_DATA[1]),
    .A3in(GPU_DATA[2]), .A4in(GPU_DATA[3]), .A5in(GPU_DATA[4]), .DIR(1'b1), .nOE(n7408_2_pin8),
    .B6in(t74245_7_b1out[5]), .B7in(t74245_7_b1out[6]), .B8in(t74245_7_b1out[7]), .B1in(t74245_7_b1out[0]),
    .B2in(t74245_7_b1out[1]), .B3in(t74245_7_b1out[2]), .B4in(t74245_7_b1out[3]), .B5in(t74245_7_b1out[4]),
    .B8out(t74245_7_b1out[7]), .B6out(t74245_7_b1out[5]), .B7out(t74245_7_b1out[6]),
    .B1out(t74245_7_b1out[0]), .B2out(t74245_7_b1out[1]), .B3out(t74245_7_b1out[2]),
    .B4out(t74245_7_b1out[3]), .B5out(t74245_7_b1out[4]));  // open: A6out, A7out, A8out, A1out, A2out, A3out, A4out, A5out
  T74245 t74245_8 (
    .A6in(GPU_DATA[13]), .A7in(GPU_DATA[14]), .A8in(GPU_DATA[15]), .A1in(GPU_DATA[8]), .A2in(GPU_DATA[9]),
    .A3in(GPU_DATA[10]), .A4in(GPU_DATA[11]), .A5in(GPU_DATA[12]), .DIR(1'b1), .nOE(n7408_2_pin8),
    .B6in(t74245_7_b1out[13]), .B7in(t74245_7_b1out[14]), .B8in(t74245_7_b1out[15]),
    .B1in(t74245_7_b1out[8]), .B2in(t74245_7_b1out[9]), .B3in(t74245_7_b1out[10]), .B4in(t74245_7_b1out[11]),
    .B5in(t74245_7_b1out[12]), .B8out(t74245_7_b1out[15]), .B6out(t74245_7_b1out[13]),
    .B7out(t74245_7_b1out[14]), .B1out(t74245_7_b1out[8]), .B2out(t74245_7_b1out[9]),
    .B3out(t74245_7_b1out[10]), .B4out(t74245_7_b1out[11]), .B5out(t74245_7_b1out[12]));  // open: A6out, A7out, A8out, A1out, A2out, A3out, A4out, A5out
  T74245 t74245_9 (
    .A6in(rom_1_data[5]), .A7in(rom_1_data[6]), .A8in(rom_1_data[7]), .A1in(rom_1_data[0]),
    .A2in(rom_1_data[1]), .A3in(rom_1_data[2]), .A4in(rom_1_data[3]), .A5in(rom_1_data[4]), .DIR(1'b1),
    .nOE(\bit ), .B6in(t74245_9_b6out), .B7in(t74245_9_b7out), .B8in(t74245_9_b8out), .B1in(t74245_9_b1out),
    .B2in(t74245_9_b2out), .B3in(t74245_9_b3out), .B4in(t74245_9_b4out), .B5in(t74245_9_b5out),
    .A6out(rom_1_data[5]), .A7out(rom_1_data[6]), .A8out(rom_1_data[7]), .A1out(rom_1_data[0]),
    .A2out(rom_1_data[1]), .A3out(rom_1_data[2]), .A4out(rom_1_data[3]), .A5out(rom_1_data[4]),
    .B8out(t74245_9_b8out), .B6out(t74245_9_b6out), .B7out(t74245_9_b7out), .B1out(t74245_9_b1out),
    .B2out(t74245_9_b2out), .B3out(t74245_9_b3out), .B4out(t74245_9_b4out), .B5out(t74245_9_b5out));
  T74245 t74245_10 (
    .A6in(t74245_9_b6out), .A7in(t74245_9_b7out), .A8in(t74245_9_b8out), .A1in(t74245_9_b1out),
    .A2in(t74245_9_b2out), .A3in(t74245_9_b3out), .A4in(t74245_9_b4out), .A5in(t74245_9_b5out), .DIR(1'b0),
    .nOE(muxnOE_n), .B6in(t74245_7_b1out[5]), .B7in(t74245_7_b1out[6]), .B8in(t74245_7_b1out[7]),
    .B1in(t74245_7_b1out[0]), .B2in(t74245_7_b1out[1]), .B3in(t74245_7_b1out[2]), .B4in(t74245_7_b1out[3]),
    .B5in(t74245_7_b1out[4]), .A6out(t74245_9_b6out), .A7out(t74245_9_b7out), .A8out(t74245_9_b8out),
    .A1out(t74245_9_b1out), .A2out(t74245_9_b2out), .A3out(t74245_9_b3out), .A4out(t74245_9_b4out),
    .A5out(t74245_9_b5out), .B8out(t74245_7_b1out[7]), .B6out(t74245_7_b1out[5]), .B7out(t74245_7_b1out[6]),
    .B1out(t74245_7_b1out[0]), .B2out(t74245_7_b1out[1]), .B3out(t74245_7_b1out[2]),
    .B4out(t74245_7_b1out[3]), .B5out(t74245_7_b1out[4]));
  T74245 t74245_11 (
    .A6in(t74245_11_a6out), .A7in(t74245_11_a7out), .A8in(t74245_11_a8out), .A1in(t74245_11_a1out),
    .A2in(t74245_11_a2out), .A3in(t74245_11_a3out), .A4in(t74245_11_a4out), .A5in(t74245_11_a5out),
    .DIR(1'b0), .nOE(muxnOE_n), .B6in(t74245_7_b1out[13]), .B7in(t74245_7_b1out[14]),
    .B8in(t74245_7_b1out[15]), .B1in(t74245_7_b1out[8]), .B2in(t74245_7_b1out[9]), .B3in(t74245_7_b1out[10]),
    .B4in(t74245_7_b1out[11]), .B5in(t74245_7_b1out[12]), .A6out(t74245_11_a6out), .A7out(t74245_11_a7out),
    .A8out(t74245_11_a8out), .A1out(t74245_11_a1out), .A2out(t74245_11_a2out), .A3out(t74245_11_a3out),
    .A4out(t74245_11_a4out), .A5out(t74245_11_a5out), .B8out(t74245_7_b1out[15]), .B6out(t74245_7_b1out[13]),
    .B7out(t74245_7_b1out[14]), .B1out(t74245_7_b1out[8]), .B2out(t74245_7_b1out[9]),
    .B3out(t74245_7_b1out[10]), .B4out(t74245_7_b1out[11]), .B5out(t74245_7_b1out[12]));
  T74245 t74245_12 (
    .A6in(rom_1_data[13]), .A7in(rom_1_data[14]), .A8in(rom_1_data[15]), .A1in(rom_1_data[8]),
    .A2in(rom_1_data[9]), .A3in(rom_1_data[10]), .A4in(rom_1_data[11]), .A5in(rom_1_data[12]), .DIR(1'b1),
    .nOE(\bit ), .B6in(t74245_11_a6out), .B7in(t74245_11_a7out), .B8in(t74245_11_a8out),
    .B1in(t74245_11_a1out), .B2in(t74245_11_a2out), .B3in(t74245_11_a3out), .B4in(t74245_11_a4out),
    .B5in(t74245_11_a5out), .A6out(rom_1_data[13]), .A7out(rom_1_data[14]), .A8out(rom_1_data[15]),
    .A1out(rom_1_data[8]), .A2out(rom_1_data[9]), .A3out(rom_1_data[10]), .A4out(rom_1_data[11]),
    .A5out(rom_1_data[12]), .B8out(t74245_11_a8out), .B6out(t74245_11_a6out), .B7out(t74245_11_a7out),
    .B1out(t74245_11_a1out), .B2out(t74245_11_a2out), .B3out(t74245_11_a3out), .B4out(t74245_11_a4out),
    .B5out(t74245_11_a5out));
  T74245 t74245_13 (
    .A6in(t74245_9_b6out), .A7in(t74245_9_b7out), .A8in(t74245_9_b8out), .A1in(t74245_9_b1out),
    .A2in(t74245_9_b2out), .A3in(t74245_9_b3out), .A4in(t74245_9_b4out), .A5in(t74245_9_b5out), .DIR(1'b1),
    .nOE(nOutput_enable), .B6in(DataBUSout[5]), .B7in(DataBUSout[6]), .B8in(DataBUSout[7]),
    .B1in(DataBUSout[0]), .B2in(DataBUSout[1]), .B3in(DataBUSout[2]), .B4in(DataBUSout[3]),
    .B5in(DataBUSout[4]), .B8out(DataBUSout[7]), .B6out(DataBUSout[5]), .B7out(DataBUSout[6]),
    .B1out(DataBUSout[0]), .B2out(DataBUSout[1]), .B3out(DataBUSout[2]), .B4out(DataBUSout[3]),
    .B5out(DataBUSout[4]));  // open: A6out, A7out, A8out, A1out, A2out, A3out, A4out, A5out
  T74245 t74245_14 (
    .A6in(t74245_11_a6out), .A7in(t74245_11_a7out), .A8in(t74245_11_a8out), .A1in(t74245_11_a1out),
    .A2in(t74245_11_a2out), .A3in(t74245_11_a3out), .A4in(t74245_11_a4out), .A5in(t74245_11_a5out),
    .DIR(1'b1), .nOE(nOutput_enable), .B6in(DataBUSout[13]), .B7in(DataBUSout[14]), .B8in(DataBUSout[15]),
    .B1in(DataBUSout[8]), .B2in(DataBUSout[9]), .B3in(DataBUSout[10]), .B4in(DataBUSout[11]),
    .B5in(DataBUSout[12]), .B8out(DataBUSout[15]), .B6out(DataBUSout[13]), .B7out(DataBUSout[14]),
    .B1out(DataBUSout[8]), .B2out(DataBUSout[9]), .B3out(DataBUSout[10]), .B4out(DataBUSout[11]),
    .B5out(DataBUSout[12]));  // open: A6out, A7out, A8out, A1out, A2out, A3out, A4out, A5out
  // also tied to GND on the sheet: {n74283_1_pin14, n74283_1_pin3, n74283_2_pin14, n74283_2_pin3, n74283_3_pin14, n74283_3_pin3, n74283_4_pin14, n74283_4_pin3, n74283_1_pin12, n74283_1_pin5, n74283_2_pin12, n74283_2_pin5, n74283_3_pin12, n74283_3_pin5, n74283_4_pin12, n74283_4_pin7}
  // also tied to VCC on the sheet: n74283_4_pin5

  // Other names for the same wires on the sheet: muxnOE_p = \bit ; Data_in[15:0] = GPU_DATA

  // Notes on the sheet:
  //   TRI-STATE BUFFER
  //   MUX
  //   AND
  //   RegAddr
  //   ADDER
  //   nWE
  //   contents of rom_1 (hex, n*v repeats v):
  //   4800 ee c008 6080 8880 fecf 2880 1 9880 fecf d080 b100 c004 c005 c008 c009 c00a 6140 8850 feff 1084
  //   a800 50 3940 a 4900 30 3940 8 4900 3e 9045 2850 1 3950 fff0 4e00 28 1850 ff00 9850 feff d0a0 d090
  //   d080 d050 d040 b100 1850 ff00 9850 feff 1880 1 9880 fefe d0a0 d090 d080 d050 d040 b100 3950 ff00
  //   4900 49 2950 1 1840 20 9045 9850 feff d0a0 d090 d080 d050 d040 b100 0 8890 feef 3980 a 4900 62 3980
  //   8 4900 69 9089 2890 1 2a90 7fff 9890 feef b000 2890 100 2a90 7f00 9890 feef b000 2990 1 2a90 7fff
  //   9890 feef 1880 20 9089 b000 3299 4900 83 c008 c009 8088 a800 50 d090 d080 2880 1 2990 1 4800 73 b000
  //   a800 73 1880 a 4800 50 c004 1048 1880 78 a800 50 1084 2f80 c 2a80 f 2880 fed0 8088 a800 50 1084 2f80
  //   8 2a80 f 2880 fed0 8088 a800 50 1084 2f80 4 2a80 f 2880 fed0 8088 a800 50 1084 2f80 0 2a80 f 2880
  //   fed0 8088 a800 50 d040 b000 3288 4900 c4 1880 f000 1890 4 a800 73 b000 1880 f004 1890 5 a800 73 b000
  //   1880 7fff 1890 20 9098 2980 1 4a00 cf 9098 9880 feef b000 32aa 4900 e8 80b8 80c9 31bc 4a00 eb 2880 1
  //   2890 1 29a0 1 4800 d8 1880 1 b000 1880 0 b000 1820 f000 1880 f009 1890 b a800 84 2b10 8000 2b10 4000
  //   1880 3e a800 50 1880 20 9880 ff00 9880 ff01 9880 ff02 9880 ff03 9880 ff04 9880 ff05 9880 ff06 9880
  //   ff07 9880 ff08 9880 ff09 9880 ff0a 9880 ff0b 9880 ff0c 9880 ff0d 9880 ff0e 9880 ff0f 9880 ff10 9880
  //   ff11 9880 ff12 9880 ff13 9880 ff14 9880 ff15 9880 ff16 9880 ff17 9880 ff18 9880 ff19 9880 ff1a 9880
  //   ff1b 9880 ff1c 9880 ff1d 9880 ff1e 9880 ff1f 9880 ff20 9880 ff21 9880 ff22 9880 ff23 9880 ff24 9880
  //   ff25 9880 ff26 9880 ff27 9880 ff28 9880 ff29 9880 ff2a 9880 ff2b 9880 ff2c 9880 ff2d 9880 ff2e 9880
  //   ff2f 9880 ff30 9880 ff31 9880 ff32 9880 ff33 9880 ff34 9880 ff35 9880 ff36 9880 ff37 9880 ff38 9880
  //   ff39 9880 ff3a 9880 ff3b 9880 ff3c 9880 ff3d 9880 ff3e 9880 ff3f 9880 ff40 9880 ff41 9880 ff42 9880
  //   ff43 9880 ff44 9880 ff45 9880 ff46 9880 ff47 9880 ff48 9880 ff49 9880 ff4a 9880 ff4b 9880 ff4c 9880
  //   ff4d 9880 ff4e 9880 ff4f 9880 ff50 9880 ff51 9880 ff52 9880 ff53 9880 ff54 9880 ff55 9880 ff56 9880
  //   ff57 9880 ff58 9880 ff59 9880 ff5a 9880 ff5b 9880 ff5c 9880 ff5d 9880 ff5e 9880 ff5f 9880 ff60 9880
  //   ff61 9880 ff62 9880 ff63 9880 ff64 9880 ff65 9880 ff66 9880 ff67 9880 ff68 9880 ff69 9880 ff6a 9880
  //   ff6b 9880 ff6c 9880 ff6d 9880 ff6e 9880 ff6f 9880 ff70 9880 ff71 9880 ff72 9880 ff73 9880 ff74 9880
  //   ff75 9880 ff76 9880 ff77 9880 ff78 9880 ff79 9880 ff7a 9880 ff7b 9880 ff7c 9880 ff7d 9880 ff7e 9880
  //   ff7f 9880 ff80 9880 ff81 9880 ff82 9880 ff83 9880 ff84 9880 ff85 9880 ff86 9880 ff87 9880 ff88 9880
  //   ff89 9880 ff8a 9880 ff8b 9880 ff8c 9880 ff8d 9880 ff8e 9880 ff8f 9880 ff90 9880 ff91 9880 ff92 9880
  //   ff93 9880 ff94 9880 ff95 9880 ff96 9880 ff97 9880 ff98 9880 ff99 9880 ff9a 9880 ff9b 9880 ff9c 9880
  //   ff9d 9880 ff9e 9880 ff9f 9880 ffa0 9880 ffa1 9880 ffa2 9880 ffa3 9880 ffa4 9880 ffa5 9880 ffa6 9880
  //   ffa7 9880 ffa8 9880 ffa9 9880 ffaa 9880 ffab 9880 ffac 9880 ffad 9880 ffae 9880 ffaf 9880 ffb0 9880
  //   ffb1 9880 ffb2 9880 ffb3 9880 ffb4 9880 ffb5 9880 ffb6 9880 ffb7 9880 ffb8 9880 ffb9 9880 ffba 9880
  //   ffbb 9880 ffbc 9880 ffbd 9880 ffbe 9880 ffbf 9880 ffc0 9880 ffc1 9880 ffc2 9880 ffc3 9880 ffc4 9880
  //   ffc5 9880 ffc6 9880 ffc7 9880 ffc8 9880 ffc9 9880 ffca 9880 ffcb 9880 ffcc 9880 ffcd 9880 ffce 9880
  //   ffcf 9880 ffd0 9880 ffd1 9880 ffd2 9880 ffd3 9880 ffd4 9880 ffd5 9880 ffd6 9880 ffd7 9880 ffd8 9880
  //   ffd9 9880 ffda 9880 ffdb 9880 ffdc 9880 ffdd 9880 ffde 9880 ffdf 9880 ffe0 9880 ffe1 9880 ffe2 9880
  //   ffe3 9880 ffe4 9880 ffe5 9880 ffe6 9880 ffe7 9880 ffe8 9880 ffe9 9880 ffea 9880 ffeb 9880 ffec 9880
  //   ffed 9880 ffee 9880 ffef 8840 fefe 3244 4900 2e0 1840 0 9840 fefe 1880 ff00 1890 f018 18a0 4 a800 d8
  //   3288 4a00 31d 1880 ff00 1890 f084 18a0 4 a800 d8 3288 4a00 325 1880 ff00 1890 f014 18a0 4 a800 d8
  //   3288 4a00 32d 1880 ff00 1890 f088 18a0 5 a800 d8 3288 4a00 337 1880 f08d 1890 f a800 84 4800 fa 1880
  //   f01c 1890 68 a800 84 4800 fa 1880 ff05 1890 fa a800 84 4800 fa 8880 fecf a800 8a 1880 a a800 50 4800
  //   fa a800 cb 4800 fa 60613*0 74 72 75 65 66 61 6c 73 65 6d 41 4c 55 73 68 20 76 30 2e 31 74 69 6d 65
  //   68 65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
  //   nOE
  //   ROM
  //   TRI-STATE BUFFER
  //   MUX
  //   TRI-STATE BUFFER
endmodule

module control (
  input  CLK,
  input  [15:0] ialubus,
  input  ifs,
  input  ifo,
  input  ifc,
  input  ifz,
  input  [15:0] imembus,
  input  [15:0] iregbus,
  input  iint,
  input  [2:0] iintid,
  input  ibusy,
  input  [15:0] iiobus,
  output [3:0] oaluop,
  output [15:0] oalubus,
  output [2:0] omemop,
  output [15:0] omembus,
  output oregwe,
  output [15:0] oregbus,
  output [3:0] oregid,
  output mask_save,
  output mask_restore,
  output [1:0] oioop,
  output [15:0] oiobus,
  output [2:0] oioaddr
);

  wire c, flwe, instr_load, isimm, isint, isjump, isret, isstack, m28c64atop_1_o6, m28c64atop_1_o7,
       n7400_1_pin8, n7400_1_pin11, n7404_1_pin5, n7404_1_pin10, n7404_1_pin12, n7404_2_pin2, n7404_2_pin4,
       n7404_2_pin6, n7404_2_pin8, n7404_2_pin10, n7404_2_pin12, n7404_3_pin2, n7404_3_pin3, n7404_3_pin4,
       n7404_3_pin6, n7404_3_pin8, n7404_3_pin9, n7404_3_pin10, n7404_3_pin11, n7404_3_pin12, n7404_4_pin8,
       n7404_4_pin10, n7404_4_pin12, n7404_5_pin2, n7404_5_pin4, n7404_5_pin6, n7404_5_pin12, n7404_5_pin13,
       n7408_1_pin3, n7408_3_pin11, n7432_2_pin3, n7432_2_pin11, n7486_1_pin3, n7486_1_pin5, n7486_1_pin6,
       n74139_1_pin1, n74139_1_pin4, n74139_1_pin5, n74139_1_pin6, n74139_1_pin7, n74139_1_pin9,
       n74139_1_pin10, n74139_1_pin11, n74139_1_pin12, n74283_1_pin2, n74283_1_pin6, n74283_1_pin9,
       n74283_1_pin15, n74283_2_pin2, n74283_2_pin9, n74283_2_pin15, n74283_3_pin2, n74283_3_pin9,
       n74283_3_pin15, n74283_4_pin2, n74283_4_pin9, n74283_4_pin15, n74283_5_pin1, n74283_5_pin2,
       n74283_5_pin4, n74283_5_pin7, n74283_5_pin10, n74283_5_pin13, n74283_5_pin14, n74377_1_pin1,
       n74377_1_pin3, n74377_1_pin4, n74377_1_pin7, n74377_1_pin8, n74377_1_pin13, n74377_1_pin14,
       n74377_1_pin17, n74377_1_pin18, n74377_2_pin3, n74377_2_pin4, n74377_2_pin7, n74377_2_pin8,
       n74377_2_pin13, n74377_2_pin14, n74377_2_pin17, n74377_2_pin18, n74377_3_pin1, n74377_3_pin2,
       n74377_3_pin3, n74377_3_pin5, n74377_3_pin6, n74377_3_pin9, n74377_3_pin13, n74377_3_pin14,
       n74377_3_pin17, n74377_3_pin18, n74377_4_pin1, n74377_4_pin2, n74377_4_pin3, n74377_4_pin5,
       n74377_4_pin6, n74377_4_pin9, n74377_4_pin13, n74377_4_pin14, n74377_4_pin17, n74377_4_pin18,
       n74377_6_pin1, n74377_6_pin2, n74377_6_pin5, n74377_6_pin6, n74377_6_pin9, n74377_7_pin3, next_instr,
       o, regds, regsrc, s, should_jump, t74245_39_a6out, t74257_3_y1, t74257_3_y2, t74257_3_y3, t74257_3_y4,
       t74257_5_y1, t74257_5_y2, t74257_5_y3, t74257_5_y4, t74257_6_y1, t74257_6_y2, t74257_6_y3,
       t74257_6_y4, tempregwe, valid, z;
  wire [0:0] t74245_17_b1out;
  wire [1:0] alumode, alusrc, m28c64abot_1_o2, m28c64abot_1_o4, memsrc;
  wire [2:0] intid_saved;
  wire [3:0] cycle, flags_saved, opcode;
  wire [7:0] n74377_1_pin19;
  wire [11:0] t74245_17_b5out;
  wire [15:0] ip, ipnext, srcbus, srctempbus, t74245_3_a1out, t74245_7_b1out, t74245_13_a1out,
       t74245_17_a1out, t74245_31_a1out, tempreg;
  wire [21:0] m28c64abot_1_o0;
  wire [23:22] rom_1_data;

  _74377 u_74377_1 (
    .pin1(n74377_1_pin1), .pin2(n74377_1_pin19[1]), .pin3(n74377_1_pin3), .pin4(n74377_1_pin4),
    .pin5(n74377_1_pin19[3]), .pin6(n74377_1_pin19[5]), .pin7(n74377_1_pin7), .pin8(n74377_1_pin8),
    .pin9(n74377_1_pin19[7]), .pin19(n74377_1_pin19[0]), .pin18(n74377_1_pin18), .pin17(n74377_1_pin17),
    .pin16(n74377_1_pin19[2]), .pin15(n74377_1_pin19[4]), .pin14(n74377_1_pin14), .pin13(n74377_1_pin13),
    .pin12(n74377_1_pin19[6]), .pin11(CLK));
  T74245 t74245_1 (
    .A6in(imembus[5]), .A7in(imembus[6]), .A8in(imembus[7]), .A1in(imembus[0]), .A2in(imembus[1]),
    .A3in(imembus[2]), .A4in(imembus[3]), .A5in(imembus[4]), .DIR(1'b1), .nOE(isint), .B6in(n74377_1_pin7),
    .B7in(n74377_1_pin13), .B8in(n74377_1_pin8), .B1in(n74377_1_pin18), .B2in(n74377_1_pin3),
    .B3in(n74377_1_pin17), .B4in(n74377_1_pin4), .B5in(n74377_1_pin14), .A6out(imembus[5]),
    .A7out(imembus[6]), .A8out(imembus[7]), .A1out(imembus[0]), .A2out(imembus[1]), .A3out(imembus[2]),
    .A4out(imembus[3]), .A5out(imembus[4]), .B8out(n74377_1_pin8), .B6out(n74377_1_pin7),
    .B7out(n74377_1_pin13), .B1out(n74377_1_pin18), .B2out(n74377_1_pin3), .B3out(n74377_1_pin17),
    .B4out(n74377_1_pin4), .B5out(n74377_1_pin14));
  Pull_Resistor pull_resistor_1 (.node(n74377_1_pin18));
  Pull_Resistor pull_resistor_2 (.node(n74377_1_pin3));
  Pull_Resistor pull_resistor_3 (.node(n74377_1_pin17));
  Pull_Resistor pull_resistor_4 (.node(n74377_1_pin4));
  Pull_Resistor pull_resistor_5 (.node(n74377_1_pin14));
  Pull_Resistor pull_resistor_6 (.node(n74377_1_pin7));
  Pull_Resistor pull_resistor_7 (.node(n74377_1_pin13));
  Pull_Resistor pull_resistor_8 (.node(n74377_1_pin8));
  _74283 u_74283_1 (
    .pin1(ipnext[1]), .pin2(n74283_1_pin2), .pin3(ip[1]), .pin4(ipnext[0]), .pin5(ip[0]),
    .pin6(n74283_1_pin6), .pin7(isimm), .pin15(n74283_1_pin15), .pin14(ip[2]), .pin13(ipnext[2]),
    .pin12(ip[3]), .pin11(n74283_1_pin15), .pin10(ipnext[3]), .pin9(n74283_1_pin9));
  _74377 u_74377_2 (
    .pin1(n74377_1_pin1), .pin2(oioaddr[1]), .pin3(n74377_2_pin3), .pin4(n74377_2_pin4), .pin5(isimm),
    .pin6(opcode[1]), .pin7(n74377_2_pin7), .pin8(n74377_2_pin8), .pin9(opcode[3]), .pin19(oioaddr[0]),
    .pin18(n74377_2_pin18), .pin17(n74377_2_pin17), .pin16(oioaddr[2]), .pin15(opcode[0]),
    .pin14(n74377_2_pin14), .pin13(n74377_2_pin13), .pin12(opcode[2]), .pin11(CLK));
  Pull_Resistor pull_resistor_9 (.node(n74377_2_pin18));
  Pull_Resistor pull_resistor_10 (.node(n74377_2_pin3));
  T74245 t74245_2 (
    .A6in(imembus[13]), .A7in(imembus[14]), .A8in(imembus[15]), .A1in(imembus[8]), .A2in(imembus[9]),
    .A3in(imembus[10]), .A4in(imembus[11]), .A5in(imembus[12]), .DIR(1'b1), .nOE(isint),
    .B6in(n74377_2_pin7), .B7in(n74377_2_pin13), .B8in(n74377_2_pin8), .B1in(n74377_2_pin18),
    .B2in(n74377_2_pin3), .B3in(n74377_2_pin17), .B4in(n74377_2_pin4), .B5in(n74377_2_pin14),
    .A6out(imembus[13]), .A7out(imembus[14]), .A8out(imembus[15]), .A1out(imembus[8]), .A2out(imembus[9]),
    .A3out(imembus[10]), .A4out(imembus[11]), .A5out(imembus[12]), .B8out(n74377_2_pin8),
    .B6out(n74377_2_pin7), .B7out(n74377_2_pin13), .B1out(n74377_2_pin18), .B2out(n74377_2_pin3),
    .B3out(n74377_2_pin17), .B4out(n74377_2_pin4), .B5out(n74377_2_pin14));
  _74377 u_74377_3 (
    .pin1(n74377_3_pin1), .pin2(n74377_3_pin2), .pin3(n74377_3_pin3), .pin4(n74377_3_pin3),
    .pin5(n74377_3_pin5), .pin6(n74377_3_pin6), .pin7(n74377_3_pin3), .pin8(n74377_3_pin3),
    .pin9(n74377_3_pin9), .pin19(flags_saved[0]), .pin18(n74377_3_pin18), .pin17(n74377_3_pin17),
    .pin16(flags_saved[1]), .pin15(flags_saved[2]), .pin14(n74377_3_pin14), .pin13(n74377_3_pin13),
    .pin12(flags_saved[3]), .pin11(CLK));
  // NoConnect on n74377_3_pin2
  _74377 u_74377_4 (
    .pin1(n74377_4_pin1), .pin2(n74377_4_pin2), .pin3(n74377_4_pin3), .pin4(n74377_4_pin3),
    .pin5(n74377_4_pin5), .pin6(n74377_4_pin6), .pin7(n74377_4_pin3), .pin8(n74377_4_pin3),
    .pin9(n74377_4_pin9), .pin19(s), .pin18(n74377_4_pin18), .pin17(n74377_4_pin17), .pin16(o), .pin15(c),
    .pin14(n74377_4_pin14), .pin13(n74377_4_pin13), .pin12(z), .pin11(CLK));
  // NoConnect on n74377_4_pin2
  Clock clock_1 ();  // open: out
  ROM #(.dataWidth(24)) rom_1 (
    .addr({opcode, cycle}),
    .data({rom_1_data, oioop, isret, isstack, tempregwe, isjump, flwe, omemop, memsrc, instr_load, regsrc, oregwe, regds, alusrc, alumode, valid, next_instr}));
  Pull_Resistor pull_resistor_11 (.node(n74377_2_pin17));
  Pull_Resistor pull_resistor_12 (.node(n74377_2_pin4));
  Pull_Resistor pull_resistor_13 (.node(n74377_2_pin14));
  Pull_Resistor pull_resistor_14 (.node(n74377_2_pin7));
  // NoConnect on n74377_3_pin5
  // NoConnect on n74377_3_pin6
  T74257 t74257_1 (
    .nOE(1'b0), .isB(flwe), .A1(z), .B1(ifz), .A2(c), .B2(ifc), .A3(o), .B3(ifo), .A4(s), .B4(ifs),
    .Y1(n74377_3_pin13), .Y2(n74377_3_pin14), .Y3(n74377_3_pin17), .Y4(n74377_3_pin18));
  // NoConnect on n74377_4_pin5
  // NoConnect on n74377_4_pin6
  T74257 t74257_2 (
    .nOE(1'b0), .isB(mask_restore), .A1(ifz), .B1(flags_saved[3]), .A2(ifc), .B2(flags_saved[2]), .A3(ifo),
    .B3(flags_saved[1]), .A4(ifs), .B4(flags_saved[0]), .Y1(n74377_4_pin13), .Y2(n74377_4_pin14),
    .Y3(n74377_4_pin17), .Y4(n74377_4_pin18));
  _74283 u_74283_2 (
    .pin1(ipnext[5]), .pin2(n74283_2_pin2), .pin3(ip[5]), .pin4(ipnext[4]), .pin5(ip[4]),
    .pin6(n74283_2_pin2), .pin7(n74283_1_pin9), .pin15(n74283_2_pin15), .pin14(ip[6]), .pin13(ipnext[6]),
    .pin12(ip[7]), .pin11(n74283_2_pin15), .pin10(ipnext[7]), .pin9(n74283_2_pin9));
  M28C64Atop m28c64atop_1 (
    .nCE(1'b0), .A0(cycle[0]), .A1(cycle[1]), .A2(cycle[2]), .A3(cycle[3]), .A4(opcode[0]), .A5(opcode[1]),
    .A6(opcode[2]), .A7(opcode[3]), .nWE(1'b1), .A8(1'b0), .A9(1'b0), .A10(1'b0), .A11(1'b0), .A12(1'b0),
    .nOE(1'b0), .O0(m28c64abot_1_o0[16]), .O1(m28c64abot_1_o0[17]), .O2(m28c64abot_1_o0[18]),
    .O3(m28c64abot_1_o0[19]), .O4(m28c64abot_1_o0[20]), .O5(m28c64abot_1_o0[21]), .O6(m28c64atop_1_o6),
    .O7(m28c64atop_1_o7));
  M28C64Amid m28c64amid_1 (
    .nCE(1'b0), .A0(cycle[0]), .A1(cycle[1]), .A2(cycle[2]), .A3(cycle[3]), .A4(opcode[0]), .A5(opcode[1]),
    .A6(opcode[2]), .A7(opcode[3]), .nWE(1'b1), .A8(1'b0), .A9(1'b0), .A10(1'b0), .A11(1'b0), .A12(1'b0),
    .nOE(1'b0), .O0(m28c64abot_1_o0[8]), .O1(m28c64abot_1_o0[9]), .O2(m28c64abot_1_o0[10]),
    .O3(m28c64abot_1_o0[11]), .O4(m28c64abot_1_o0[12]), .O5(m28c64abot_1_o0[13]), .O6(m28c64abot_1_o0[14]),
    .O7(m28c64abot_1_o0[15]));
  M28C64Abot m28c64abot_1 (
    .nCE(1'b0), .A0(cycle[0]), .A1(cycle[1]), .A2(cycle[2]), .A3(cycle[3]), .A4(opcode[0]), .A5(opcode[1]),
    .A6(opcode[2]), .A7(opcode[3]), .nWE(1'b1), .A8(1'b0), .A9(1'b0), .A10(1'b0), .A11(1'b0), .A12(1'b0),
    .nOE(1'b0), .O0(m28c64abot_1_o0[0]), .O1(m28c64abot_1_o0[1]), .O2(m28c64abot_1_o2[0]),
    .O3(m28c64abot_1_o2[1]), .O4(m28c64abot_1_o4[0]), .O5(m28c64abot_1_o4[1]), .O6(m28c64abot_1_o0[6]),
    .O7(m28c64abot_1_o0[7]));
  Pull_Resistor pull_resistor_15 (.node(n74377_2_pin13));
  Pull_Resistor pull_resistor_16 (.node(n74377_2_pin8));
  // NoConnect on n74377_3_pin9
  // NoConnect on n74377_4_pin9
  // NoConnect on m28c64atop_1_o7
  // NoConnect on m28c64atop_1_o6
  Pull_Resistor pull_resistor_17 (.node({opcode, isimm, oioaddr, n74377_1_pin19}));
  _74283 u_74283_3 (
    .pin1(ipnext[9]), .pin2(n74283_3_pin2), .pin3(ip[9]), .pin4(ipnext[8]), .pin5(ip[8]),
    .pin6(n74283_3_pin2), .pin7(n74283_2_pin9), .pin15(n74283_3_pin15), .pin14(ip[10]), .pin13(ipnext[10]),
    .pin12(ip[11]), .pin11(n74283_3_pin15), .pin10(ipnext[11]), .pin9(n74283_3_pin9));
  T74257 t74257_3 (
    .nOE(1'b0), .isB(regds), .A1(n74377_1_pin19[4]), .B1(n74377_1_pin19[0]), .A2(n74377_1_pin19[6]),
    .B2(n74377_1_pin19[2]), .A3(n74377_1_pin19[7]), .B3(n74377_1_pin19[3]), .A4(n74377_1_pin19[5]),
    .B4(n74377_1_pin19[1]), .Y1(t74257_3_y1), .Y2(t74257_3_y2), .Y3(t74257_3_y3), .Y4(t74257_3_y4));
  _74283 u_74283_4 (
    .pin1(ipnext[13]), .pin2(n74283_4_pin2), .pin3(ip[13]), .pin4(ipnext[12]), .pin5(ip[12]),
    .pin6(n74283_4_pin2), .pin7(n74283_3_pin9), .pin15(n74283_4_pin15), .pin14(ip[14]), .pin13(ipnext[14]),
    .pin12(ip[15]), .pin11(n74283_4_pin15), .pin10(ipnext[15]), .pin9(n74283_4_pin9));
  // NoConnect on n74283_4_pin9
  T74257 t74257_4 (
    .nOE(1'b0), .isB(isstack), .A1(t74257_3_y1), .B1(1'b0), .A2(t74257_3_y2), .B2(1'b0), .A3(t74257_3_y3),
    .B3(1'b0), .A4(t74257_3_y4), .B4(1'b1), .Y1(oregid[0]), .Y2(oregid[2]), .Y3(oregid[3]), .Y4(oregid[1]));
  _7400 u_7400_1 (
    .pin13(isjump), .pin12(should_jump), .pin11(n7400_1_pin11), .pin10(n7400_1_pin11), .pin9(n7400_1_pin11),
    .pin8(n7400_1_pin8));  // open: pin1, pin2, pin3, pin4, pin5, pin6
  Pull_Resistor pull_resistor_18 (.node({rom_1_data, oioop, isret, isstack, tempregwe, isjump, flwe, omemop, memsrc, instr_load, regsrc, oregwe, regds, alusrc, alumode, valid, next_instr}));
  _7404 u_7404_1 (
    .pin1(instr_load), .pin2(n74377_1_pin1), .pin3(mask_save), .pin4(n74377_3_pin1), .pin5(n7404_1_pin5),
    .pin6(n74377_4_pin1), .pin13(next_instr), .pin12(n7404_1_pin12), .pin11(tempregwe), .pin10(n7404_1_pin10));  // open: pin9, pin8
  _7432 u_7432_1 (
    .pin1(mask_restore), .pin2(flwe), .pin3(n7404_1_pin5));  // open: pin4, pin5, pin6, pin13, pin12, pin11, pin10, pin9, pin8
  T74257 t74257_5 (
    .nOE(1'b0), .isB(next_instr), .A1(n74283_5_pin4), .B1(1'b0), .A2(n74283_5_pin13), .B2(1'b0),
    .A3(n74283_5_pin10), .B3(1'b0), .A4(n74283_5_pin1), .B4(1'b0), .Y1(t74257_5_y1), .Y2(t74257_5_y2),
    .Y3(t74257_5_y3), .Y4(t74257_5_y4));
  _74377 u_74377_5 (
    .pin1(n7404_1_pin10), .pin2(tempreg[1]), .pin3(imembus[1]), .pin4(imembus[3]), .pin5(tempreg[3]),
    .pin6(tempreg[5]), .pin7(imembus[5]), .pin8(imembus[7]), .pin9(tempreg[7]), .pin19(tempreg[0]),
    .pin18(imembus[0]), .pin17(imembus[2]), .pin16(tempreg[2]), .pin15(tempreg[4]), .pin14(imembus[4]),
    .pin13(imembus[6]), .pin12(tempreg[6]), .pin11(CLK));
  T74245 t74245_3 (
    .A6in(t74245_3_a1out[5]), .A7in(t74245_3_a1out[6]), .A8in(t74245_3_a1out[7]), .A1in(t74245_3_a1out[0]),
    .A2in(t74245_3_a1out[1]), .A3in(t74245_3_a1out[2]), .A4in(t74245_3_a1out[3]), .A5in(t74245_3_a1out[4]),
    .nOE(n7400_1_pin11), .B6in(srcbus[5]), .B7in(srcbus[6]), .B8in(srcbus[7]), .B1in(srcbus[0]),
    .B2in(srcbus[1]), .B3in(srcbus[2]), .B4in(srcbus[3]), .B5in(srcbus[4]), .A6out(t74245_3_a1out[5]),
    .A7out(t74245_3_a1out[6]), .A8out(t74245_3_a1out[7]), .A1out(t74245_3_a1out[0]),
    .A2out(t74245_3_a1out[1]), .A3out(t74245_3_a1out[2]), .A4out(t74245_3_a1out[3]),
    .A5out(t74245_3_a1out[4]), .B8out(srcbus[7]), .B6out(srcbus[5]), .B7out(srcbus[6]), .B1out(srcbus[0]),
    .B2out(srcbus[1]), .B3out(srcbus[2]), .B4out(srcbus[3]), .B5out(srcbus[4]));  // open: DIR
  T74245 t74245_4 (
    .A6in(ipnext[5]), .A7in(ipnext[6]), .A8in(ipnext[7]), .A1in(ipnext[0]), .A2in(ipnext[1]),
    .A3in(ipnext[2]), .A4in(ipnext[3]), .A5in(ipnext[4]), .DIR(1'b1), .nOE(n7400_1_pin8),
    .B6in(t74245_3_a1out[5]), .B7in(t74245_3_a1out[6]), .B8in(t74245_3_a1out[7]), .B1in(t74245_3_a1out[0]),
    .B2in(t74245_3_a1out[1]), .B3in(t74245_3_a1out[2]), .B4in(t74245_3_a1out[3]), .B5in(t74245_3_a1out[4]),
    .A6out(ipnext[5]), .A7out(ipnext[6]), .A8out(ipnext[7]), .A1out(ipnext[0]), .A2out(ipnext[1]),
    .A3out(ipnext[2]), .A4out(ipnext[3]), .A5out(ipnext[4]), .B8out(t74245_3_a1out[7]),
    .B6out(t74245_3_a1out[5]), .B7out(t74245_3_a1out[6]), .B1out(t74245_3_a1out[0]),
    .B2out(t74245_3_a1out[1]), .B3out(t74245_3_a1out[2]), .B4out(t74245_3_a1out[3]), .B5out(t74245_3_a1out[4]));
  _74377 u_74377_6 (
    .pin1(n74377_6_pin1), .pin2(n74377_6_pin2), .pin3(n74377_6_pin1), .pin4(n74377_6_pin1),
    .pin5(n74377_6_pin5), .pin6(n74377_6_pin6), .pin7(n74377_6_pin1), .pin8(n74377_6_pin1),
    .pin9(n74377_6_pin9), .pin19(cycle[0]), .pin18(t74257_5_y1), .pin17(t74257_5_y4), .pin16(cycle[1]),
    .pin15(cycle[2]), .pin14(t74257_5_y2), .pin13(t74257_5_y3), .pin12(cycle[3]), .pin11(CLK));
  // NoConnect on n74377_6_pin2
  _74283 u_74283_5 (
    .pin1(n74283_5_pin1), .pin2(n74283_5_pin2), .pin3(cycle[1]), .pin4(n74283_5_pin4), .pin5(n74283_5_pin2),
    .pin6(cycle[0]), .pin7(n74283_5_pin7), .pin15(cycle[2]), .pin14(n74283_5_pin14), .pin13(n74283_5_pin13),
    .pin12(cycle[3]), .pin11(n74283_5_pin14), .pin10(n74283_5_pin10));  // open: pin9
  _74377 u_74377_7 (
    .pin1(n7404_1_pin12), .pin3(n74377_7_pin3), .pin4(n74377_7_pin3), .pin7(n74377_7_pin3),
    .pin8(n74377_7_pin3), .pin19(isint), .pin18(iint), .pin17(iintid[2]), .pin16(intid_saved[2]),
    .pin15(intid_saved[1]), .pin14(iintid[1]), .pin13(iintid[0]), .pin12(intid_saved[0]), .pin11(CLK));  // open: pin2, pin5, pin6, pin9
  // NoConnect on n74377_6_pin5
  // NoConnect on n74377_6_pin6
  Pull_Resistor pull_resistor_19 (.node(iintid));
  T74245 t74245_5 (
    .A6in(ipnext[13]), .A7in(ipnext[14]), .A8in(ipnext[15]), .A1in(ipnext[8]), .A2in(ipnext[9]),
    .A3in(ipnext[10]), .A4in(ipnext[11]), .A5in(ipnext[12]), .DIR(1'b1), .nOE(n7400_1_pin8),
    .B6in(t74245_3_a1out[13]), .B7in(t74245_3_a1out[14]), .B8in(t74245_3_a1out[15]),
    .B1in(t74245_3_a1out[8]), .B2in(t74245_3_a1out[9]), .B3in(t74245_3_a1out[10]), .B4in(t74245_3_a1out[11]),
    .B5in(t74245_3_a1out[12]), .A6out(ipnext[13]), .A7out(ipnext[14]), .A8out(ipnext[15]), .A1out(ipnext[8]),
    .A2out(ipnext[9]), .A3out(ipnext[10]), .A4out(ipnext[11]), .A5out(ipnext[12]),
    .B8out(t74245_3_a1out[15]), .B6out(t74245_3_a1out[13]), .B7out(t74245_3_a1out[14]),
    .B1out(t74245_3_a1out[8]), .B2out(t74245_3_a1out[9]), .B3out(t74245_3_a1out[10]),
    .B4out(t74245_3_a1out[11]), .B5out(t74245_3_a1out[12]));
  // NoConnect on n74377_6_pin9
  _74377 u_74377_8 (
    .pin1(n7404_1_pin10), .pin2(tempreg[9]), .pin3(imembus[9]), .pin4(imembus[11]), .pin5(tempreg[11]),
    .pin6(tempreg[13]), .pin7(imembus[13]), .pin8(imembus[15]), .pin9(tempreg[15]), .pin19(tempreg[8]),
    .pin18(imembus[8]), .pin17(imembus[10]), .pin16(tempreg[10]), .pin15(tempreg[12]), .pin14(imembus[12]),
    .pin13(imembus[14]), .pin12(tempreg[14]), .pin11(CLK));
  T74245 t74245_6 (
    .A6in(t74245_3_a1out[13]), .A7in(t74245_3_a1out[14]), .A8in(t74245_3_a1out[15]),
    .A1in(t74245_3_a1out[8]), .A2in(t74245_3_a1out[9]), .A3in(t74245_3_a1out[10]), .A4in(t74245_3_a1out[11]),
    .A5in(t74245_3_a1out[12]), .DIR(1'b0), .nOE(n7400_1_pin11), .B6in(srcbus[13]), .B7in(srcbus[14]),
    .B8in(srcbus[15]), .B1in(srcbus[8]), .B2in(srcbus[9]), .B3in(srcbus[10]), .B4in(srcbus[11]),
    .B5in(srcbus[12]), .A6out(t74245_3_a1out[13]), .A7out(t74245_3_a1out[14]), .A8out(t74245_3_a1out[15]),
    .A1out(t74245_3_a1out[8]), .A2out(t74245_3_a1out[9]), .A3out(t74245_3_a1out[10]),
    .A4out(t74245_3_a1out[11]), .A5out(t74245_3_a1out[12]), .B8out(srcbus[15]), .B6out(srcbus[13]),
    .B7out(srcbus[14]), .B1out(srcbus[8]), .B2out(srcbus[9]), .B3out(srcbus[10]), .B4out(srcbus[11]),
    .B5out(srcbus[12]));
  _7408 u_7408_1 (
    .pin1(isret), .pin2(next_instr), .pin3(n7408_1_pin3), .pin4(n7408_1_pin3), .pin5(oioaddr[0]),
    .pin6(mask_restore), .pin13(iint), .pin12(next_instr), .pin11(mask_save));  // open: pin10, pin9, pin8
  T74245 t74245_7 (
    .A6in(t74245_3_a1out[5]), .A7in(t74245_3_a1out[6]), .A8in(t74245_3_a1out[7]), .A1in(t74245_3_a1out[0]),
    .A2in(t74245_3_a1out[1]), .A3in(t74245_3_a1out[2]), .A4in(t74245_3_a1out[3]), .A5in(t74245_3_a1out[4]),
    .DIR(1'b1), .nOE(isret), .B6in(t74245_7_b1out[5]), .B7in(t74245_7_b1out[6]), .B8in(t74245_7_b1out[7]),
    .B1in(t74245_7_b1out[0]), .B2in(t74245_7_b1out[1]), .B3in(t74245_7_b1out[2]), .B4in(t74245_7_b1out[3]),
    .B5in(t74245_7_b1out[4]), .A6out(t74245_3_a1out[5]), .A7out(t74245_3_a1out[6]),
    .A8out(t74245_3_a1out[7]), .A1out(t74245_3_a1out[0]), .A2out(t74245_3_a1out[1]),
    .A3out(t74245_3_a1out[2]), .A4out(t74245_3_a1out[3]), .A5out(t74245_3_a1out[4]),
    .B8out(t74245_7_b1out[7]), .B6out(t74245_7_b1out[5]), .B7out(t74245_7_b1out[6]),
    .B1out(t74245_7_b1out[0]), .B2out(t74245_7_b1out[1]), .B3out(t74245_7_b1out[2]),
    .B4out(t74245_7_b1out[3]), .B5out(t74245_7_b1out[4]));
  T74245 t74245_8 (
    .A6in(t74245_7_b1out[5]), .A7in(t74245_7_b1out[6]), .A8in(t74245_7_b1out[7]), .A1in(t74245_7_b1out[0]),
    .A2in(t74245_7_b1out[1]), .A3in(t74245_7_b1out[2]), .A4in(t74245_7_b1out[3]), .A5in(t74245_7_b1out[4]),
    .nOE(n7404_4_pin12), .B6in(imembus[5]), .B7in(imembus[6]), .B8in(imembus[7]), .B1in(imembus[0]),
    .B2in(imembus[1]), .B3in(imembus[2]), .B4in(imembus[3]), .B5in(imembus[4]), .A6out(t74245_7_b1out[5]),
    .A7out(t74245_7_b1out[6]), .A8out(t74245_7_b1out[7]), .A1out(t74245_7_b1out[0]),
    .A2out(t74245_7_b1out[1]), .A3out(t74245_7_b1out[2]), .A4out(t74245_7_b1out[3]),
    .A5out(t74245_7_b1out[4]), .B8out(imembus[7]), .B6out(imembus[5]), .B7out(imembus[6]),
    .B1out(imembus[0]), .B2out(imembus[1]), .B3out(imembus[2]), .B4out(imembus[3]), .B5out(imembus[4]));  // open: DIR
  T74245 t74245_9 (
    .A6in(t74245_7_b1out[13]), .A7in(t74245_7_b1out[14]), .A8in(t74245_7_b1out[15]),
    .A1in(t74245_7_b1out[8]), .A2in(t74245_7_b1out[9]), .A3in(t74245_7_b1out[10]), .A4in(t74245_7_b1out[11]),
    .A5in(t74245_7_b1out[12]), .DIR(1'b0), .nOE(n7404_4_pin12), .B6in(imembus[13]), .B7in(imembus[14]),
    .B8in(imembus[15]), .B1in(imembus[8]), .B2in(imembus[9]), .B3in(imembus[10]), .B4in(imembus[11]),
    .B5in(imembus[12]), .A6out(t74245_7_b1out[13]), .A7out(t74245_7_b1out[14]), .A8out(t74245_7_b1out[15]),
    .A1out(t74245_7_b1out[8]), .A2out(t74245_7_b1out[9]), .A3out(t74245_7_b1out[10]),
    .A4out(t74245_7_b1out[11]), .A5out(t74245_7_b1out[12]), .B8out(imembus[15]), .B6out(imembus[13]),
    .B7out(imembus[14]), .B1out(imembus[8]), .B2out(imembus[9]), .B3out(imembus[10]), .B4out(imembus[11]),
    .B5out(imembus[12]));
  T74245 t74245_10 (
    .A6in(t74245_3_a1out[13]), .A7in(t74245_3_a1out[14]), .A8in(t74245_3_a1out[15]),
    .A1in(t74245_3_a1out[8]), .A2in(t74245_3_a1out[9]), .A3in(t74245_3_a1out[10]), .A4in(t74245_3_a1out[11]),
    .A5in(t74245_3_a1out[12]), .DIR(1'b1), .nOE(isret), .B6in(t74245_7_b1out[13]), .B7in(t74245_7_b1out[14]),
    .B8in(t74245_7_b1out[15]), .B1in(t74245_7_b1out[8]), .B2in(t74245_7_b1out[9]), .B3in(t74245_7_b1out[10]),
    .B4in(t74245_7_b1out[11]), .B5in(t74245_7_b1out[12]), .A6out(t74245_3_a1out[13]),
    .A7out(t74245_3_a1out[14]), .A8out(t74245_3_a1out[15]), .A1out(t74245_3_a1out[8]),
    .A2out(t74245_3_a1out[9]), .A3out(t74245_3_a1out[10]), .A4out(t74245_3_a1out[11]),
    .A5out(t74245_3_a1out[12]), .B8out(t74245_7_b1out[15]), .B6out(t74245_7_b1out[13]),
    .B7out(t74245_7_b1out[14]), .B1out(t74245_7_b1out[8]), .B2out(t74245_7_b1out[9]),
    .B3out(t74245_7_b1out[10]), .B4out(t74245_7_b1out[11]), .B5out(t74245_7_b1out[12]));
  _7486 u_7486_1 (
    .pin1(s), .pin2(o), .pin3(n7486_1_pin3), .pin4(n7486_1_pin3), .pin5(n7486_1_pin5), .pin6(n7486_1_pin6));  // open: pin13, pin12, pin11, pin10, pin9, pin8
  _7432 u_7432_2 (
    .pin1(c), .pin2(z), .pin3(n7432_2_pin3), .pin13(z), .pin12(n7486_1_pin3), .pin11(n7432_2_pin11));  // open: pin4, pin5, pin6, pin10, pin9, pin8
  T74245 t74245_11 (
    .A6in(srcbus[5]), .A7in(srcbus[6]), .A8in(srcbus[7]), .A1in(srcbus[0]), .A2in(srcbus[1]),
    .A3in(srcbus[2]), .A4in(srcbus[3]), .A5in(srcbus[4]), .nOE(n7404_3_pin12), .B6in(imembus[5]),
    .B7in(imembus[6]), .B8in(imembus[7]), .B1in(imembus[0]), .B2in(imembus[1]), .B3in(imembus[2]),
    .B4in(imembus[3]), .B5in(imembus[4]), .A6out(srcbus[5]), .A7out(srcbus[6]), .A8out(srcbus[7]),
    .A1out(srcbus[0]), .A2out(srcbus[1]), .A3out(srcbus[2]), .A4out(srcbus[3]), .A5out(srcbus[4]),
    .B8out(imembus[7]), .B6out(imembus[5]), .B7out(imembus[6]), .B1out(imembus[0]), .B2out(imembus[1]),
    .B3out(imembus[2]), .B4out(imembus[3]), .B5out(imembus[4]));  // open: DIR
  T74245 t74245_12 (
    .A6in(iregbus[5]), .A7in(iregbus[6]), .A8in(iregbus[7]), .A1in(iregbus[0]), .A2in(iregbus[1]),
    .A3in(iregbus[2]), .A4in(iregbus[3]), .A5in(iregbus[4]), .DIR(1'b1), .nOE(isimm), .B6in(srcbus[5]),
    .B7in(srcbus[6]), .B8in(srcbus[7]), .B1in(srcbus[0]), .B2in(srcbus[1]), .B3in(srcbus[2]),
    .B4in(srcbus[3]), .B5in(srcbus[4]), .A6out(iregbus[5]), .A7out(iregbus[6]), .A8out(iregbus[7]),
    .A1out(iregbus[0]), .A2out(iregbus[1]), .A3out(iregbus[2]), .A4out(iregbus[3]), .A5out(iregbus[4]),
    .B8out(srcbus[7]), .B6out(srcbus[5]), .B7out(srcbus[6]), .B1out(srcbus[0]), .B2out(srcbus[1]),
    .B3out(srcbus[2]), .B4out(srcbus[3]), .B5out(srcbus[4]));
  T74245 t74245_13 (
    .A6in(t74245_13_a1out[5]), .A7in(t74245_13_a1out[6]), .A8in(t74245_13_a1out[7]),
    .A1in(t74245_13_a1out[0]), .A2in(t74245_13_a1out[1]), .A3in(t74245_13_a1out[2]),
    .A4in(t74245_13_a1out[3]), .A5in(t74245_13_a1out[4]), .nOE(n7404_3_pin8), .B6in(imembus[5]),
    .B7in(imembus[6]), .B8in(imembus[7]), .B1in(imembus[0]), .B2in(imembus[1]), .B3in(imembus[2]),
    .B4in(imembus[3]), .B5in(imembus[4]), .A6out(t74245_13_a1out[5]), .A7out(t74245_13_a1out[6]),
    .A8out(t74245_13_a1out[7]), .A1out(t74245_13_a1out[0]), .A2out(t74245_13_a1out[1]),
    .A3out(t74245_13_a1out[2]), .A4out(t74245_13_a1out[3]), .A5out(t74245_13_a1out[4]), .B8out(imembus[7]),
    .B6out(imembus[5]), .B7out(imembus[6]), .B1out(imembus[0]), .B2out(imembus[1]), .B3out(imembus[2]),
    .B4out(imembus[3]), .B5out(imembus[4]));  // open: DIR
  T74245 t74245_14 (
    .A6in(ialubus[5]), .A7in(ialubus[6]), .A8in(ialubus[7]), .A1in(ialubus[0]), .A2in(ialubus[1]),
    .A3in(ialubus[2]), .A4in(ialubus[3]), .A5in(ialubus[4]), .DIR(1'b1), .nOE(n7404_3_pin10),
    .B6in(t74245_13_a1out[5]), .B7in(t74245_13_a1out[6]), .B8in(t74245_13_a1out[7]),
    .B1in(t74245_13_a1out[0]), .B2in(t74245_13_a1out[1]), .B3in(t74245_13_a1out[2]),
    .B4in(t74245_13_a1out[3]), .B5in(t74245_13_a1out[4]), .A6out(ialubus[5]), .A7out(ialubus[6]),
    .A8out(ialubus[7]), .A1out(ialubus[0]), .A2out(ialubus[1]), .A3out(ialubus[2]), .A4out(ialubus[3]),
    .A5out(ialubus[4]), .B8out(t74245_13_a1out[7]), .B6out(t74245_13_a1out[5]), .B7out(t74245_13_a1out[6]),
    .B1out(t74245_13_a1out[0]), .B2out(t74245_13_a1out[1]), .B3out(t74245_13_a1out[2]),
    .B4out(t74245_13_a1out[3]), .B5out(t74245_13_a1out[4]));
  T74257 t74257_6 (
    .nOE(1'b0), .isB(alumode[0]), .A1(oioaddr[1]), .B1(1'b0), .A2(oioaddr[0]), .B2(regds), .A3(oioaddr[2]),
    .B3(1'b0), .A4(1'b0), .B4(1'b1), .Y1(t74257_6_y1), .Y2(t74257_6_y2), .Y3(t74257_6_y3), .Y4(t74257_6_y4));
  _7404 u_7404_2 (
    .pin1(s), .pin2(n7404_2_pin2), .pin3(o), .pin4(n7404_2_pin4), .pin5(n7432_2_pin3), .pin6(n7404_2_pin6),
    .pin13(z), .pin12(n7404_2_pin12), .pin11(n7432_2_pin11), .pin10(n7404_2_pin10), .pin9(c),
    .pin8(n7404_2_pin8));
  T74245 t74245_15 (
    .A6in(iregbus[13]), .A7in(iregbus[14]), .A8in(iregbus[15]), .A1in(iregbus[8]), .A2in(iregbus[9]),
    .A3in(iregbus[10]), .A4in(iregbus[11]), .A5in(iregbus[12]), .DIR(1'b1), .nOE(isimm), .B6in(srcbus[13]),
    .B7in(srcbus[14]), .B8in(srcbus[15]), .B1in(srcbus[8]), .B2in(srcbus[9]), .B3in(srcbus[10]),
    .B4in(srcbus[11]), .B5in(srcbus[12]), .A6out(iregbus[13]), .A7out(iregbus[14]), .A8out(iregbus[15]),
    .A1out(iregbus[8]), .A2out(iregbus[9]), .A3out(iregbus[10]), .A4out(iregbus[11]), .A5out(iregbus[12]),
    .B8out(srcbus[15]), .B6out(srcbus[13]), .B7out(srcbus[14]), .B1out(srcbus[8]), .B2out(srcbus[9]),
    .B3out(srcbus[10]), .B4out(srcbus[11]), .B5out(srcbus[12]));
  T74245 t74245_16 (
    .A6in(ialubus[13]), .A7in(ialubus[14]), .A8in(ialubus[15]), .A1in(ialubus[8]), .A2in(ialubus[9]),
    .A3in(ialubus[10]), .A4in(ialubus[11]), .A5in(ialubus[12]), .DIR(1'b1), .nOE(n7404_3_pin10),
    .B6in(t74245_13_a1out[13]), .B7in(t74245_13_a1out[14]), .B8in(t74245_13_a1out[15]),
    .B1in(t74245_13_a1out[8]), .B2in(t74245_13_a1out[9]), .B3in(t74245_13_a1out[10]),
    .B4in(t74245_13_a1out[11]), .B5in(t74245_13_a1out[12]), .A6out(ialubus[13]), .A7out(ialubus[14]),
    .A8out(ialubus[15]), .A1out(ialubus[8]), .A2out(ialubus[9]), .A3out(ialubus[10]), .A4out(ialubus[11]),
    .A5out(ialubus[12]), .B8out(t74245_13_a1out[15]), .B6out(t74245_13_a1out[13]),
    .B7out(t74245_13_a1out[14]), .B1out(t74245_13_a1out[8]), .B2out(t74245_13_a1out[9]),
    .B3out(t74245_13_a1out[10]), .B4out(t74245_13_a1out[11]), .B5out(t74245_13_a1out[12]));
  T744067 t744067_1 (
    .nE(1'b0), .S0(oioaddr[0]), .S1(oioaddr[1]), .S2(oioaddr[2]), .S3(opcode[0]), .Y0in(n7486_1_pin5),
    .Y1in(z), .Y2in(n7404_2_pin12), .Y3in(n7486_1_pin6), .Y4in(n7432_2_pin11), .Y5in(n7404_2_pin10),
    .Y6in(n7486_1_pin3), .Y7in(o), .Y8in(ibusy), .Y9in(s), .Y10in(n7404_2_pin2), .Y11in(n7404_2_pin4),
    .Y12in(n7432_2_pin3), .Y13in(n7404_2_pin6), .Y14in(c), .Y15in(n7404_2_pin8), .Zout(should_jump));
  T74245 t74245_17 (
    .A6in(t74245_17_a1out[5]), .A7in(t74245_17_a1out[6]), .A8in(t74245_17_a1out[7]),
    .A1in(t74245_17_a1out[0]), .A2in(t74245_17_a1out[1]), .A3in(t74245_17_a1out[2]),
    .A4in(t74245_17_a1out[3]), .A5in(t74245_17_a1out[4]), .nOE(n7404_4_pin10), .B6in(t74245_17_b5out[1]),
    .B7in(t74245_17_b5out[2]), .B8in(t74245_17_b5out[3]), .B1in(t74245_17_b1out[0]), .B2in(intid_saved[0]),
    .B3in(intid_saved[1]), .B4in(intid_saved[2]), .B5in(t74245_17_b5out[0]), .A6out(t74245_17_a1out[5]),
    .A7out(t74245_17_a1out[6]), .A8out(t74245_17_a1out[7]), .A1out(t74245_17_a1out[0]),
    .A2out(t74245_17_a1out[1]), .A3out(t74245_17_a1out[2]), .A4out(t74245_17_a1out[3]),
    .A5out(t74245_17_a1out[4]), .B8out(t74245_17_b5out[3]), .B6out(t74245_17_b5out[1]),
    .B7out(t74245_17_b5out[2]), .B1out(t74245_17_b1out[0]), .B2out(intid_saved[0]), .B3out(intid_saved[1]),
    .B4out(intid_saved[2]), .B5out(t74245_17_b5out[0]));  // open: DIR
  T74245 t74245_18 (
    .A6in(t74245_7_b1out[5]), .A7in(t74245_7_b1out[6]), .A8in(t74245_7_b1out[7]), .A1in(t74245_7_b1out[0]),
    .A2in(t74245_7_b1out[1]), .A3in(t74245_7_b1out[2]), .A4in(t74245_7_b1out[3]), .A5in(t74245_7_b1out[4]),
    .DIR(1'b1), .nOE(isint), .B6in(t74245_17_a1out[5]), .B7in(t74245_17_a1out[6]), .B8in(t74245_17_a1out[7]),
    .B1in(t74245_17_a1out[0]), .B2in(t74245_17_a1out[1]), .B3in(t74245_17_a1out[2]),
    .B4in(t74245_17_a1out[3]), .B5in(t74245_17_a1out[4]), .A6out(t74245_7_b1out[5]),
    .A7out(t74245_7_b1out[6]), .A8out(t74245_7_b1out[7]), .A1out(t74245_7_b1out[0]),
    .A2out(t74245_7_b1out[1]), .A3out(t74245_7_b1out[2]), .A4out(t74245_7_b1out[3]),
    .A5out(t74245_7_b1out[4]), .B8out(t74245_17_a1out[7]), .B6out(t74245_17_a1out[5]),
    .B7out(t74245_17_a1out[6]), .B1out(t74245_17_a1out[0]), .B2out(t74245_17_a1out[1]),
    .B3out(t74245_17_a1out[2]), .B4out(t74245_17_a1out[3]), .B5out(t74245_17_a1out[4]));
  T74245 t74245_19 (
    .A6in(srcbus[13]), .A7in(srcbus[14]), .A8in(srcbus[15]), .A1in(srcbus[8]), .A2in(srcbus[9]),
    .A3in(srcbus[10]), .A4in(srcbus[11]), .A5in(srcbus[12]), .DIR(1'b0), .nOE(n7404_3_pin12),
    .B6in(imembus[13]), .B7in(imembus[14]), .B8in(imembus[15]), .B1in(imembus[8]), .B2in(imembus[9]),
    .B3in(imembus[10]), .B4in(imembus[11]), .B5in(imembus[12]), .A6out(srcbus[13]), .A7out(srcbus[14]),
    .A8out(srcbus[15]), .A1out(srcbus[8]), .A2out(srcbus[9]), .A3out(srcbus[10]), .A4out(srcbus[11]),
    .A5out(srcbus[12]), .B8out(imembus[15]), .B6out(imembus[13]), .B7out(imembus[14]), .B1out(imembus[8]),
    .B2out(imembus[9]), .B3out(imembus[10]), .B4out(imembus[11]), .B5out(imembus[12]));
  T74245 t74245_20 (
    .A6in(t74245_13_a1out[13]), .A7in(t74245_13_a1out[14]), .A8in(t74245_13_a1out[15]),
    .A1in(t74245_13_a1out[8]), .A2in(t74245_13_a1out[9]), .A3in(t74245_13_a1out[10]),
    .A4in(t74245_13_a1out[11]), .A5in(t74245_13_a1out[12]), .DIR(1'b0), .nOE(n7404_3_pin8),
    .B6in(imembus[13]), .B7in(imembus[14]), .B8in(imembus[15]), .B1in(imembus[8]), .B2in(imembus[9]),
    .B3in(imembus[10]), .B4in(imembus[11]), .B5in(imembus[12]), .A6out(t74245_13_a1out[13]),
    .A7out(t74245_13_a1out[14]), .A8out(t74245_13_a1out[15]), .A1out(t74245_13_a1out[8]),
    .A2out(t74245_13_a1out[9]), .A3out(t74245_13_a1out[10]), .A4out(t74245_13_a1out[11]),
    .A5out(t74245_13_a1out[12]), .B8out(imembus[15]), .B6out(imembus[13]), .B7out(imembus[14]),
    .B1out(imembus[8]), .B2out(imembus[9]), .B3out(imembus[10]), .B4out(imembus[11]), .B5out(imembus[12]));
  T74257 t74257_7 (
    .nOE(1'b0), .isB(alumode[1]), .A1(t74257_6_y1), .B1(1'b0), .A2(t74257_6_y2), .B2(alumode[0]),
    .A3(t74257_6_y3), .B3(1'b0), .A4(t74257_6_y4), .B4(1'b0), .Y1(oaluop[1]), .Y2(oaluop[0]), .Y3(oaluop[2]),
    .Y4(oaluop[3]));
  T74245 t74245_21 (
    .A6in(t74245_17_a1out[13]), .A7in(t74245_17_a1out[14]), .A8in(t74245_17_a1out[15]),
    .A1in(t74245_17_a1out[8]), .A2in(t74245_17_a1out[9]), .A3in(t74245_17_a1out[10]),
    .A4in(t74245_17_a1out[11]), .A5in(t74245_17_a1out[12]), .DIR(1'b0), .nOE(n7404_4_pin10),
    .B6in(t74245_17_b5out[9]), .B7in(t74245_17_b5out[10]), .B8in(t74245_17_b5out[11]),
    .B1in(t74245_17_b5out[4]), .B2in(t74245_17_b5out[5]), .B3in(t74245_17_b5out[6]),
    .B4in(t74245_17_b5out[7]), .B5in(t74245_17_b5out[8]), .A6out(t74245_17_a1out[13]),
    .A7out(t74245_17_a1out[14]), .A8out(t74245_17_a1out[15]), .A1out(t74245_17_a1out[8]),
    .A2out(t74245_17_a1out[9]), .A3out(t74245_17_a1out[10]), .A4out(t74245_17_a1out[11]),
    .A5out(t74245_17_a1out[12]), .B8out(t74245_17_b5out[11]), .B6out(t74245_17_b5out[9]),
    .B7out(t74245_17_b5out[10]), .B1out(t74245_17_b5out[4]), .B2out(t74245_17_b5out[5]),
    .B3out(t74245_17_b5out[6]), .B4out(t74245_17_b5out[7]), .B5out(t74245_17_b5out[8]));
  T74245 t74245_22 (
    .A6in(t74245_7_b1out[13]), .A7in(t74245_7_b1out[14]), .A8in(t74245_7_b1out[15]),
    .A1in(t74245_7_b1out[8]), .A2in(t74245_7_b1out[9]), .A3in(t74245_7_b1out[10]), .A4in(t74245_7_b1out[11]),
    .A5in(t74245_7_b1out[12]), .DIR(1'b1), .nOE(isint), .B6in(t74245_17_a1out[13]),
    .B7in(t74245_17_a1out[14]), .B8in(t74245_17_a1out[15]), .B1in(t74245_17_a1out[8]),
    .B2in(t74245_17_a1out[9]), .B3in(t74245_17_a1out[10]), .B4in(t74245_17_a1out[11]),
    .B5in(t74245_17_a1out[12]), .A6out(t74245_7_b1out[13]), .A7out(t74245_7_b1out[14]),
    .A8out(t74245_7_b1out[15]), .A1out(t74245_7_b1out[8]), .A2out(t74245_7_b1out[9]),
    .A3out(t74245_7_b1out[10]), .A4out(t74245_7_b1out[11]), .A5out(t74245_7_b1out[12]),
    .B8out(t74245_17_a1out[15]), .B6out(t74245_17_a1out[13]), .B7out(t74245_17_a1out[14]),
    .B1out(t74245_17_a1out[8]), .B2out(t74245_17_a1out[9]), .B3out(t74245_17_a1out[10]),
    .B4out(t74245_17_a1out[11]), .B5out(t74245_17_a1out[12]));
  _7404 u_7404_3 (
    .pin1(oioop[0]), .pin2(n7404_3_pin2), .pin3(n7404_3_pin3), .pin4(n7404_3_pin4), .pin5(regsrc),
    .pin6(n7404_3_pin6), .pin13(isimm), .pin12(n7404_3_pin12), .pin11(n7404_3_pin11), .pin10(n7404_3_pin10),
    .pin9(n7404_3_pin9), .pin8(n7404_3_pin8));
  _7408 u_7408_2 (
    .pin4(n7404_3_pin4), .pin5(n7404_3_pin6), .pin6(n7404_3_pin11), .pin13(oioop[1]), .pin12(n7404_3_pin2),
    .pin11(n7404_3_pin3), .pin10(regsrc), .pin9(n7404_3_pin4), .pin8(n7404_3_pin9));  // open: pin1, pin2, pin3
  _7404 u_7404_4 (
    .pin13(isret), .pin12(n7404_4_pin12), .pin11(isint), .pin10(n7404_4_pin10), .pin9(next_instr),
    .pin8(n7404_4_pin8));  // open: pin1, pin2, pin3, pin4, pin5, pin6
  T74245 t74245_23 (
    .A6in(iregbus[5]), .A7in(iregbus[6]), .A8in(iregbus[7]), .A1in(iregbus[0]), .A2in(iregbus[1]),
    .A3in(iregbus[2]), .A4in(iregbus[3]), .A5in(iregbus[4]), .DIR(1'b1), .nOE(isimm), .B6in(srctempbus[5]),
    .B7in(srctempbus[6]), .B8in(srctempbus[7]), .B1in(srctempbus[0]), .B2in(srctempbus[1]),
    .B3in(srctempbus[2]), .B4in(srctempbus[3]), .B5in(srctempbus[4]), .A6out(iregbus[5]), .A7out(iregbus[6]),
    .A8out(iregbus[7]), .A1out(iregbus[0]), .A2out(iregbus[1]), .A3out(iregbus[2]), .A4out(iregbus[3]),
    .A5out(iregbus[4]), .B8out(srctempbus[7]), .B6out(srctempbus[5]), .B7out(srctempbus[6]),
    .B1out(srctempbus[0]), .B2out(srctempbus[1]), .B3out(srctempbus[2]), .B4out(srctempbus[3]),
    .B5out(srctempbus[4]));
  T74245 t74245_24 (
    .A6in(srctempbus[5]), .A7in(srctempbus[6]), .A8in(srctempbus[7]), .A1in(srctempbus[0]),
    .A2in(srctempbus[1]), .A3in(srctempbus[2]), .A4in(srctempbus[3]), .A5in(srctempbus[4]),
    .nOE(n7404_3_pin12), .B6in(tempreg[5]), .B7in(tempreg[6]), .B8in(tempreg[7]), .B1in(tempreg[0]),
    .B2in(tempreg[1]), .B3in(tempreg[2]), .B4in(tempreg[3]), .B5in(tempreg[4]), .A6out(srctempbus[5]),
    .A7out(srctempbus[6]), .A8out(srctempbus[7]), .A1out(srctempbus[0]), .A2out(srctempbus[1]),
    .A3out(srctempbus[2]), .A4out(srctempbus[3]), .A5out(srctempbus[4]), .B8out(tempreg[7]),
    .B6out(tempreg[5]), .B7out(tempreg[6]), .B1out(tempreg[0]), .B2out(tempreg[1]), .B3out(tempreg[2]),
    .B4out(tempreg[3]), .B5out(tempreg[4]));  // open: DIR
  T74245 t74245_25 (
    .A6in(t74245_13_a1out[5]), .A7in(t74245_13_a1out[6]), .A8in(t74245_13_a1out[7]),
    .A1in(t74245_13_a1out[0]), .A2in(t74245_13_a1out[1]), .A3in(t74245_13_a1out[2]),
    .A4in(t74245_13_a1out[3]), .A5in(t74245_13_a1out[4]), .nOE(n7404_3_pin4), .B6in(iiobus[5]),
    .B7in(iiobus[6]), .B8in(iiobus[7]), .B1in(iiobus[0]), .B2in(iiobus[1]), .B3in(iiobus[2]),
    .B4in(iiobus[3]), .B5in(iiobus[4]), .A6out(t74245_13_a1out[5]), .A7out(t74245_13_a1out[6]),
    .A8out(t74245_13_a1out[7]), .A1out(t74245_13_a1out[0]), .A2out(t74245_13_a1out[1]),
    .A3out(t74245_13_a1out[2]), .A4out(t74245_13_a1out[3]), .A5out(t74245_13_a1out[4]), .B8out(iiobus[7]),
    .B6out(iiobus[5]), .B7out(iiobus[6]), .B1out(iiobus[0]), .B2out(iiobus[1]), .B3out(iiobus[2]),
    .B4out(iiobus[3]), .B5out(iiobus[4]));  // open: DIR
  _74377 u_74377_9 (
    .pin1(n7404_4_pin8), .pin2(ip[1]), .pin3(t74245_17_a1out[1]), .pin4(t74245_17_a1out[3]), .pin5(ip[3]),
    .pin6(ip[5]), .pin7(t74245_17_a1out[5]), .pin8(t74245_17_a1out[7]), .pin9(ip[7]), .pin19(ip[0]),
    .pin18(t74245_17_a1out[0]), .pin17(t74245_17_a1out[2]), .pin16(ip[2]), .pin15(ip[4]),
    .pin14(t74245_17_a1out[4]), .pin13(t74245_17_a1out[6]), .pin12(ip[6]), .pin11(CLK));
  T74245 t74245_26 (
    .A6in(srctempbus[13]), .A7in(srctempbus[14]), .A8in(srctempbus[15]), .A1in(srctempbus[8]),
    .A2in(srctempbus[9]), .A3in(srctempbus[10]), .A4in(srctempbus[11]), .A5in(srctempbus[12]), .DIR(1'b0),
    .nOE(n7404_3_pin12), .B6in(tempreg[13]), .B7in(tempreg[14]), .B8in(tempreg[15]), .B1in(tempreg[8]),
    .B2in(tempreg[9]), .B3in(tempreg[10]), .B4in(tempreg[11]), .B5in(tempreg[12]), .A6out(srctempbus[13]),
    .A7out(srctempbus[14]), .A8out(srctempbus[15]), .A1out(srctempbus[8]), .A2out(srctempbus[9]),
    .A3out(srctempbus[10]), .A4out(srctempbus[11]), .A5out(srctempbus[12]), .B8out(tempreg[15]),
    .B6out(tempreg[13]), .B7out(tempreg[14]), .B1out(tempreg[8]), .B2out(tempreg[9]), .B3out(tempreg[10]),
    .B4out(tempreg[11]), .B5out(tempreg[12]));
  T74245 t74245_27 (
    .A6in(iregbus[13]), .A7in(iregbus[14]), .A8in(iregbus[15]), .A1in(iregbus[8]), .A2in(iregbus[9]),
    .A3in(iregbus[10]), .A4in(iregbus[11]), .A5in(iregbus[12]), .DIR(1'b1), .nOE(isimm),
    .B6in(srctempbus[13]), .B7in(srctempbus[14]), .B8in(srctempbus[15]), .B1in(srctempbus[8]),
    .B2in(srctempbus[9]), .B3in(srctempbus[10]), .B4in(srctempbus[11]), .B5in(srctempbus[12]),
    .A6out(iregbus[13]), .A7out(iregbus[14]), .A8out(iregbus[15]), .A1out(iregbus[8]), .A2out(iregbus[9]),
    .A3out(iregbus[10]), .A4out(iregbus[11]), .A5out(iregbus[12]), .B8out(srctempbus[15]),
    .B6out(srctempbus[13]), .B7out(srctempbus[14]), .B1out(srctempbus[8]), .B2out(srctempbus[9]),
    .B3out(srctempbus[10]), .B4out(srctempbus[11]), .B5out(srctempbus[12]));
  T74245 t74245_28 (
    .A6in(t74245_13_a1out[13]), .A7in(t74245_13_a1out[14]), .A8in(t74245_13_a1out[15]),
    .A1in(t74245_13_a1out[8]), .A2in(t74245_13_a1out[9]), .A3in(t74245_13_a1out[10]),
    .A4in(t74245_13_a1out[11]), .A5in(t74245_13_a1out[12]), .DIR(1'b0), .nOE(n7404_3_pin4),
    .B6in(iiobus[13]), .B7in(iiobus[14]), .B8in(iiobus[15]), .B1in(iiobus[8]), .B2in(iiobus[9]),
    .B3in(iiobus[10]), .B4in(iiobus[11]), .B5in(iiobus[12]), .A6out(t74245_13_a1out[13]),
    .A7out(t74245_13_a1out[14]), .A8out(t74245_13_a1out[15]), .A1out(t74245_13_a1out[8]),
    .A2out(t74245_13_a1out[9]), .A3out(t74245_13_a1out[10]), .A4out(t74245_13_a1out[11]),
    .A5out(t74245_13_a1out[12]), .B8out(iiobus[15]), .B6out(iiobus[13]), .B7out(iiobus[14]),
    .B1out(iiobus[8]), .B2out(iiobus[9]), .B3out(iiobus[10]), .B4out(iiobus[11]), .B5out(iiobus[12]));
  _74377 u_74377_10 (
    .pin1(n7404_4_pin8), .pin2(ip[9]), .pin3(t74245_17_a1out[9]), .pin4(t74245_17_a1out[11]), .pin5(ip[11]),
    .pin6(ip[13]), .pin7(t74245_17_a1out[13]), .pin8(t74245_17_a1out[15]), .pin9(ip[15]), .pin19(ip[8]),
    .pin18(t74245_17_a1out[8]), .pin17(t74245_17_a1out[10]), .pin16(ip[10]), .pin15(ip[12]),
    .pin14(t74245_17_a1out[12]), .pin13(t74245_17_a1out[14]), .pin12(ip[14]), .pin11(CLK));
  T74245 t74245_29 (
    .A6in(oregbus[5]), .A7in(oregbus[6]), .A8in(oregbus[7]), .A1in(oregbus[0]), .A2in(oregbus[1]),
    .A3in(oregbus[2]), .A4in(oregbus[3]), .A5in(oregbus[4]), .nOE(n7404_5_pin4), .B6in(t74245_13_a1out[5]),
    .B7in(t74245_13_a1out[6]), .B8in(t74245_13_a1out[7]), .B1in(t74245_13_a1out[0]),
    .B2in(t74245_13_a1out[1]), .B3in(t74245_13_a1out[2]), .B4in(t74245_13_a1out[3]),
    .B5in(t74245_13_a1out[4]), .A6out(oregbus[5]), .A7out(oregbus[6]), .A8out(oregbus[7]),
    .A1out(oregbus[0]), .A2out(oregbus[1]), .A3out(oregbus[2]), .A4out(oregbus[3]), .A5out(oregbus[4]),
    .B8out(t74245_13_a1out[7]), .B6out(t74245_13_a1out[5]), .B7out(t74245_13_a1out[6]),
    .B1out(t74245_13_a1out[0]), .B2out(t74245_13_a1out[1]), .B3out(t74245_13_a1out[2]),
    .B4out(t74245_13_a1out[3]), .B5out(t74245_13_a1out[4]));  // open: DIR
  T74245 t74245_30 (
    .A6in(oregbus[13]), .A7in(oregbus[14]), .A8in(oregbus[15]), .A1in(oregbus[8]), .A2in(oregbus[9]),
    .A3in(oregbus[10]), .A4in(oregbus[11]), .A5in(oregbus[12]), .DIR(1'b0), .nOE(n7404_5_pin4),
    .B6in(t74245_13_a1out[13]), .B7in(t74245_13_a1out[14]), .B8in(t74245_13_a1out[15]),
    .B1in(t74245_13_a1out[8]), .B2in(t74245_13_a1out[9]), .B3in(t74245_13_a1out[10]),
    .B4in(t74245_13_a1out[11]), .B5in(t74245_13_a1out[12]), .A6out(oregbus[13]), .A7out(oregbus[14]),
    .A8out(oregbus[15]), .A1out(oregbus[8]), .A2out(oregbus[9]), .A3out(oregbus[10]), .A4out(oregbus[11]),
    .A5out(oregbus[12]), .B8out(t74245_13_a1out[15]), .B6out(t74245_13_a1out[13]),
    .B7out(t74245_13_a1out[14]), .B1out(t74245_13_a1out[8]), .B2out(t74245_13_a1out[9]),
    .B3out(t74245_13_a1out[10]), .B4out(t74245_13_a1out[11]), .B5out(t74245_13_a1out[12]));
  T74245 t74245_31 (
    .A6in(t74245_31_a1out[5]), .A7in(t74245_31_a1out[6]), .A8in(t74245_31_a1out[7]),
    .A1in(t74245_31_a1out[0]), .A2in(t74245_31_a1out[1]), .A3in(t74245_31_a1out[2]),
    .A4in(t74245_31_a1out[3]), .A5in(t74245_31_a1out[4]), .nOE(n7404_5_pin2), .B6in(ipnext[5]),
    .B7in(ipnext[6]), .B8in(ipnext[7]), .B1in(ipnext[0]), .B2in(ipnext[1]), .B3in(ipnext[2]),
    .B4in(ipnext[3]), .B5in(ipnext[4]), .A6out(t74245_31_a1out[5]), .A7out(t74245_31_a1out[6]),
    .A8out(t74245_31_a1out[7]), .A1out(t74245_31_a1out[0]), .A2out(t74245_31_a1out[1]),
    .A3out(t74245_31_a1out[2]), .A4out(t74245_31_a1out[3]), .A5out(t74245_31_a1out[4]), .B8out(ipnext[7]),
    .B6out(ipnext[5]), .B7out(ipnext[6]), .B1out(ipnext[0]), .B2out(ipnext[1]), .B3out(ipnext[2]),
    .B4out(ipnext[3]), .B5out(ipnext[4]));  // open: DIR
  T74245 t74245_32 (
    .A6in(ip[5]), .A7in(ip[6]), .A8in(ip[7]), .A1in(ip[0]), .A2in(ip[1]), .A3in(ip[2]), .A4in(ip[3]),
    .A5in(ip[4]), .DIR(1'b1), .nOE(isjump), .B6in(t74245_31_a1out[5]), .B7in(t74245_31_a1out[6]),
    .B8in(t74245_31_a1out[7]), .B1in(t74245_31_a1out[0]), .B2in(t74245_31_a1out[1]),
    .B3in(t74245_31_a1out[2]), .B4in(t74245_31_a1out[3]), .B5in(t74245_31_a1out[4]), .A6out(ip[5]),
    .A7out(ip[6]), .A8out(ip[7]), .A1out(ip[0]), .A2out(ip[1]), .A3out(ip[2]), .A4out(ip[3]), .A5out(ip[4]),
    .B8out(t74245_31_a1out[7]), .B6out(t74245_31_a1out[5]), .B7out(t74245_31_a1out[6]),
    .B1out(t74245_31_a1out[0]), .B2out(t74245_31_a1out[1]), .B3out(t74245_31_a1out[2]),
    .B4out(t74245_31_a1out[3]), .B5out(t74245_31_a1out[4]));
  T74245 t74245_33 (
    .A6in(oiobus[5]), .A7in(oiobus[6]), .A8in(oiobus[7]), .A1in(oiobus[0]), .A2in(oiobus[1]),
    .A3in(oiobus[2]), .A4in(oiobus[3]), .A5in(oiobus[4]), .nOE(n7404_5_pin12), .B6in(srcbus[5]),
    .B7in(srcbus[6]), .B8in(srcbus[7]), .B1in(srcbus[0]), .B2in(srcbus[1]), .B3in(srcbus[2]),
    .B4in(srcbus[3]), .B5in(srcbus[4]), .A6out(oiobus[5]), .A7out(oiobus[6]), .A8out(oiobus[7]),
    .A1out(oiobus[0]), .A2out(oiobus[1]), .A3out(oiobus[2]), .A4out(oiobus[3]), .A5out(oiobus[4]),
    .B8out(srcbus[7]), .B6out(srcbus[5]), .B7out(srcbus[6]), .B1out(srcbus[0]), .B2out(srcbus[1]),
    .B3out(srcbus[2]), .B4out(srcbus[3]), .B5out(srcbus[4]));  // open: DIR
  T74245 t74245_34 (
    .A6in(ip[13]), .A7in(ip[14]), .A8in(ip[15]), .A1in(ip[8]), .A2in(ip[9]), .A3in(ip[10]), .A4in(ip[11]),
    .A5in(ip[12]), .DIR(1'b1), .nOE(isjump), .B6in(t74245_31_a1out[13]), .B7in(t74245_31_a1out[14]),
    .B8in(t74245_31_a1out[15]), .B1in(t74245_31_a1out[8]), .B2in(t74245_31_a1out[9]),
    .B3in(t74245_31_a1out[10]), .B4in(t74245_31_a1out[11]), .B5in(t74245_31_a1out[12]), .A6out(ip[13]),
    .A7out(ip[14]), .A8out(ip[15]), .A1out(ip[8]), .A2out(ip[9]), .A3out(ip[10]), .A4out(ip[11]),
    .A5out(ip[12]), .B8out(t74245_31_a1out[15]), .B6out(t74245_31_a1out[13]), .B7out(t74245_31_a1out[14]),
    .B1out(t74245_31_a1out[8]), .B2out(t74245_31_a1out[9]), .B3out(t74245_31_a1out[10]),
    .B4out(t74245_31_a1out[11]), .B5out(t74245_31_a1out[12]));
  T74245 t74245_35 (
    .A6in(oiobus[13]), .A7in(oiobus[14]), .A8in(oiobus[15]), .A1in(oiobus[8]), .A2in(oiobus[9]),
    .A3in(oiobus[10]), .A4in(oiobus[11]), .A5in(oiobus[12]), .DIR(1'b0), .nOE(n7404_5_pin12),
    .B6in(srcbus[13]), .B7in(srcbus[14]), .B8in(srcbus[15]), .B1in(srcbus[8]), .B2in(srcbus[9]),
    .B3in(srcbus[10]), .B4in(srcbus[11]), .B5in(srcbus[12]), .A6out(oiobus[13]), .A7out(oiobus[14]),
    .A8out(oiobus[15]), .A1out(oiobus[8]), .A2out(oiobus[9]), .A3out(oiobus[10]), .A4out(oiobus[11]),
    .A5out(oiobus[12]), .B8out(srcbus[15]), .B6out(srcbus[13]), .B7out(srcbus[14]), .B1out(srcbus[8]),
    .B2out(srcbus[9]), .B3out(srcbus[10]), .B4out(srcbus[11]), .B5out(srcbus[12]));
  T74245 t74245_36 (
    .A6in(t74245_31_a1out[13]), .A7in(t74245_31_a1out[14]), .A8in(t74245_31_a1out[15]),
    .A1in(t74245_31_a1out[8]), .A2in(t74245_31_a1out[9]), .A3in(t74245_31_a1out[10]),
    .A4in(t74245_31_a1out[11]), .A5in(t74245_31_a1out[12]), .DIR(1'b0), .nOE(n7404_5_pin2),
    .B6in(ipnext[13]), .B7in(ipnext[14]), .B8in(ipnext[15]), .B1in(ipnext[8]), .B2in(ipnext[9]),
    .B3in(ipnext[10]), .B4in(ipnext[11]), .B5in(ipnext[12]), .A6out(t74245_31_a1out[13]),
    .A7out(t74245_31_a1out[14]), .A8out(t74245_31_a1out[15]), .A1out(t74245_31_a1out[8]),
    .A2out(t74245_31_a1out[9]), .A3out(t74245_31_a1out[10]), .A4out(t74245_31_a1out[11]),
    .A5out(t74245_31_a1out[12]), .B8out(ipnext[15]), .B6out(ipnext[13]), .B7out(ipnext[14]),
    .B1out(ipnext[8]), .B2out(ipnext[9]), .B3out(ipnext[10]), .B4out(ipnext[11]), .B5out(ipnext[12]));
  _7404 u_7404_5 (
    .pin1(isjump), .pin2(n7404_5_pin2), .pin3(oregwe), .pin4(n7404_5_pin4), .pin5(oaluop[3]),
    .pin6(n7404_5_pin6), .pin13(n7404_5_pin13), .pin12(n7404_5_pin12));  // open: pin11, pin10, pin9, pin8
  T74245 t74245_37 (
    .A6in(t74245_31_a1out[5]), .A7in(t74245_31_a1out[6]), .A8in(t74245_31_a1out[7]),
    .A1in(t74245_31_a1out[0]), .A2in(t74245_31_a1out[1]), .A3in(t74245_31_a1out[2]),
    .A4in(t74245_31_a1out[3]), .A5in(t74245_31_a1out[4]), .DIR(1'b1), .nOE(n74139_1_pin6), .B6in(omembus[5]),
    .B7in(omembus[6]), .B8in(omembus[7]), .B1in(omembus[0]), .B2in(omembus[1]), .B3in(omembus[2]),
    .B4in(omembus[3]), .B5in(omembus[4]), .A6out(t74245_31_a1out[5]), .A7out(t74245_31_a1out[6]),
    .A8out(t74245_31_a1out[7]), .A1out(t74245_31_a1out[0]), .A2out(t74245_31_a1out[1]),
    .A3out(t74245_31_a1out[2]), .A4out(t74245_31_a1out[3]), .A5out(t74245_31_a1out[4]), .B8out(omembus[7]),
    .B6out(omembus[5]), .B7out(omembus[6]), .B1out(omembus[0]), .B2out(omembus[1]), .B3out(omembus[2]),
    .B4out(omembus[3]), .B5out(omembus[4]));
  T74245 t74245_38 (
    .A6in(oalubus[5]), .A7in(oalubus[6]), .A8in(oalubus[7]), .A1in(oalubus[0]), .A2in(oalubus[1]),
    .A3in(oalubus[2]), .A4in(oalubus[3]), .A5in(oalubus[4]), .nOE(n74139_1_pin12), .B6in(iregbus[5]),
    .B7in(iregbus[6]), .B8in(iregbus[7]), .B1in(iregbus[0]), .B2in(iregbus[1]), .B3in(iregbus[2]),
    .B4in(iregbus[3]), .B5in(iregbus[4]), .A6out(oalubus[5]), .A7out(oalubus[6]), .A8out(oalubus[7]),
    .A1out(oalubus[0]), .A2out(oalubus[1]), .A3out(oalubus[2]), .A4out(oalubus[3]), .A5out(oalubus[4]),
    .B8out(iregbus[7]), .B6out(iregbus[5]), .B7out(iregbus[6]), .B1out(iregbus[0]), .B2out(iregbus[1]),
    .B3out(iregbus[2]), .B4out(iregbus[3]), .B5out(iregbus[4]));  // open: DIR
  T74245 t74245_39 (
    .A6in(t74245_39_a6out), .A7in(t74245_39_a6out), .A8in(t74245_39_a6out), .A1in(alusrc[0]),
    .A2in(t74245_39_a6out), .A3in(t74245_39_a6out), .A4in(t74245_39_a6out), .A5in(t74245_39_a6out),
    .DIR(1'b1), .nOE(n7408_3_pin11), .B6in(oalubus[5]), .B7in(oalubus[6]), .B8in(oalubus[7]),
    .B1in(oalubus[0]), .B2in(oalubus[1]), .B3in(oalubus[2]), .B4in(oalubus[3]), .B5in(oalubus[4]),
    .A6out(t74245_39_a6out), .A7out(t74245_39_a6out), .A8out(t74245_39_a6out), .A1out(alusrc[0]),
    .A2out(t74245_39_a6out), .A3out(t74245_39_a6out), .A4out(t74245_39_a6out), .A5out(t74245_39_a6out),
    .B8out(oalubus[7]), .B6out(oalubus[5]), .B7out(oalubus[6]), .B1out(oalubus[0]), .B2out(oalubus[1]),
    .B3out(oalubus[2]), .B4out(oalubus[3]), .B5out(oalubus[4]));
  T74245 t74245_40 (
    .A6in(omembus[5]), .A7in(omembus[6]), .A8in(omembus[7]), .A1in(omembus[0]), .A2in(omembus[1]),
    .A3in(omembus[2]), .A4in(omembus[3]), .A5in(omembus[4]), .nOE(n74139_1_pin4), .B6in(iregbus[5]),
    .B7in(iregbus[6]), .B8in(iregbus[7]), .B1in(iregbus[0]), .B2in(iregbus[1]), .B3in(iregbus[2]),
    .B4in(iregbus[3]), .B5in(iregbus[4]), .A6out(omembus[5]), .A7out(omembus[6]), .A8out(omembus[7]),
    .A1out(omembus[0]), .A2out(omembus[1]), .A3out(omembus[2]), .A4out(omembus[3]), .A5out(omembus[4]),
    .B8out(iregbus[7]), .B6out(iregbus[5]), .B7out(iregbus[6]), .B1out(iregbus[0]), .B2out(iregbus[1]),
    .B3out(iregbus[2]), .B4out(iregbus[3]), .B5out(iregbus[4]));  // open: DIR
  T74245 t74245_41 (
    .A6in(oalubus[13]), .A7in(oalubus[14]), .A8in(oalubus[15]), .A1in(oalubus[8]), .A2in(oalubus[9]),
    .A3in(oalubus[10]), .A4in(oalubus[11]), .A5in(oalubus[12]), .DIR(1'b0), .nOE(n74139_1_pin12),
    .B6in(iregbus[13]), .B7in(iregbus[14]), .B8in(iregbus[15]), .B1in(iregbus[8]), .B2in(iregbus[9]),
    .B3in(iregbus[10]), .B4in(iregbus[11]), .B5in(iregbus[12]), .A6out(oalubus[13]), .A7out(oalubus[14]),
    .A8out(oalubus[15]), .A1out(oalubus[8]), .A2out(oalubus[9]), .A3out(oalubus[10]), .A4out(oalubus[11]),
    .A5out(oalubus[12]), .B8out(iregbus[15]), .B6out(iregbus[13]), .B7out(iregbus[14]), .B1out(iregbus[8]),
    .B2out(iregbus[9]), .B3out(iregbus[10]), .B4out(iregbus[11]), .B5out(iregbus[12]));
  T74245 t74245_42 (
    .A6in(t74245_39_a6out), .A7in(t74245_39_a6out), .A8in(t74245_39_a6out), .A1in(t74245_39_a6out),
    .A2in(t74245_39_a6out), .A3in(t74245_39_a6out), .A4in(t74245_39_a6out), .A5in(t74245_39_a6out),
    .DIR(1'b1), .nOE(n7408_3_pin11), .B6in(oalubus[13]), .B7in(oalubus[14]), .B8in(oalubus[15]),
    .B1in(oalubus[8]), .B2in(oalubus[9]), .B3in(oalubus[10]), .B4in(oalubus[11]), .B5in(oalubus[12]),
    .A6out(t74245_39_a6out), .A7out(t74245_39_a6out), .A8out(t74245_39_a6out), .A1out(t74245_39_a6out),
    .A2out(t74245_39_a6out), .A3out(t74245_39_a6out), .A4out(t74245_39_a6out), .A5out(t74245_39_a6out),
    .B8out(oalubus[15]), .B6out(oalubus[13]), .B7out(oalubus[14]), .B1out(oalubus[8]), .B2out(oalubus[9]),
    .B3out(oalubus[10]), .B4out(oalubus[11]), .B5out(oalubus[12]));
  T74245 t74245_43 (
    .A6in(omembus[13]), .A7in(omembus[14]), .A8in(omembus[15]), .A1in(omembus[8]), .A2in(omembus[9]),
    .A3in(omembus[10]), .A4in(omembus[11]), .A5in(omembus[12]), .DIR(1'b0), .nOE(n74139_1_pin4),
    .B6in(iregbus[13]), .B7in(iregbus[14]), .B8in(iregbus[15]), .B1in(iregbus[8]), .B2in(iregbus[9]),
    .B3in(iregbus[10]), .B4in(iregbus[11]), .B5in(iregbus[12]), .A6out(omembus[13]), .A7out(omembus[14]),
    .A8out(omembus[15]), .A1out(omembus[8]), .A2out(omembus[9]), .A3out(omembus[10]), .A4out(omembus[11]),
    .A5out(omembus[12]), .B8out(iregbus[15]), .B6out(iregbus[13]), .B7out(iregbus[14]), .B1out(iregbus[8]),
    .B2out(iregbus[9]), .B3out(iregbus[10]), .B4out(iregbus[11]), .B5out(iregbus[12]));
  T74245 t74245_44 (
    .A6in(t74245_31_a1out[13]), .A7in(t74245_31_a1out[14]), .A8in(t74245_31_a1out[15]),
    .A1in(t74245_31_a1out[8]), .A2in(t74245_31_a1out[9]), .A3in(t74245_31_a1out[10]),
    .A4in(t74245_31_a1out[11]), .A5in(t74245_31_a1out[12]), .DIR(1'b1), .nOE(n74139_1_pin6),
    .B6in(omembus[13]), .B7in(omembus[14]), .B8in(omembus[15]), .B1in(omembus[8]), .B2in(omembus[9]),
    .B3in(omembus[10]), .B4in(omembus[11]), .B5in(omembus[12]), .A6out(t74245_31_a1out[13]),
    .A7out(t74245_31_a1out[14]), .A8out(t74245_31_a1out[15]), .A1out(t74245_31_a1out[8]),
    .A2out(t74245_31_a1out[9]), .A3out(t74245_31_a1out[10]), .A4out(t74245_31_a1out[11]),
    .A5out(t74245_31_a1out[12]), .B8out(omembus[15]), .B6out(omembus[13]), .B7out(omembus[14]),
    .B1out(omembus[8]), .B2out(omembus[9]), .B3out(omembus[10]), .B4out(omembus[11]), .B5out(omembus[12]));
  _74139 u_74139_1 (
    .pin1(n74139_1_pin1), .pin2(memsrc[0]), .pin3(memsrc[1]), .pin4(n74139_1_pin4), .pin5(n74139_1_pin5),
    .pin6(n74139_1_pin6), .pin7(n74139_1_pin7), .pin15(n7404_5_pin6), .pin14(alusrc[0]), .pin13(alusrc[1]),
    .pin12(n74139_1_pin12), .pin11(n74139_1_pin11), .pin10(n74139_1_pin10), .pin9(n74139_1_pin9));
  _7408 u_7408_3 (
    .pin1(omemop[2]), .pin2(omemop[0]), .pin3(n74139_1_pin1), .pin4(oioop[1]), .pin5(oioop[0]),
    .pin6(n7404_5_pin13), .pin13(n74139_1_pin9), .pin12(n74139_1_pin10), .pin11(n7408_3_pin11));  // open: pin10, pin9, pin8
  T74245 t74245_45 (
    .A6in(oalubus[5]), .A7in(oalubus[6]), .A8in(oalubus[7]), .A1in(oalubus[0]), .A2in(oalubus[1]),
    .A3in(oalubus[2]), .A4in(oalubus[3]), .A5in(oalubus[4]), .nOE(n74139_1_pin11), .B6in(srcbus[5]),
    .B7in(srcbus[6]), .B8in(srcbus[7]), .B1in(srcbus[0]), .B2in(srcbus[1]), .B3in(srcbus[2]),
    .B4in(srcbus[3]), .B5in(srcbus[4]), .A6out(oalubus[5]), .A7out(oalubus[6]), .A8out(oalubus[7]),
    .A1out(oalubus[0]), .A2out(oalubus[1]), .A3out(oalubus[2]), .A4out(oalubus[3]), .A5out(oalubus[4]),
    .B8out(srcbus[7]), .B6out(srcbus[5]), .B7out(srcbus[6]), .B1out(srcbus[0]), .B2out(srcbus[1]),
    .B3out(srcbus[2]), .B4out(srcbus[3]), .B5out(srcbus[4]));  // open: DIR
  T74245 t74245_46 (
    .A6in(omembus[5]), .A7in(omembus[6]), .A8in(omembus[7]), .A1in(omembus[0]), .A2in(omembus[1]),
    .A3in(omembus[2]), .A4in(omembus[3]), .A5in(omembus[4]), .nOE(n74139_1_pin5), .B6in(srcbus[5]),
    .B7in(srcbus[6]), .B8in(srcbus[7]), .B1in(srcbus[0]), .B2in(srcbus[1]), .B3in(srcbus[2]),
    .B4in(srcbus[3]), .B5in(srcbus[4]), .A6out(omembus[5]), .A7out(omembus[6]), .A8out(omembus[7]),
    .A1out(omembus[0]), .A2out(omembus[1]), .A3out(omembus[2]), .A4out(omembus[3]), .A5out(omembus[4]),
    .B8out(srcbus[7]), .B6out(srcbus[5]), .B7out(srcbus[6]), .B1out(srcbus[0]), .B2out(srcbus[1]),
    .B3out(srcbus[2]), .B4out(srcbus[3]), .B5out(srcbus[4]));  // open: DIR
  T74245 t74245_47 (
    .A6in(srctempbus[5]), .A7in(srctempbus[6]), .A8in(srctempbus[7]), .A1in(srctempbus[0]),
    .A2in(srctempbus[1]), .A3in(srctempbus[2]), .A4in(srctempbus[3]), .A5in(srctempbus[4]), .DIR(1'b1),
    .nOE(n74139_1_pin7), .B6in(omembus[5]), .B7in(omembus[6]), .B8in(omembus[7]), .B1in(omembus[0]),
    .B2in(omembus[1]), .B3in(omembus[2]), .B4in(omembus[3]), .B5in(omembus[4]), .A6out(srctempbus[5]),
    .A7out(srctempbus[6]), .A8out(srctempbus[7]), .A1out(srctempbus[0]), .A2out(srctempbus[1]),
    .A3out(srctempbus[2]), .A4out(srctempbus[3]), .A5out(srctempbus[4]), .B8out(omembus[7]),
    .B6out(omembus[5]), .B7out(omembus[6]), .B1out(omembus[0]), .B2out(omembus[1]), .B3out(omembus[2]),
    .B4out(omembus[3]), .B5out(omembus[4]));
  T74245 t74245_48 (
    .A6in(oalubus[13]), .A7in(oalubus[14]), .A8in(oalubus[15]), .A1in(oalubus[8]), .A2in(oalubus[9]),
    .A3in(oalubus[10]), .A4in(oalubus[11]), .A5in(oalubus[12]), .DIR(1'b0), .nOE(n74139_1_pin11),
    .B6in(srcbus[13]), .B7in(srcbus[14]), .B8in(srcbus[15]), .B1in(srcbus[8]), .B2in(srcbus[9]),
    .B3in(srcbus[10]), .B4in(srcbus[11]), .B5in(srcbus[12]), .A6out(oalubus[13]), .A7out(oalubus[14]),
    .A8out(oalubus[15]), .A1out(oalubus[8]), .A2out(oalubus[9]), .A3out(oalubus[10]), .A4out(oalubus[11]),
    .A5out(oalubus[12]), .B8out(srcbus[15]), .B6out(srcbus[13]), .B7out(srcbus[14]), .B1out(srcbus[8]),
    .B2out(srcbus[9]), .B3out(srcbus[10]), .B4out(srcbus[11]), .B5out(srcbus[12]));
  T74245 t74245_49 (
    .A6in(omembus[13]), .A7in(omembus[14]), .A8in(omembus[15]), .A1in(omembus[8]), .A2in(omembus[9]),
    .A3in(omembus[10]), .A4in(omembus[11]), .A5in(omembus[12]), .DIR(1'b0), .nOE(n74139_1_pin5),
    .B6in(srcbus[13]), .B7in(srcbus[14]), .B8in(srcbus[15]), .B1in(srcbus[8]), .B2in(srcbus[9]),
    .B3in(srcbus[10]), .B4in(srcbus[11]), .B5in(srcbus[12]), .A6out(omembus[13]), .A7out(omembus[14]),
    .A8out(omembus[15]), .A1out(omembus[8]), .A2out(omembus[9]), .A3out(omembus[10]), .A4out(omembus[11]),
    .A5out(omembus[12]), .B8out(srcbus[15]), .B6out(srcbus[13]), .B7out(srcbus[14]), .B1out(srcbus[8]),
    .B2out(srcbus[9]), .B3out(srcbus[10]), .B4out(srcbus[11]), .B5out(srcbus[12]));
  T74245 t74245_50 (
    .A6in(srctempbus[13]), .A7in(srctempbus[14]), .A8in(srctempbus[15]), .A1in(srctempbus[8]),
    .A2in(srctempbus[9]), .A3in(srctempbus[10]), .A4in(srctempbus[11]), .A5in(srctempbus[12]), .DIR(1'b1),
    .nOE(n74139_1_pin7), .B6in(omembus[13]), .B7in(omembus[14]), .B8in(omembus[15]), .B1in(omembus[8]),
    .B2in(omembus[9]), .B3in(omembus[10]), .B4in(omembus[11]), .B5in(omembus[12]), .A6out(srctempbus[13]),
    .A7out(srctempbus[14]), .A8out(srctempbus[15]), .A1out(srctempbus[8]), .A2out(srctempbus[9]),
    .A3out(srctempbus[10]), .A4out(srctempbus[11]), .A5out(srctempbus[12]), .B8out(omembus[15]),
    .B6out(omembus[13]), .B7out(omembus[14]), .B1out(omembus[8]), .B2out(omembus[9]), .B3out(omembus[10]),
    .B4out(omembus[11]), .B5out(omembus[12]));
  // also tied to GND on the sheet: {n74283_1_pin2, n74283_1_pin15, n74283_2_pin2, n74283_2_pin15, n74377_3_pin3, n74377_4_pin3, n74283_3_pin2, n74283_3_pin15, n74283_4_pin2, n74283_4_pin15, n74283_5_pin2, n74283_5_pin14, n74377_6_pin1, n74377_7_pin3, t74245_17_b1out[0], t74245_39_a6out}
  // also tied to VCC on the sheet: {n74283_1_pin6, n74283_5_pin7, t74245_17_b5out[0], t74245_17_b5out[1], t74245_17_b5out[2], t74245_17_b5out[3], t74245_17_b5out[4], t74245_17_b5out[5], t74245_17_b5out[6], t74245_17_b5out[7], t74245_17_b5out[8], t74245_17_b5out[9], t74245_17_b5out[10], t74245_17_b5out[11], n7486_1_pin5}

  // Other names for the same wires on the sheet: funct[2:0] = oioaddr; regwe = oregwe; memop[2:0] = omemop;
  //   ioop[1:0] = oioop; alubus[15:0] = ialubus; alubuswrite[15:0] = oalubus; aluop[3:0] = oaluop; busy = ibusy;
  //   enter_int = mask_save; fc = ifc; fo = ifo; fs = ifs; fz = ifz; int = iint; intid[2:0] = iintid;
  //   iobus[15:0] = iiobus; iobuswrite[15:0] = oiobus; leave_int = mask_restore; membus[15:0] = imembus;
  //   membuswrite[15:0] = omembus; regbus[15:0] = iregbus; regbuswrite[15:0] = oregbus; regid[3:0] = oregid

  // Notes on the sheet:
  //   MEM
  //   REG
  //   IO
  //   ALU
  //   contents of rom_1 (hex, n*v repeats v):
  //   2802 7202 40004 25074 4208c 4841 10*1 2802 7202 26 5056 8b 11*1 2802 7202 6 5056 8083 11*1 2802 7202
  //   6 5056 8003 11*1 2802 7202 15043 13*1 2802 7202 15043 13*1 2802 7202 200083 13*1 2802 7202 305043
  //   13*1 2802 7202 25002 2c42 5183 11*1 2802 7202 25002 2c42 4003 11*1 2802 7202 40006 25076 4208e 14802
  //   2802 3002 15103 7*1 2802 7202 42006 76 c508b 11*1 2802 7202 40006 25076 4208e 4c43 10*1 2802 7202
  //   42006 76 4008a 5183 10*1 2802 7202 14*1 2802 7202 14*1
  //   CONTROL SIGNALS
  //   the logisim ROM is to be used for simulations
  //   chips are supposed to be used in production due to much more tedious way of updating their  ROM in the simulation view
  //   REGISTERS
  //   BUSES
  //   JUMPS
endmodule

module alu (
  input  [15:0] A,
  input  [15:0] B,
  input  [2:0] funct,
  output FO,
  output FC,
  output FS,
  output [15:0] Y,
  output FZ
);

  wire add_1_cout, add_1_msbcin, multiplexer_1_out, multiplexer_2_out, nor_1_out, sub_1_cout, sub_1_msbcin,
       xor_1_out;
  wire [3:0] add_1_y, add_1_y_2, add_1_y_3, add_1_y_4, and16b_1_y, and16b_1_y_2, and16b_1_y_3, and16b_1_y_4,
       logicshifter_1_y, logicshifter_1_y_2, logicshifter_1_y_3, logicshifter_1_y_4, not16b_1_y,
       not16b_1_y_2, not16b_1_y_3, not16b_1_y_4, or16b_1_y, or16b_1_y_2, or16b_1_y_3, or16b_1_y_4, sub_1_y,
       sub_1_y_2, sub_1_y_3, sub_1_y_4, xor16b_1_y, xor16b_1_y_2, xor16b_1_y_3, xor16b_1_y_4;
  wire [15:0] logicshifter_1_ry, multiplexer_3_out;

  Hex_Digit_Display #(.decimalPoint("false")) hex_digit_display_1 (.value(add_1_y_4));
  Hex_Digit_Display #(.decimalPoint("false")) hex_digit_display_2 (.value(add_1_y_3));
  Hex_Digit_Display #(.decimalPoint("false")) hex_digit_display_3 (.value(add_1_y_2));
  add add_1 (.A(A), .B(B), .Cout(add_1_cout), .MsbCin(add_1_msbcin), .Y({add_1_y_4, add_1_y_3, add_1_y_2, add_1_y}));
  Hex_Digit_Display #(.decimalPoint("false")) hex_digit_display_4 (.value(add_1_y));
  Multiplexer multiplexer_1 (.in0(add_1_cout), .in1(sub_1_msbcin), .out(multiplexer_1_out), .sel(funct[0]));
  xor xor_1 (xor_1_out, multiplexer_1_out, multiplexer_2_out);
  buf buffer_1 (FO, xor_1_out);
  Hex_Digit_Display #(.decimalPoint("false")) hex_digit_display_5 (.value(sub_1_y_4));
  Multiplexer multiplexer_2 (.in0(add_1_msbcin), .in1(sub_1_cout), .out(multiplexer_2_out), .sel(funct[0]));
  buf buffer_2 (FC, multiplexer_2_out);
  Hex_Digit_Display #(.decimalPoint("false")) hex_digit_display_6 (.value(sub_1_y_2));
  Hex_Digit_Display #(.decimalPoint("false")) hex_digit_display_7 (.value(sub_1_y_3));
  sub sub_1 (.A(A), .B(B), .Y({sub_1_y_4, sub_1_y_3, sub_1_y_2, sub_1_y}), .Cout(sub_1_cout), .MsbCin(sub_1_msbcin));
  buf buffer_3 (FS, multiplexer_3_out[15]);
  Hex_Digit_Display #(.decimalPoint("false")) hex_digit_display_8 (.value(sub_1_y));
  Multiplexer #(.select(3), .width(16)) multiplexer_3 (
    .in0({add_1_y_4, add_1_y_3, add_1_y_2, add_1_y}), .in1({sub_1_y_4, sub_1_y_3, sub_1_y_2, sub_1_y}),
    .in2({and16b_1_y_4, and16b_1_y_3, and16b_1_y_2, and16b_1_y}),
    .in3({or16b_1_y_4, or16b_1_y_3, or16b_1_y_2, or16b_1_y}),
    .in4({xor16b_1_y_4, xor16b_1_y_3, xor16b_1_y_2, xor16b_1_y}),
    .in5({not16b_1_y_4, not16b_1_y_3, not16b_1_y_2, not16b_1_y}),
    .in6({logicshifter_1_y_4, logicshifter_1_y_3, logicshifter_1_y_2, logicshifter_1_y}),
    .in7(logicshifter_1_ry), .out(multiplexer_3_out), .sel(funct));
  assign Y = multiplexer_3_out;  // Buffer buffer_4, 16 bits wide
  Hex_Digit_Display #(.decimalPoint("false")) hex_digit_display_9 (.value(and16b_1_y_4));
  Hex_Digit_Display #(.decimalPoint("false")) hex_digit_display_10 (.value(and16b_1_y_3));
  and16b and16b_1 (.B(B), .A(A), .Y({and16b_1_y_4, and16b_1_y_3, and16b_1_y_2, and16b_1_y}));
  Hex_Digit_Display #(.decimalPoint("false")) hex_digit_display_11 (.value(and16b_1_y_2));
  Hex_Digit_Display #(.decimalPoint("false")) hex_digit_display_12 (.value(and16b_1_y));
  nor nor_1 (nor_1_out, multiplexer_3_out[15], multiplexer_3_out[14], multiplexer_3_out[13], multiplexer_3_out[12], multiplexer_3_out[11], multiplexer_3_out[10], multiplexer_3_out[9], multiplexer_3_out[8], multiplexer_3_out[6], multiplexer_3_out[5], multiplexer_3_out[4], multiplexer_3_out[3], multiplexer_3_out[2], multiplexer_3_out[1], multiplexer_3_out[0], multiplexer_3_out[7]);
  buf buffer_5 (FZ, nor_1_out);
  Hex_Digit_Display #(.decimalPoint("false")) hex_digit_display_13 (.value(or16b_1_y_4));
  Hex_Digit_Display #(.decimalPoint("false")) hex_digit_display_14 (.value(or16b_1_y_3));
  Hex_Digit_Display #(.decimalPoint("false")) hex_digit_display_15 (.value(or16b_1_y_2));
  or16b or16b_1 (.B(B), .A(A), .Y({or16b_1_y_4, or16b_1_y_3, or16b_1_y_2, or16b_1_y}));
  Hex_Digit_Display #(.decimalPoint("false")) hex_digit_display_16 (.value(or16b_1_y));
  Hex_Digit_Display #(.decimalPoint("false")) hex_digit_display_17 (.value(xor16b_1_y_4));
  Hex_Digit_Display #(.decimalPoint("false")) hex_digit_display_18 (.value(xor16b_1_y_3));
  xor16b xor16b_1 (.A(A), .B(B), .Y({xor16b_1_y_4, xor16b_1_y_3, xor16b_1_y_2, xor16b_1_y}));
  Hex_Digit_Display #(.decimalPoint("false")) hex_digit_display_19 (.value(xor16b_1_y_2));
  Hex_Digit_Display #(.decimalPoint("false")) hex_digit_display_20 (.value(xor16b_1_y));
  Hex_Digit_Display #(.decimalPoint("false")) hex_digit_display_21 (.value(not16b_1_y_4));
  Hex_Digit_Display #(.decimalPoint("false")) hex_digit_display_22 (.value(not16b_1_y_3));
  not16b not16b_1 (.B(B), .Y({not16b_1_y_4, not16b_1_y_3, not16b_1_y_2, not16b_1_y}));
  Hex_Digit_Display #(.decimalPoint("false")) hex_digit_display_23 (.value(not16b_1_y_2));
  Hex_Digit_Display #(.decimalPoint("false")) hex_digit_display_24 (.value(not16b_1_y));
  Hex_Digit_Display #(.decimalPoint("false")) hex_digit_display_25 (.value(logicshifter_1_y_4));
  Hex_Digit_Display #(.decimalPoint("false")) hex_digit_display_26 (.value(logicshifter_1_y_3));
  Hex_Digit_Display #(.decimalPoint("false")) hex_digit_display_27 (.value(logicshifter_1_y_2));
  logicshifter logicshifter_1 (
    .B(B), .A(A), .Right(funct[0]),
    .Y({logicshifter_1_y_4, logicshifter_1_y_3, logicshifter_1_y_2, logicshifter_1_y}), .rY(logicshifter_1_ry));
  Hex_Digit_Display #(.decimalPoint("false")) hex_digit_display_28 (.value(logicshifter_1_y));
endmodule

module IO (
  input  CLK,
  input  [15:0] iiobus,
  input  [2:0] iioid,
  input  [6:0] ikeychar,
  input  [1:0] iiocmd,
  input  ikeyaval,
  output [7:0] ointasssert,
  output [7:0] obusyassert,
  output [15:0] oiobus,
  output ogpu_clear,
  output okeyread,
  output [15:0] oled
);

  wire isclock, isgpu, iskeyboard, isled, n7408_1_pin3, n7408_1_pin6, n7408_1_pin11, n7408_3_pin3,
       n7408_3_pin11, n7408_4_pin2, n7436_1_pin1, n7436_1_pin4, n7436_1_pin5, n7436_1_pin8, n7436_2_pin3,
       n7436_2_pin8, n7436_2_pin11, n7436_3_pin3, n7436_3_pin5, n7436_3_pin8, n7436_3_pin11, n74377_2_pin1,
       n74377_4_pin1, n74377_4_pin3, re, we;
  wire [11:0] adder_1_out, register_1_q;
  wire [15:0] gpuoutput, keyoutput;

  _7436 u_7436_1 (
    .pin1(n7436_1_pin1), .pin2(n7436_1_pin1), .pin3(okeyread), .pin4(n7436_1_pin4), .pin5(n7436_1_pin5),
    .pin6(n7436_1_pin1), .pin13(ointasssert[6]), .pin12(ointasssert[6]), .pin10(ointasssert[6]),
    .pin9(ointasssert[6]), .pin8(n7436_1_pin8));  // open: pin11
  _74377 u_74377_1 (
    .pin1(n7436_1_pin1), .pin2(keyoutput[0]), .pin3(ikeychar[0]), .pin4(ikeychar[2]), .pin5(keyoutput[2]),
    .pin6(keyoutput[5]), .pin7(ikeychar[5]), .pin8(ikeychar[6]), .pin9(keyoutput[6]), .pin19(keyoutput[1]),
    .pin18(ikeychar[1]), .pin17(ikeychar[3]), .pin16(keyoutput[3]), .pin15(keyoutput[4]),
    .pin14(ikeychar[4]), .pin13(ikeyaval), .pin12(ointasssert[6]), .pin11(CLK));
  _74377 u_74377_2 (
    .pin1(n74377_2_pin1), .pin2(oled[0]), .pin3(iiobus[0]), .pin4(iiobus[2]), .pin5(oled[2]), .pin6(oled[5]),
    .pin7(iiobus[5]), .pin8(iiobus[6]), .pin9(oled[6]), .pin19(oled[1]), .pin18(iiobus[1]),
    .pin17(iiobus[3]), .pin16(oled[3]), .pin15(oled[4]), .pin14(iiobus[4]), .pin13(iiobus[7]),
    .pin12(oled[7]), .pin11(CLK));
  _74377 u_74377_3 (
    .pin1(n74377_2_pin1), .pin2(oled[8]), .pin3(iiobus[8]), .pin4(iiobus[10]), .pin5(oled[10]),
    .pin6(oled[13]), .pin7(iiobus[13]), .pin8(iiobus[14]), .pin9(oled[14]), .pin19(oled[9]),
    .pin18(iiobus[9]), .pin17(iiobus[11]), .pin16(oled[11]), .pin15(oled[12]), .pin14(iiobus[12]),
    .pin13(iiobus[15]), .pin12(oled[15]), .pin11(CLK));
  _7408 u_7408_1 (
    .pin1(re), .pin2(isgpu), .pin3(n7408_1_pin3), .pin4(re), .pin5(iskeyboard), .pin6(n7408_1_pin6),
    .pin13(isled), .pin12(we), .pin11(n7408_1_pin11));  // open: pin10, pin9, pin8
  _7436 u_7436_2 (
    .pin1(iiocmd[0]), .pin2(iiocmd[0]), .pin3(n7436_2_pin3), .pin4(n7408_1_pin11), .pin5(n7408_1_pin11),
    .pin6(n74377_2_pin1), .pin13(n7408_1_pin3), .pin12(n7408_1_pin3), .pin11(n7436_2_pin11),
    .pin10(n7408_1_pin6), .pin9(n7408_1_pin6), .pin8(n7436_2_pin8));
  _7408 u_7408_2 (
    .pin1(iiocmd[1]), .pin2(iiocmd[0]), .pin3(we), .pin4(iiocmd[1]), .pin5(n7436_2_pin3), .pin6(re),
    .pin13(iskeyboard), .pin12(re), .pin11(n7436_1_pin5), .pin10(n7436_1_pin8), .pin9(ikeyaval),
    .pin8(n7436_1_pin4));
  Register #(.width(12)) register_1 (.D(adder_1_out), .en(1'b1), .clk(CLK), .Q(register_1_q), .clr(ointasssert[7]));
  Adder #(.width(12)) adder_1 (.a(register_1_q), .b(12'h1), .out(adder_1_out));  // open: cin, cout
  _74377 u_74377_4 (
    .pin1(n74377_4_pin1), .pin3(n74377_4_pin3), .pin4(n74377_4_pin3), .pin7(n74377_4_pin3),
    .pin8(n74377_4_pin3), .pin19(ointasssert[7]), .pin18(register_1_q[11]), .pin17(n74377_4_pin3),
    .pin14(n74377_4_pin3), .pin13(n74377_4_pin3), .pin11(CLK));  // open: pin2, pin5, pin6, pin9, pin16, pin15, pin12
  T74245 t74245_1 (
    .A6in(oiobus[5]), .A7in(oiobus[6]), .A8in(oiobus[7]), .A1in(oiobus[0]), .A2in(oiobus[1]),
    .A3in(oiobus[2]), .A4in(oiobus[3]), .A5in(oiobus[4]), .nOE(n7436_2_pin11), .B6in(gpuoutput[5]),
    .B7in(gpuoutput[6]), .B8in(gpuoutput[7]), .B1in(gpuoutput[0]), .B2in(gpuoutput[1]), .B3in(gpuoutput[2]),
    .B4in(gpuoutput[3]), .B5in(gpuoutput[4]), .A6out(oiobus[5]), .A7out(oiobus[6]), .A8out(oiobus[7]),
    .A1out(oiobus[0]), .A2out(oiobus[1]), .A3out(oiobus[2]), .A4out(oiobus[3]), .A5out(oiobus[4]),
    .B8out(gpuoutput[7]), .B6out(gpuoutput[5]), .B7out(gpuoutput[6]), .B1out(gpuoutput[0]),
    .B2out(gpuoutput[1]), .B3out(gpuoutput[2]), .B4out(gpuoutput[3]), .B5out(gpuoutput[4]));  // open: DIR
  T74245 t74245_2 (
    .A6in(keyoutput[5]), .A7in(keyoutput[6]), .A8in(keyoutput[7]), .A1in(keyoutput[0]), .A2in(keyoutput[1]),
    .A3in(keyoutput[2]), .A4in(keyoutput[3]), .A5in(keyoutput[4]), .DIR(1'b1), .nOE(n7436_2_pin8),
    .B6in(oiobus[5]), .B7in(oiobus[6]), .B8in(oiobus[7]), .B1in(oiobus[0]), .B2in(oiobus[1]),
    .B3in(oiobus[2]), .B4in(oiobus[3]), .B5in(oiobus[4]), .A6out(keyoutput[5]), .A7out(keyoutput[6]),
    .A8out(keyoutput[7]), .A1out(keyoutput[0]), .A2out(keyoutput[1]), .A3out(keyoutput[2]),
    .A4out(keyoutput[3]), .A5out(keyoutput[4]), .B8out(oiobus[7]), .B6out(oiobus[5]), .B7out(oiobus[6]),
    .B1out(oiobus[0]), .B2out(oiobus[1]), .B3out(oiobus[2]), .B4out(oiobus[3]), .B5out(oiobus[4]));
  _7436 u_7436_3 (
    .pin1(iioid[2]), .pin2(iioid[2]), .pin3(n7436_3_pin3), .pin4(register_1_q[11]), .pin5(n7436_3_pin5),
    .pin6(n74377_4_pin1), .pin13(iioid[0]), .pin12(iioid[0]), .pin11(n7436_3_pin11), .pin10(iioid[1]),
    .pin9(iioid[1]), .pin8(n7436_3_pin8));
  _7408 u_7408_3 (
    .pin1(iioid[2]), .pin2(iioid[1]), .pin3(n7408_3_pin3), .pin4(n7408_3_pin3), .pin5(iioid[0]),
    .pin6(isled), .pin13(n7436_3_pin3), .pin12(n7436_3_pin11), .pin11(n7408_3_pin11), .pin10(n7408_3_pin11),
    .pin9(iioid[1]), .pin8(isgpu));
  T74245 t74245_3 (
    .A6in(oiobus[13]), .A7in(oiobus[14]), .A8in(oiobus[15]), .A1in(oiobus[8]), .A2in(oiobus[9]),
    .A3in(oiobus[10]), .A4in(oiobus[11]), .A5in(oiobus[12]), .DIR(1'b0), .nOE(n7436_2_pin11),
    .B6in(gpuoutput[13]), .B7in(gpuoutput[14]), .B8in(gpuoutput[15]), .B1in(gpuoutput[8]),
    .B2in(gpuoutput[9]), .B3in(gpuoutput[10]), .B4in(gpuoutput[11]), .B5in(gpuoutput[12]),
    .A6out(oiobus[13]), .A7out(oiobus[14]), .A8out(oiobus[15]), .A1out(oiobus[8]), .A2out(oiobus[9]),
    .A3out(oiobus[10]), .A4out(oiobus[11]), .A5out(oiobus[12]), .B8out(gpuoutput[15]), .B6out(gpuoutput[13]),
    .B7out(gpuoutput[14]), .B1out(gpuoutput[8]), .B2out(gpuoutput[9]), .B3out(gpuoutput[10]),
    .B4out(gpuoutput[11]), .B5out(gpuoutput[12]));
  T74245 t74245_4 (
    .A6in(keyoutput[13]), .A7in(keyoutput[14]), .A8in(keyoutput[15]), .A1in(keyoutput[8]),
    .A2in(keyoutput[9]), .A3in(keyoutput[10]), .A4in(keyoutput[11]), .A5in(keyoutput[12]), .DIR(1'b1),
    .nOE(n7436_2_pin8), .B6in(oiobus[13]), .B7in(oiobus[14]), .B8in(oiobus[15]), .B1in(oiobus[8]),
    .B2in(oiobus[9]), .B3in(oiobus[10]), .B4in(oiobus[11]), .B5in(oiobus[12]), .A6out(keyoutput[13]),
    .A7out(keyoutput[14]), .A8out(keyoutput[15]), .A1out(keyoutput[8]), .A2out(keyoutput[9]),
    .A3out(keyoutput[10]), .A4out(keyoutput[11]), .A5out(keyoutput[12]), .B8out(oiobus[15]),
    .B6out(oiobus[13]), .B7out(oiobus[14]), .B1out(oiobus[8]), .B2out(oiobus[9]), .B3out(oiobus[10]),
    .B4out(oiobus[11]), .B5out(oiobus[12]));
  _7408 u_7408_4 (
    .pin1(n7436_3_pin3), .pin2(n7408_4_pin2), .pin3(iskeyboard), .pin4(n7408_3_pin11), .pin5(n7436_3_pin3),
    .pin6(isclock), .pin13(iioid[0]), .pin12(n7436_3_pin8), .pin11(n7408_4_pin2), .pin10(re), .pin9(isclock),
    .pin8(n7436_3_pin5));

  assign obusyassert = {8{1'b0}};
  assign ogpu_clear = 1'b0;
  assign ointasssert[5:0] = {6{1'b0}};
  // also tied to GND on the sheet: {n74377_4_pin3, gpuoutput[1], gpuoutput[2], gpuoutput[3], gpuoutput[4], gpuoutput[5], gpuoutput[6], gpuoutput[7], gpuoutput[8], gpuoutput[9], gpuoutput[10], gpuoutput[11], gpuoutput[12], gpuoutput[13], gpuoutput[14], gpuoutput[15], keyoutput[7], keyoutput[8], keyoutput[9], keyoutput[10], keyoutput[11], keyoutput[12], keyoutput[13], keyoutput[14], keyoutput[15]}
  // also tied to VCC on the sheet: gpuoutput[0]

  // Other names for the same wires on the sheet: keychar[6:0] = ikeychar; keyaval = ikeyaval; iobus[15:0] = iiobus;
  //   ioid[2:0] = iioid; keyread = okeyread; key_present = ointasssert[6]; clockint = ointasssert[7]

  // Notes on the sheet:
  //   CPU interface
  //   GPU interface
  //   keyboard interface
  //   led interface
  //   IO interface
  //   clock
  //   this part will be replaced by external async circuit
endmodule
module add (
  input  [15:0] B,
  input  [15:0] A,
  output [15:0] Y,
  output Cout,
  output MsbCin
);

  wire n74283_1_pin9, n74283_2_pin9, n74283_3_pin9;

  fulladd4b fulladd4b_1 (
    .B0(B[12]), .B1(B[13]), .B2(B[14]), .B3(B[15]), .A0(A[12]), .A1(A[13]), .A2(A[14]), .A3(A[15]),
    .Cin(n74283_3_pin9), .MsbCin(MsbCin), .Cout(Cout), .Y0(Y[12]), .Y1(Y[13]), .Y2(Y[14]), .Y3(Y[15]));
  _74283 u_74283_1 (
    .pin1(Y[1]), .pin2(B[1]), .pin3(A[1]), .pin4(Y[0]), .pin5(A[0]), .pin6(B[0]), .pin15(B[2]), .pin14(A[2]),
    .pin13(Y[2]), .pin12(A[3]), .pin11(B[3]), .pin10(Y[3]), .pin9(n74283_1_pin9));  // open: pin7
  _74283 u_74283_2 (
    .pin1(Y[5]), .pin2(B[5]), .pin3(A[5]), .pin4(Y[4]), .pin5(A[4]), .pin6(B[4]), .pin7(n74283_1_pin9),
    .pin15(B[6]), .pin14(A[6]), .pin13(Y[6]), .pin12(A[7]), .pin11(B[7]), .pin10(Y[7]), .pin9(n74283_2_pin9));
  _74283 u_74283_3 (
    .pin1(Y[9]), .pin2(B[9]), .pin3(A[9]), .pin4(Y[8]), .pin5(A[8]), .pin6(B[8]), .pin7(n74283_2_pin9),
    .pin15(B[10]), .pin14(A[10]), .pin13(Y[10]), .pin12(A[11]), .pin11(B[11]), .pin10(Y[11]),
    .pin9(n74283_3_pin9));
endmodule

module sub (
  input  [15:0] A,
  input  [15:0] B,
  output Cout,
  output MsbCin,
  output [15:0] Y
);

  wire n74283_1_pin7, n74283_1_pin9, n74283_2_pin9, n74283_3_pin9;
  wire [15:0] n7404_1_pin2;

  _7404 u_7404_1 (
    .pin1(B[0]), .pin2(n7404_1_pin2[0]), .pin3(B[1]), .pin4(n7404_1_pin2[1]), .pin5(B[2]),
    .pin6(n7404_1_pin2[2]), .pin13(B[8]), .pin12(n7404_1_pin2[8]), .pin11(B[9]), .pin10(n7404_1_pin2[9]),
    .pin9(B[10]), .pin8(n7404_1_pin2[10]));
  _7404 u_7404_2 (
    .pin1(B[3]), .pin2(n7404_1_pin2[3]), .pin3(B[4]), .pin4(n7404_1_pin2[4]), .pin5(B[5]),
    .pin6(n7404_1_pin2[5]), .pin13(B[11]), .pin12(n7404_1_pin2[11]), .pin11(B[12]), .pin10(n7404_1_pin2[12]),
    .pin9(B[13]), .pin8(n7404_1_pin2[13]));
  _7404 u_7404_3 (
    .pin1(B[6]), .pin2(n7404_1_pin2[6]), .pin3(B[7]), .pin4(n7404_1_pin2[7]), .pin13(B[14]),
    .pin12(n7404_1_pin2[14]), .pin11(B[15]), .pin10(n7404_1_pin2[15]));  // open: pin5, pin6, pin9, pin8
  fulladd4b fulladd4b_1 (
    .B0(A[12]), .B1(A[13]), .B2(A[14]), .B3(A[15]), .A0(n7404_1_pin2[12]), .A1(n7404_1_pin2[13]),
    .A2(n7404_1_pin2[14]), .A3(n7404_1_pin2[15]), .Cin(n74283_3_pin9), .MsbCin(MsbCin), .Cout(Cout),
    .Y0(Y[12]), .Y1(Y[13]), .Y2(Y[14]), .Y3(Y[15]));
  _74283 u_74283_1 (
    .pin1(Y[1]), .pin2(n7404_1_pin2[1]), .pin3(A[1]), .pin4(Y[0]), .pin5(A[0]), .pin6(n7404_1_pin2[0]),
    .pin7(n74283_1_pin7), .pin15(n7404_1_pin2[2]), .pin14(A[2]), .pin13(Y[2]), .pin12(A[3]),
    .pin11(n7404_1_pin2[3]), .pin10(Y[3]), .pin9(n74283_1_pin9));
  _74283 u_74283_2 (
    .pin1(Y[5]), .pin2(n7404_1_pin2[5]), .pin3(A[5]), .pin4(Y[4]), .pin5(A[4]), .pin6(n7404_1_pin2[4]),
    .pin7(n74283_1_pin9), .pin15(n7404_1_pin2[6]), .pin14(A[6]), .pin13(Y[6]), .pin12(A[7]),
    .pin11(n7404_1_pin2[7]), .pin10(Y[7]), .pin9(n74283_2_pin9));
  _74283 u_74283_3 (
    .pin1(Y[9]), .pin2(n7404_1_pin2[9]), .pin3(A[9]), .pin4(Y[8]), .pin5(A[8]), .pin6(n7404_1_pin2[8]),
    .pin7(n74283_2_pin9), .pin15(n7404_1_pin2[10]), .pin14(A[10]), .pin13(Y[10]), .pin12(A[11]),
    .pin11(n7404_1_pin2[11]), .pin10(Y[11]), .pin9(n74283_3_pin9));
  // also tied to VCC on the sheet: n74283_1_pin7
endmodule

module fulladd4b (
  input  Cin,
  input  A0,
  input  B0,
  input  A1,
  input  B1,
  input  A2,
  input  B2,
  input  A3,
  input  B3,
  output Y0,
  output Y1,
  output Y2,
  output MsbCin,
  output Cout,
  output Y3
);

  wire n7408_1_pin3, n7408_1_pin6, n7408_1_pin8, n7408_1_pin11, n7408_2_pin3, n7408_2_pin6, n7408_2_pin8,
       n7408_2_pin11, n7486_1_pin3, n7486_1_pin5, n7486_1_pin11, n7486_2_pin3, n7486_2_pin9, n7486_2_pin11;

  _7486 u_7486_1 (
    .pin1(A1), .pin2(B1), .pin3(n7486_1_pin3), .pin4(n7486_1_pin3), .pin5(n7486_1_pin5), .pin6(Y1),
    .pin13(B0), .pin12(A0), .pin11(n7486_1_pin11), .pin10(n7486_1_pin11), .pin9(Cin), .pin8(Y0));
  _7486 u_7486_2 (
    .pin1(A3), .pin2(B3), .pin3(n7486_2_pin3), .pin4(n7486_2_pin3), .pin5(MsbCin), .pin6(Y3), .pin13(B2),
    .pin12(A2), .pin11(n7486_2_pin11), .pin10(n7486_2_pin11), .pin9(n7486_2_pin9), .pin8(Y2));
  _7408 u_7408_1 (
    .pin1(B1), .pin2(A1), .pin3(n7408_1_pin3), .pin4(n7486_1_pin3), .pin5(n7486_1_pin5), .pin6(n7408_1_pin6),
    .pin13(A0), .pin12(B0), .pin11(n7408_1_pin11), .pin10(n7486_1_pin11), .pin9(Cin), .pin8(n7408_1_pin8));
  _7408 u_7408_2 (
    .pin1(B3), .pin2(A3), .pin3(n7408_2_pin3), .pin4(n7486_2_pin3), .pin5(MsbCin), .pin6(n7408_2_pin6),
    .pin13(A2), .pin12(B2), .pin11(n7408_2_pin11), .pin10(n7486_2_pin11), .pin9(n7486_2_pin9),
    .pin8(n7408_2_pin8));
  _7432 u_7432_1 (
    .pin1(n7408_2_pin11), .pin2(n7408_2_pin8), .pin3(MsbCin), .pin4(n7408_2_pin6), .pin5(n7408_2_pin3),
    .pin6(Cout), .pin13(n7408_1_pin8), .pin12(n7408_1_pin11), .pin11(n7486_1_pin5), .pin10(n7408_1_pin6),
    .pin9(n7408_1_pin3), .pin8(n7486_2_pin9));
endmodule

module and16b (
  input  [15:0] A,
  input  [15:0] B,
  output [15:0] Y
);

  _7408 u_7408_1 (
    .pin1(A[2]), .pin2(B[2]), .pin3(Y[2]), .pin4(A[3]), .pin5(B[3]), .pin6(Y[3]), .pin13(A[1]), .pin12(B[1]),
    .pin11(Y[1]), .pin10(A[0]), .pin9(B[0]), .pin8(Y[0]));
  _7408 u_7408_2 (
    .pin1(A[6]), .pin2(B[6]), .pin3(Y[6]), .pin4(A[7]), .pin5(B[7]), .pin6(Y[7]), .pin13(A[5]), .pin12(B[5]),
    .pin11(Y[5]), .pin10(A[4]), .pin9(B[4]), .pin8(Y[4]));
  _7408 u_7408_3 (
    .pin1(A[10]), .pin2(B[10]), .pin3(Y[10]), .pin4(A[11]), .pin5(B[11]), .pin6(Y[11]), .pin13(A[9]),
    .pin12(B[9]), .pin11(Y[9]), .pin10(A[8]), .pin9(B[8]), .pin8(Y[8]));
  _7408 u_7408_4 (
    .pin1(A[14]), .pin2(B[14]), .pin3(Y[14]), .pin4(A[15]), .pin5(B[15]), .pin6(Y[15]), .pin13(A[13]),
    .pin12(B[13]), .pin11(Y[13]), .pin10(A[12]), .pin9(B[12]), .pin8(Y[12]));
endmodule

module or16b (
  input  [15:0] A,
  input  [15:0] B,
  output [15:0] Y
);

  _7432 u_7432_1 (
    .pin1(A[2]), .pin2(B[2]), .pin3(Y[2]), .pin4(A[3]), .pin5(B[3]), .pin6(Y[3]), .pin13(A[1]), .pin12(B[1]),
    .pin11(Y[1]), .pin10(A[0]), .pin9(B[0]), .pin8(Y[0]));
  _7432 u_7432_2 (
    .pin1(A[6]), .pin2(B[6]), .pin3(Y[6]), .pin4(A[7]), .pin5(B[7]), .pin6(Y[7]), .pin13(A[5]), .pin12(B[5]),
    .pin11(Y[5]), .pin10(A[4]), .pin9(B[4]), .pin8(Y[4]));
  _7432 u_7432_3 (
    .pin1(A[10]), .pin2(B[10]), .pin3(Y[10]), .pin4(A[11]), .pin5(B[11]), .pin6(Y[11]), .pin13(A[9]),
    .pin12(B[9]), .pin11(Y[9]), .pin10(A[8]), .pin9(B[8]), .pin8(Y[8]));
  _7432 u_7432_4 (
    .pin1(A[14]), .pin2(B[14]), .pin3(Y[14]), .pin4(A[15]), .pin5(B[15]), .pin6(Y[15]), .pin13(A[13]),
    .pin12(B[13]), .pin11(Y[13]), .pin10(A[12]), .pin9(B[12]), .pin8(Y[12]));
endmodule

module xor16b (
  input  [15:0] A,
  input  [15:0] B,
  output [15:0] Y
);

  _7486 u_7486_1 (
    .pin1(A[2]), .pin2(B[2]), .pin3(Y[2]), .pin4(A[3]), .pin5(B[3]), .pin6(Y[3]), .pin13(A[1]), .pin12(B[1]),
    .pin11(Y[1]), .pin10(A[0]), .pin9(B[0]), .pin8(Y[0]));
  _7486 u_7486_2 (
    .pin1(A[6]), .pin2(B[6]), .pin3(Y[6]), .pin4(A[7]), .pin5(B[7]), .pin6(Y[7]), .pin13(A[5]), .pin12(B[5]),
    .pin11(Y[5]), .pin10(A[4]), .pin9(B[4]), .pin8(Y[4]));
  _7486 u_7486_3 (
    .pin1(A[10]), .pin2(B[10]), .pin3(Y[10]), .pin4(A[11]), .pin5(B[11]), .pin6(Y[11]), .pin13(A[9]),
    .pin12(B[9]), .pin11(Y[9]), .pin10(A[8]), .pin9(B[8]), .pin8(Y[8]));
  _7486 u_7486_4 (
    .pin1(A[14]), .pin2(B[14]), .pin3(Y[14]), .pin4(A[15]), .pin5(B[15]), .pin6(Y[15]), .pin13(A[13]),
    .pin12(B[13]), .pin11(Y[13]), .pin10(A[12]), .pin9(B[12]), .pin8(Y[12]));
endmodule

module not16b (
  input  [15:0] B,
  output [15:0] Y
);

  _7414 u_7414_1 (
    .pin1(B[3]), .pin2(Y[3]), .pin3(B[4]), .pin4(Y[4]), .pin5(B[5]), .pin6(Y[5]), .pin13(B[2]), .pin12(Y[2]),
    .pin11(B[1]), .pin10(Y[1]), .pin9(B[0]), .pin8(Y[0]));
  _7414 u_7414_2 (
    .pin1(B[9]), .pin2(Y[9]), .pin3(B[10]), .pin4(Y[10]), .pin5(B[11]), .pin6(Y[11]), .pin13(B[8]),
    .pin12(Y[8]), .pin11(B[7]), .pin10(Y[7]), .pin9(B[6]), .pin8(Y[6]));
  _7414 u_7414_3 (
    .pin1(B[15]), .pin2(Y[15]), .pin13(B[14]), .pin12(Y[14]), .pin11(B[13]), .pin10(Y[13]), .pin9(B[12]),
    .pin8(Y[12]));  // open: pin3, pin4, pin5, pin6
endmodule

module lsl (
  input  [15:0] B,
  input  [15:0] A,
  output [15:0] Y
);

  wire pull_resistor_1_node;

  Multiplexer #(.select(4)) multiplexer_1 (
    .in0(A[15]), .in1(A[14]), .in2(A[13]), .in3(A[12]), .in4(A[11]), .in5(A[10]), .in6(A[9]), .in7(A[8]),
    .in8(A[7]), .in9(A[6]), .in10(A[5]), .in11(A[4]), .in12(A[3]), .in13(A[2]), .in14(A[1]), .in15(A[0]),
    .out(Y[15]), .sel(B[3:0]));
  Multiplexer #(.select(4)) multiplexer_2 (
    .in0(A[14]), .in1(A[13]), .in2(A[12]), .in3(A[11]), .in4(A[10]), .in5(A[9]), .in6(A[8]), .in7(A[7]),
    .in8(A[6]), .in9(A[5]), .in10(A[4]), .in11(A[3]), .in12(A[2]), .in13(A[1]), .in14(A[0]),
    .in15(pull_resistor_1_node), .out(Y[14]), .sel(B[3:0]));
  Multiplexer #(.select(4)) multiplexer_3 (
    .in0(A[13]), .in1(A[12]), .in2(A[11]), .in3(A[10]), .in4(A[9]), .in5(A[8]), .in6(A[7]), .in7(A[6]),
    .in8(A[5]), .in9(A[4]), .in10(A[3]), .in11(A[2]), .in12(A[1]), .in13(A[0]), .in14(pull_resistor_1_node),
    .in15(pull_resistor_1_node), .out(Y[13]), .sel(B[3:0]));
  Multiplexer #(.select(4)) multiplexer_4 (
    .in0(A[12]), .in1(A[11]), .in2(A[10]), .in3(A[9]), .in4(A[8]), .in5(A[7]), .in6(A[6]), .in7(A[5]),
    .in8(A[4]), .in9(A[3]), .in10(A[2]), .in11(A[1]), .in12(A[0]), .in13(pull_resistor_1_node),
    .in14(pull_resistor_1_node), .in15(pull_resistor_1_node), .out(Y[12]), .sel(B[3:0]));
  Multiplexer #(.select(4)) multiplexer_5 (
    .in0(A[11]), .in1(A[10]), .in2(A[9]), .in3(A[8]), .in4(A[7]), .in5(A[6]), .in6(A[5]), .in7(A[4]),
    .in8(A[3]), .in9(A[2]), .in10(A[1]), .in11(A[0]), .in12(pull_resistor_1_node),
    .in13(pull_resistor_1_node), .in14(pull_resistor_1_node), .in15(pull_resistor_1_node), .out(Y[11]),
    .sel(B[3:0]));
  Multiplexer #(.select(4)) multiplexer_6 (
    .in0(A[10]), .in1(A[9]), .in2(A[8]), .in3(A[7]), .in4(A[6]), .in5(A[5]), .in6(A[4]), .in7(A[3]),
    .in8(A[2]), .in9(A[1]), .in10(A[0]), .in11(pull_resistor_1_node), .in12(pull_resistor_1_node),
    .in13(pull_resistor_1_node), .in14(pull_resistor_1_node), .in15(pull_resistor_1_node), .out(Y[10]),
    .sel(B[3:0]));
  Multiplexer #(.select(4)) multiplexer_7 (
    .in0(A[9]), .in1(A[8]), .in2(A[7]), .in3(A[6]), .in4(A[5]), .in5(A[4]), .in6(A[3]), .in7(A[2]),
    .in8(A[1]), .in9(A[0]), .in10(pull_resistor_1_node), .in11(pull_resistor_1_node),
    .in12(pull_resistor_1_node), .in13(pull_resistor_1_node), .in14(pull_resistor_1_node),
    .in15(pull_resistor_1_node), .out(Y[9]), .sel(B[3:0]));
  Multiplexer #(.select(4)) multiplexer_8 (
    .in0(A[8]), .in1(A[7]), .in2(A[6]), .in3(A[5]), .in4(A[4]), .in5(A[3]), .in6(A[2]), .in7(A[1]),
    .in8(A[0]), .in9(pull_resistor_1_node), .in10(pull_resistor_1_node), .in11(pull_resistor_1_node),
    .in12(pull_resistor_1_node), .in13(pull_resistor_1_node), .in14(pull_resistor_1_node),
    .in15(pull_resistor_1_node), .out(Y[8]), .sel(B[3:0]));
  Multiplexer #(.select(4)) multiplexer_9 (
    .in0(A[7]), .in1(A[6]), .in2(A[5]), .in3(A[4]), .in4(A[3]), .in5(A[2]), .in6(A[1]), .in7(A[0]),
    .in8(pull_resistor_1_node), .in9(pull_resistor_1_node), .in10(pull_resistor_1_node),
    .in11(pull_resistor_1_node), .in12(pull_resistor_1_node), .in13(pull_resistor_1_node),
    .in14(pull_resistor_1_node), .in15(pull_resistor_1_node), .out(Y[7]), .sel(B[3:0]));
  Multiplexer #(.select(4)) multiplexer_10 (
    .in0(A[6]), .in1(A[5]), .in2(A[4]), .in3(A[3]), .in4(A[2]), .in5(A[1]), .in6(A[0]),
    .in7(pull_resistor_1_node), .in8(pull_resistor_1_node), .in9(pull_resistor_1_node),
    .in10(pull_resistor_1_node), .in11(pull_resistor_1_node), .in12(pull_resistor_1_node),
    .in13(pull_resistor_1_node), .in14(pull_resistor_1_node), .in15(pull_resistor_1_node), .out(Y[6]),
    .sel(B[3:0]));
  Multiplexer #(.select(4)) multiplexer_11 (
    .in0(A[5]), .in1(A[4]), .in2(A[3]), .in3(A[2]), .in4(A[1]), .in5(A[0]), .in6(pull_resistor_1_node),
    .in7(pull_resistor_1_node), .in8(pull_resistor_1_node), .in9(pull_resistor_1_node),
    .in10(pull_resistor_1_node), .in11(pull_resistor_1_node), .in12(pull_resistor_1_node),
    .in13(pull_resistor_1_node), .in14(pull_resistor_1_node), .in15(pull_resistor_1_node), .out(Y[5]),
    .sel(B[3:0]));
  Multiplexer #(.select(4)) multiplexer_12 (
    .in0(A[4]), .in1(A[3]), .in2(A[2]), .in3(A[1]), .in4(A[0]), .in5(pull_resistor_1_node),
    .in6(pull_resistor_1_node), .in7(pull_resistor_1_node), .in8(pull_resistor_1_node),
    .in9(pull_resistor_1_node), .in10(pull_resistor_1_node), .in11(pull_resistor_1_node),
    .in12(pull_resistor_1_node), .in13(pull_resistor_1_node), .in14(pull_resistor_1_node),
    .in15(pull_resistor_1_node), .out(Y[4]), .sel(B[3:0]));
  Multiplexer #(.select(4)) multiplexer_13 (
    .in0(A[3]), .in1(A[2]), .in2(A[1]), .in3(A[0]), .in4(pull_resistor_1_node), .in5(pull_resistor_1_node),
    .in6(pull_resistor_1_node), .in7(pull_resistor_1_node), .in8(pull_resistor_1_node),
    .in9(pull_resistor_1_node), .in10(pull_resistor_1_node), .in11(pull_resistor_1_node),
    .in12(pull_resistor_1_node), .in13(pull_resistor_1_node), .in14(pull_resistor_1_node),
    .in15(pull_resistor_1_node), .out(Y[3]), .sel(B[3:0]));
  Multiplexer #(.select(4)) multiplexer_14 (
    .in0(A[2]), .in1(A[1]), .in2(A[0]), .in3(pull_resistor_1_node), .in4(pull_resistor_1_node),
    .in5(pull_resistor_1_node), .in6(pull_resistor_1_node), .in7(pull_resistor_1_node),
    .in8(pull_resistor_1_node), .in9(pull_resistor_1_node), .in10(pull_resistor_1_node),
    .in11(pull_resistor_1_node), .in12(pull_resistor_1_node), .in13(pull_resistor_1_node),
    .in14(pull_resistor_1_node), .in15(pull_resistor_1_node), .out(Y[2]), .sel(B[3:0]));
  Multiplexer #(.select(4)) multiplexer_15 (
    .in0(A[1]), .in1(A[0]), .in2(pull_resistor_1_node), .in3(pull_resistor_1_node),
    .in4(pull_resistor_1_node), .in5(pull_resistor_1_node), .in6(pull_resistor_1_node),
    .in7(pull_resistor_1_node), .in8(pull_resistor_1_node), .in9(pull_resistor_1_node),
    .in10(pull_resistor_1_node), .in11(pull_resistor_1_node), .in12(pull_resistor_1_node),
    .in13(pull_resistor_1_node), .in14(pull_resistor_1_node), .in15(pull_resistor_1_node), .out(Y[1]),
    .sel(B[3:0]));
  Multiplexer #(.select(4)) multiplexer_16 (
    .in0(A[0]), .in1(pull_resistor_1_node), .in2(pull_resistor_1_node), .in3(pull_resistor_1_node),
    .in4(pull_resistor_1_node), .in5(pull_resistor_1_node), .in6(pull_resistor_1_node),
    .in7(pull_resistor_1_node), .in8(pull_resistor_1_node), .in9(pull_resistor_1_node),
    .in10(pull_resistor_1_node), .in11(pull_resistor_1_node), .in12(pull_resistor_1_node),
    .in13(pull_resistor_1_node), .in14(pull_resistor_1_node), .in15(pull_resistor_1_node), .out(Y[0]),
    .sel(B[3:0]));
  Pull_Resistor pull_resistor_1 (.node(pull_resistor_1_node));
endmodule

module logicshifter (
  input  [15:0] B,
  input  Right,
  input  [15:0] A,
  output [15:0] rY,
  output [15:0] Y
);

  wire pull_resistor_1_node;
  wire [15:0] multiplexer_1_out;

  Multiplexer multiplexer_1 (.in0(A[0]), .in1(A[15]), .out(multiplexer_1_out[0]), .sel(Right));
  Multiplexer multiplexer_2 (.in0(A[1]), .in1(A[14]), .out(multiplexer_1_out[1]), .sel(Right));
  Multiplexer multiplexer_3 (.in0(A[2]), .in1(A[13]), .out(multiplexer_1_out[2]), .sel(Right));
  Multiplexer multiplexer_4 (.in0(A[3]), .in1(A[12]), .out(multiplexer_1_out[3]), .sel(Right));
  Multiplexer multiplexer_5 (.in0(A[4]), .in1(A[11]), .out(multiplexer_1_out[4]), .sel(Right));
  Multiplexer multiplexer_6 (.in0(A[5]), .in1(A[10]), .out(multiplexer_1_out[5]), .sel(Right));
  Multiplexer multiplexer_7 (.in0(A[6]), .in1(A[9]), .out(multiplexer_1_out[6]), .sel(Right));
  Multiplexer multiplexer_8 (.in0(A[7]), .in1(A[8]), .out(multiplexer_1_out[7]), .sel(Right));
  Multiplexer multiplexer_9 (.in0(A[8]), .in1(A[7]), .out(multiplexer_1_out[8]), .sel(Right));
  Multiplexer multiplexer_10 (.in0(A[9]), .in1(A[6]), .out(multiplexer_1_out[9]), .sel(Right));
  Multiplexer multiplexer_11 (.in0(A[10]), .in1(A[5]), .out(multiplexer_1_out[10]), .sel(Right));
  Multiplexer multiplexer_12 (.in0(A[11]), .in1(A[4]), .out(multiplexer_1_out[11]), .sel(Right));
  Multiplexer multiplexer_13 (.in0(A[12]), .in1(A[3]), .out(multiplexer_1_out[12]), .sel(Right));
  Multiplexer multiplexer_14 (.in0(A[13]), .in1(A[2]), .out(multiplexer_1_out[13]), .sel(Right));
  Multiplexer multiplexer_15 (.in0(A[14]), .in1(A[1]), .out(multiplexer_1_out[14]), .sel(Right));
  Multiplexer multiplexer_16 (.in0(A[15]), .in1(A[0]), .out(multiplexer_1_out[15]), .sel(Right));
  Multiplexer #(.select(4)) multiplexer_17 (
    .in0(multiplexer_1_out[15]), .in1(multiplexer_1_out[14]), .in2(multiplexer_1_out[13]),
    .in3(multiplexer_1_out[12]), .in4(multiplexer_1_out[11]), .in5(multiplexer_1_out[10]),
    .in6(multiplexer_1_out[9]), .in7(multiplexer_1_out[8]), .in8(multiplexer_1_out[7]),
    .in9(multiplexer_1_out[6]), .in10(multiplexer_1_out[5]), .in11(multiplexer_1_out[4]),
    .in12(multiplexer_1_out[3]), .in13(multiplexer_1_out[2]), .in14(multiplexer_1_out[1]),
    .in15(multiplexer_1_out[0]), .out(rY[0]), .sel(B[3:0]));
  Multiplexer #(.select(4)) multiplexer_18 (
    .in0(multiplexer_1_out[14]), .in1(multiplexer_1_out[13]), .in2(multiplexer_1_out[12]),
    .in3(multiplexer_1_out[11]), .in4(multiplexer_1_out[10]), .in5(multiplexer_1_out[9]),
    .in6(multiplexer_1_out[8]), .in7(multiplexer_1_out[7]), .in8(multiplexer_1_out[6]),
    .in9(multiplexer_1_out[5]), .in10(multiplexer_1_out[4]), .in11(multiplexer_1_out[3]),
    .in12(multiplexer_1_out[2]), .in13(multiplexer_1_out[1]), .in14(multiplexer_1_out[0]),
    .in15(pull_resistor_1_node), .out(rY[1]), .sel(B[3:0]));
  Multiplexer #(.select(4)) multiplexer_19 (
    .in0(multiplexer_1_out[13]), .in1(multiplexer_1_out[12]), .in2(multiplexer_1_out[11]),
    .in3(multiplexer_1_out[10]), .in4(multiplexer_1_out[9]), .in5(multiplexer_1_out[8]),
    .in6(multiplexer_1_out[7]), .in7(multiplexer_1_out[6]), .in8(multiplexer_1_out[5]),
    .in9(multiplexer_1_out[4]), .in10(multiplexer_1_out[3]), .in11(multiplexer_1_out[2]),
    .in12(multiplexer_1_out[1]), .in13(multiplexer_1_out[0]), .in14(pull_resistor_1_node),
    .in15(pull_resistor_1_node), .out(rY[2]), .sel(B[3:0]));
  Multiplexer #(.select(4)) multiplexer_20 (
    .in0(multiplexer_1_out[12]), .in1(multiplexer_1_out[11]), .in2(multiplexer_1_out[10]),
    .in3(multiplexer_1_out[9]), .in4(multiplexer_1_out[8]), .in5(multiplexer_1_out[7]),
    .in6(multiplexer_1_out[6]), .in7(multiplexer_1_out[5]), .in8(multiplexer_1_out[4]),
    .in9(multiplexer_1_out[3]), .in10(multiplexer_1_out[2]), .in11(multiplexer_1_out[1]),
    .in12(multiplexer_1_out[0]), .in13(pull_resistor_1_node), .in14(pull_resistor_1_node),
    .in15(pull_resistor_1_node), .out(rY[3]), .sel(B[3:0]));
  Multiplexer #(.select(4)) multiplexer_21 (
    .in0(multiplexer_1_out[11]), .in1(multiplexer_1_out[10]), .in2(multiplexer_1_out[9]),
    .in3(multiplexer_1_out[8]), .in4(multiplexer_1_out[7]), .in5(multiplexer_1_out[6]),
    .in6(multiplexer_1_out[5]), .in7(multiplexer_1_out[4]), .in8(multiplexer_1_out[3]),
    .in9(multiplexer_1_out[2]), .in10(multiplexer_1_out[1]), .in11(multiplexer_1_out[0]),
    .in12(pull_resistor_1_node), .in13(pull_resistor_1_node), .in14(pull_resistor_1_node),
    .in15(pull_resistor_1_node), .out(rY[4]), .sel(B[3:0]));
  Multiplexer #(.select(4)) multiplexer_22 (
    .in0(multiplexer_1_out[10]), .in1(multiplexer_1_out[9]), .in2(multiplexer_1_out[8]),
    .in3(multiplexer_1_out[7]), .in4(multiplexer_1_out[6]), .in5(multiplexer_1_out[5]),
    .in6(multiplexer_1_out[4]), .in7(multiplexer_1_out[3]), .in8(multiplexer_1_out[2]),
    .in9(multiplexer_1_out[1]), .in10(multiplexer_1_out[0]), .in11(pull_resistor_1_node),
    .in12(pull_resistor_1_node), .in13(pull_resistor_1_node), .in14(pull_resistor_1_node),
    .in15(pull_resistor_1_node), .out(rY[5]), .sel(B[3:0]));
  Multiplexer #(.select(4)) multiplexer_23 (
    .in0(multiplexer_1_out[9]), .in1(multiplexer_1_out[8]), .in2(multiplexer_1_out[7]),
    .in3(multiplexer_1_out[6]), .in4(multiplexer_1_out[5]), .in5(multiplexer_1_out[4]),
    .in6(multiplexer_1_out[3]), .in7(multiplexer_1_out[2]), .in8(multiplexer_1_out[1]),
    .in9(multiplexer_1_out[0]), .in10(pull_resistor_1_node), .in11(pull_resistor_1_node),
    .in12(pull_resistor_1_node), .in13(pull_resistor_1_node), .in14(pull_resistor_1_node),
    .in15(pull_resistor_1_node), .out(rY[6]), .sel(B[3:0]));
  Multiplexer #(.select(4)) multiplexer_24 (
    .in0(multiplexer_1_out[8]), .in1(multiplexer_1_out[7]), .in2(multiplexer_1_out[6]),
    .in3(multiplexer_1_out[5]), .in4(multiplexer_1_out[4]), .in5(multiplexer_1_out[3]),
    .in6(multiplexer_1_out[2]), .in7(multiplexer_1_out[1]), .in8(multiplexer_1_out[0]),
    .in9(pull_resistor_1_node), .in10(pull_resistor_1_node), .in11(pull_resistor_1_node),
    .in12(pull_resistor_1_node), .in13(pull_resistor_1_node), .in14(pull_resistor_1_node),
    .in15(pull_resistor_1_node), .out(rY[7]), .sel(B[3:0]));
  Multiplexer #(.select(4)) multiplexer_25 (
    .in0(multiplexer_1_out[7]), .in1(multiplexer_1_out[6]), .in2(multiplexer_1_out[5]),
    .in3(multiplexer_1_out[4]), .in4(multiplexer_1_out[3]), .in5(multiplexer_1_out[2]),
    .in6(multiplexer_1_out[1]), .in7(multiplexer_1_out[0]), .in8(pull_resistor_1_node),
    .in9(pull_resistor_1_node), .in10(pull_resistor_1_node), .in11(pull_resistor_1_node),
    .in12(pull_resistor_1_node), .in13(pull_resistor_1_node), .in14(pull_resistor_1_node),
    .in15(pull_resistor_1_node), .out(rY[8]), .sel(B[3:0]));
  Multiplexer #(.select(4)) multiplexer_26 (
    .in0(multiplexer_1_out[6]), .in1(multiplexer_1_out[5]), .in2(multiplexer_1_out[4]),
    .in3(multiplexer_1_out[3]), .in4(multiplexer_1_out[2]), .in5(multiplexer_1_out[1]),
    .in6(multiplexer_1_out[0]), .in7(pull_resistor_1_node), .in8(pull_resistor_1_node),
    .in9(pull_resistor_1_node), .in10(pull_resistor_1_node), .in11(pull_resistor_1_node),
    .in12(pull_resistor_1_node), .in13(pull_resistor_1_node), .in14(pull_resistor_1_node),
    .in15(pull_resistor_1_node), .out(rY[9]), .sel(B[3:0]));
  Multiplexer #(.select(4)) multiplexer_27 (
    .in0(multiplexer_1_out[5]), .in1(multiplexer_1_out[4]), .in2(multiplexer_1_out[3]),
    .in3(multiplexer_1_out[2]), .in4(multiplexer_1_out[1]), .in5(multiplexer_1_out[0]),
    .in6(pull_resistor_1_node), .in7(pull_resistor_1_node), .in8(pull_resistor_1_node),
    .in9(pull_resistor_1_node), .in10(pull_resistor_1_node), .in11(pull_resistor_1_node),
    .in12(pull_resistor_1_node), .in13(pull_resistor_1_node), .in14(pull_resistor_1_node),
    .in15(pull_resistor_1_node), .out(rY[10]), .sel(B[3:0]));
  Multiplexer #(.select(4)) multiplexer_28 (
    .in0(multiplexer_1_out[4]), .in1(multiplexer_1_out[3]), .in2(multiplexer_1_out[2]),
    .in3(multiplexer_1_out[1]), .in4(multiplexer_1_out[0]), .in5(pull_resistor_1_node),
    .in6(pull_resistor_1_node), .in7(pull_resistor_1_node), .in8(pull_resistor_1_node),
    .in9(pull_resistor_1_node), .in10(pull_resistor_1_node), .in11(pull_resistor_1_node),
    .in12(pull_resistor_1_node), .in13(pull_resistor_1_node), .in14(pull_resistor_1_node),
    .in15(pull_resistor_1_node), .out(rY[11]), .sel(B[3:0]));
  Multiplexer #(.select(4)) multiplexer_29 (
    .in0(multiplexer_1_out[3]), .in1(multiplexer_1_out[2]), .in2(multiplexer_1_out[1]),
    .in3(multiplexer_1_out[0]), .in4(pull_resistor_1_node), .in5(pull_resistor_1_node),
    .in6(pull_resistor_1_node), .in7(pull_resistor_1_node), .in8(pull_resistor_1_node),
    .in9(pull_resistor_1_node), .in10(pull_resistor_1_node), .in11(pull_resistor_1_node),
    .in12(pull_resistor_1_node), .in13(pull_resistor_1_node), .in14(pull_resistor_1_node),
    .in15(pull_resistor_1_node), .out(rY[12]), .sel(B[3:0]));
  Multiplexer #(.select(4)) multiplexer_30 (
    .in0(multiplexer_1_out[2]), .in1(multiplexer_1_out[1]), .in2(multiplexer_1_out[0]),
    .in3(pull_resistor_1_node), .in4(pull_resistor_1_node), .in5(pull_resistor_1_node),
    .in6(pull_resistor_1_node), .in7(pull_resistor_1_node), .in8(pull_resistor_1_node),
    .in9(pull_resistor_1_node), .in10(pull_resistor_1_node), .in11(pull_resistor_1_node),
    .in12(pull_resistor_1_node), .in13(pull_resistor_1_node), .in14(pull_resistor_1_node),
    .in15(pull_resistor_1_node), .out(rY[13]), .sel(B[3:0]));
  Multiplexer #(.select(4)) multiplexer_31 (
    .in0(multiplexer_1_out[1]), .in1(multiplexer_1_out[0]), .in2(pull_resistor_1_node),
    .in3(pull_resistor_1_node), .in4(pull_resistor_1_node), .in5(pull_resistor_1_node),
    .in6(pull_resistor_1_node), .in7(pull_resistor_1_node), .in8(pull_resistor_1_node),
    .in9(pull_resistor_1_node), .in10(pull_resistor_1_node), .in11(pull_resistor_1_node),
    .in12(pull_resistor_1_node), .in13(pull_resistor_1_node), .in14(pull_resistor_1_node),
    .in15(pull_resistor_1_node), .out(rY[14]), .sel(B[3:0]));
  Multiplexer #(.select(4)) multiplexer_32 (
    .in0(multiplexer_1_out[0]), .in1(pull_resistor_1_node), .in2(pull_resistor_1_node),
    .in3(pull_resistor_1_node), .in4(pull_resistor_1_node), .in5(pull_resistor_1_node),
    .in6(pull_resistor_1_node), .in7(pull_resistor_1_node), .in8(pull_resistor_1_node),
    .in9(pull_resistor_1_node), .in10(pull_resistor_1_node), .in11(pull_resistor_1_node),
    .in12(pull_resistor_1_node), .in13(pull_resistor_1_node), .in14(pull_resistor_1_node),
    .in15(pull_resistor_1_node), .out(rY[15]), .sel(B[3:0]));
  Pull_Resistor pull_resistor_1 (.node(pull_resistor_1_node));

  assign Y = {rY[0], rY[1], rY[2], rY[3], rY[4], rY[5], rY[6], rY[7], rY[8], rY[9], rY[10], rY[11], rY[12], rY[13], rY[14], rY[15]};
endmodule

module aluMICROCODED (
  input  [3:0] OP,
  input  CLK,
  input  [15:0] Din,
  output FS,
  output FO,
  output FC,
  output FZ,
  output [15:0] Dout
);

  wire and_1_out, and_2_out, not_1_out, pull_resistor_1_node;
  wire [15:0] alu_1_y, register_1_q, register_2_q;

  and and_1 (and_1_out, ~OP[0], OP[3]);  // AND_Gate
  and and_2 (and_2_out, OP[0], OP[3]);
  not not_1 (not_1_out, OP[3]);
  assign Dout = not_1_out ? alu_1_y : 16'bz;  // Controlled_Buffer controlled_buffer_1
  Register #(.width(16)) register_1 (.D(Din), .en(and_1_out), .clk(CLK), .Q(register_1_q), .clr(pull_resistor_1_node));
  Register #(.width(16)) register_2 (.D(Din), .en(and_2_out), .clk(CLK), .Q(register_2_q), .clr(pull_resistor_1_node));
  Pull_Resistor pull_resistor_1 (.node(pull_resistor_1_node));
  alu alu_1 (.funct(OP[2:0]), .A(register_1_q), .B(register_2_q), .Y(alu_1_y), .FZ(FZ), .FO(FO), .FC(FC), .FS(FS));
endmodule

module T74574 (
  input  D0,
  input  D1,
  input  D2,
  input  D3,
  input  D4,
  input  D5,
  input  D6,
  input  CLK,
  input  D7,
  input  nOE,
  output O0,
  output O1,
  output O2,
  output O3,
  output O4,
  output O5,
  output O6,
  output O7
);

  wire not_1_out;
  wire [7:0] register_1_q;

  Register register_1 (.D({D7, D6, D5, D4, D3, D2, D1, D0}), .en(1'b1), .clk(CLK), .Q(register_1_q), .clr(1'b0));
  not not_1 (not_1_out, nOE);
  assign {O7, O6, O5, O4, O3, O2, O1, O0} = not_1_out ? register_1_q : 8'bz;  // Controlled_Buffer controlled_buffer_1
endmodule

module T74257 (
  input  nOE,
  input  isB,
  input  A1,
  input  B1,
  input  A2,
  input  B2,
  input  A3,
  input  B3,
  input  A4,
  input  B4,
  output Y1,
  output Y2,
  output Y3,
  output Y4
);

  wire not_1_out;

  not not_1 (not_1_out, nOE);
  Multiplexer #(.disabled("Z"), .enable("true")) multiplexer_1 (
    .in0(A1), .in1(B1), .out(Y1), .sel(isB), .en(not_1_out));
  Multiplexer #(.disabled("Z"), .enable("true")) multiplexer_2 (
    .in0(A2), .in1(B2), .out(Y2), .sel(isB), .en(not_1_out));
  Multiplexer #(.disabled("Z"), .enable("true")) multiplexer_3 (
    .in0(A3), .in1(B3), .out(Y3), .sel(isB), .en(not_1_out));
  Multiplexer #(.disabled("Z"), .enable("true")) multiplexer_4 (
    .in0(A4), .in1(B4), .out(Y4), .sel(isB), .en(not_1_out));
endmodule

module T74245 (
  input  DIR,
  input  nOE,
  input  A1in,
  input  B1in,
  input  A2in,
  input  B2in,
  input  A3in,
  input  B3in,
  input  A4in,
  input  B4in,
  input  A5in,
  input  B5in,
  input  A6in,
  input  B6in,
  input  A7in,
  input  B7in,
  input  A8in,
  input  B8in,
  output B1out,
  output A1out,
  output B2out,
  output A2out,
  output B3out,
  output A3out,
  output B4out,
  output A4out,
  output B5out,
  output A5out,
  output B6out,
  output A6out,
  output B7out,
  output A7out,
  output B8out,
  output A8out
);

  wire and_1_out, and_2_out;

  and and_1 (and_1_out, DIR, ~nOE);  // AND_Gate
  assign B1out = and_1_out ? A1in : 1'bz;  // Controlled_Buffer controlled_buffer_1
  assign B2out = and_1_out ? A2in : 1'bz;  // Controlled_Buffer controlled_buffer_2
  assign B3out = and_1_out ? A3in : 1'bz;  // Controlled_Buffer controlled_buffer_3
  assign B4out = and_1_out ? A4in : 1'bz;  // Controlled_Buffer controlled_buffer_4
  assign B5out = and_1_out ? A5in : 1'bz;  // Controlled_Buffer controlled_buffer_5
  assign B6out = and_1_out ? A6in : 1'bz;  // Controlled_Buffer controlled_buffer_6
  assign B7out = and_1_out ? A7in : 1'bz;  // Controlled_Buffer controlled_buffer_7
  assign B8out = and_1_out ? A8in : 1'bz;  // Controlled_Buffer controlled_buffer_8
  and and_2 (and_2_out, ~DIR, ~nOE);  // AND_Gate
  assign A1out = and_2_out ? B1in : 1'bz;  // Controlled_Buffer controlled_buffer_9
  assign A2out = and_2_out ? B2in : 1'bz;  // Controlled_Buffer controlled_buffer_10
  assign A3out = and_2_out ? B3in : 1'bz;  // Controlled_Buffer controlled_buffer_11
  assign A4out = and_2_out ? B4in : 1'bz;  // Controlled_Buffer controlled_buffer_12
  assign A5out = and_2_out ? B5in : 1'bz;  // Controlled_Buffer controlled_buffer_13
  assign A6out = and_2_out ? B6in : 1'bz;  // Controlled_Buffer controlled_buffer_14
  assign A7out = and_2_out ? B7in : 1'bz;  // Controlled_Buffer controlled_buffer_15
  assign A8out = and_2_out ? B8in : 1'bz;  // Controlled_Buffer controlled_buffer_16
endmodule

module T744067 (
  input  S0,
  input  S1,
  input  S2,
  input  S3,
  input  nE,
  input  Y0in,
  input  Y1in,
  input  Y2in,
  input  Y3in,
  input  Y4in,
  input  Y5in,
  input  Y6in,
  input  Y7in,
  input  Y8in,
  input  Y9in,
  input  Y10in,
  input  Y11in,
  input  Y12in,
  input  Y13in,
  input  Y14in,
  input  Y15in,
  output Zout
);

  wire not_1_out;

  not not_1 (not_1_out, nE);
  Multiplexer #(.disabled("Z"), .enable("true"), .select(4)) multiplexer_1 (
    .in0(Y0in), .in1(Y1in), .in2(Y2in), .in3(Y3in), .in4(Y4in), .in5(Y5in), .in6(Y6in), .in7(Y7in),
    .in8(Y8in), .in9(Y9in), .in10(Y10in), .in11(Y11in), .in12(Y12in), .in13(Y13in), .in14(Y14in),
    .in15(Y15in), .out(Zout), .sel({S3, S2, S1, S0}), .en(not_1_out));

  // Notes on the sheet:
  //   use ONLY in muxing configuration
endmodule

module M28C64Atop (
  input  nWE,
  input  nOE,
  input  nCE,
  input  A0,
  input  A1,
  input  A2,
  input  A3,
  input  A4,
  input  A5,
  input  A6,
  input  A7,
  input  A8,
  input  A9,
  input  A10,
  input  A11,
  input  A12,
  output O0,
  output O1,
  output O2,
  output O3,
  output O4,
  output O5,
  output O6,
  output O7
);

  wire and_1_out, not_1_out, not_2_out;
  wire [7:0] rom_1_data;

  and and_1 (and_1_out, not_1_out, not_2_out);
  not not_1 (not_1_out, nOE);
  not not_2 (not_2_out, nCE);
  ROM #(.addrWidth(13)) rom_1 (.addr({A12, A11, A10, A9, A8, A7, A6, A5, A4, A3, A2, A1, A0}), .data(rom_1_data));
  assign {O7, O6, O5, O4, O3, O2, O1, O0} = and_1_out ? rom_1_data : 8'bz;  // Controlled_Buffer controlled_buffer_1

  // Notes on the sheet:
  //   technically this chip be written too, but that is ignored here
  //   contents of rom_1 (hex, n*v repeats v):
  //   0 0 4 2 4 61*0 1 15*0 1 15*0 20 15*0 30 15*0 2 15*0 2 15*0 4 2 4 1 0 0 1 9*0 4 0 c 13*0 4 2 4 13*0 4
  //   0 4
endmodule

module M28C64Amid (
  input  nWE,
  input  nOE,
  input  nCE,
  input  A0,
  input  A1,
  input  A2,
  input  A3,
  input  A4,
  input  A5,
  input  A6,
  input  A7,
  input  A8,
  input  A9,
  input  A10,
  input  A11,
  input  A12,
  output O0,
  output O1,
  output O2,
  output O3,
  output O4,
  output O5,
  output O6,
  output O7
);

  wire and_1_out, not_1_out, not_2_out;
  wire [7:0] rom_1_data;

  and and_1 (and_1_out, not_1_out, not_2_out);
  not not_1 (not_1_out, nOE);
  not not_2 (not_2_out, nCE);
  ROM #(.addrWidth(13)) rom_1 (.addr({A12, A11, A10, A9, A8, A7, A6, A5, A4, A3, A2, A1, A0}), .data(rom_1_data));
  assign {O7, O6, O5, O4, O3, O2, O1, O0} = and_1_out ? rom_1_data : 8'bz;  // Controlled_Buffer controlled_buffer_1

  // Notes on the sheet:
  //   technically this chip be written too, but that is ignored here
  //   contents of rom_1 (hex, n*v repeats v):
  //   28 72 0 50 20 48 10*0 28 72 0 50 12*0 28 72 0 50 80 11*0 28 72 0 50 80 11*0 28 72 50 13*0 28 72 50
  //   13*0 28 72 14*0 28 72 50 13*0 28 72 50 2c 51 11*0 28 72 50 2c 40 11*0 28 72 0 50 20 48 28 30 51 7*0
  //   28 72 20 0 50 11*0 28 72 0 50 20 4c 10*0 28 72 20 0 0 51 10*0 28 72 14*0 28 72
endmodule

module M28C64Abot (
  input  nWE,
  input  nOE,
  input  nCE,
  input  A0,
  input  A1,
  input  A2,
  input  A3,
  input  A4,
  input  A5,
  input  A6,
  input  A7,
  input  A8,
  input  A9,
  input  A10,
  input  A11,
  input  A12,
  output O0,
  output O1,
  output O2,
  output O3,
  output O4,
  output O5,
  output O6,
  output O7
);

  wire and_1_out, not_1_out, not_2_out;
  wire [7:0] rom_1_data;

  and and_1 (and_1_out, not_1_out, not_2_out);
  not not_1 (not_1_out, nOE);
  not not_2 (not_2_out, nCE);
  ROM #(.addrWidth(13)) rom_1 (.addr({A12, A11, A10, A9, A8, A7, A6, A5, A4, A3, A2, A1, A0}), .data(rom_1_data));
  assign {O7, O6, O5, O4, O3, O2, O1, O0} = and_1_out ? rom_1_data : 8'bz;  // Controlled_Buffer controlled_buffer_1

  // Notes on the sheet:
  //   technically this chip be written too, but that is ignored here
  //   contents of rom_1 (hex, n*v repeats v):
  //   2 2 4 74 8c 41 10*1 2 2 26 56 8b 11*1 2 2 6 56 83 11*1 2 2 6 56 3 11*1 2 2 43 13*1 2 2 43 13*1 2 2
  //   83 13*1 2 2 43 13*1 2 2 2 42 83 11*1 2 2 2 42 3 11*1 2 2 6 76 8e 2 2 2 3 7*1 2 2 6 76 8b 11*1 2 2 6
  //   76 8e 43 10*1 2 2 6 76 8a 83 10*1 2 2 14*1 2 2 14*1
endmodule

module AT28C256_ROM_2 (
  input  A0,
  input  A1,
  input  A2,
  input  A3,
  input  A4,
  input  A5,
  input  A6,
  input  A7,
  input  A8,
  input  A9,
  input  A10,
  input  A11,
  input  A12,
  input  A13,
  input  A14,
  input  nWE,
  input  nOE,
  input  nCE,
  output O0,
  output O1,
  output O2,
  output O3,
  output O4,
  output O5,
  output O6,
  output O7
);

  wire and_1_out;
  wire [7:0] rom_1_data;

  ROM #(.addrWidth(15)) rom_1 (
    .addr({A14, A13, A12, A11, A10, A9, A8, A7, A6, A5, A4, A3, A2, A1, A0}), .data(rom_1_data));
  and and_1 (and_1_out, ~nOE, ~nCE);  // AND_Gate
  assign {O7, O6, O5, O4, O3, O2, O1, O0} = and_1_out ? rom_1_data : 8'bz;  // Controlled_Buffer controlled_buffer_1

  // Notes on the sheet:
  //   contents of rom_1 (hex, n*v repeats v):
  //   48 0 c0 60 88 fe 28 0 98 fe d0 b1 5*c0 61 88 fe 10 a8 0 39 0 49 0 39 0 49 0 90 28 0 39 ff 4e 0 18 ff
  //   98 fe 5*d0 b1 18 ff 98 fe 18 0 98 fe 5*d0 b1 39 ff 49 0 29 0 18 0 90 98 fe 5*d0 b1 0 88 fe 39 0 49 0
  //   39 0 49 0 90 28 0 2a 7f 98 fe b0 28 1 2a 7f 98 fe b0 29 0 2a 7f 98 fe 18 0 90 b0 32 49 0 c0 c0 80 a8
  //   0 d0 d0 28 0 29 0 48 0 b0 a8 0 18 0 48 0 c0 10 18 0 a8 0 10 2f 0 2a 0 28 fe 80 a8 0 10 2f 0 2a 0 28
  //   fe 80 a8 0 10 2f 0 2a 0 28 fe 80 a8 0 10 2f 0 2a 0 28 fe 80 a8 0 d0 b0 32 49 0 18 f0 18 0 a8 0 b0 18
  //   f0 18 0 a8 0 b0 18 7f 18 0 90 29 0 4a 0 90 98 fe b0 32 49 0 80 80 31 4a 0 28 0 28 0 29 0 48 0 18 0
  //   b0 18 0 b0 18 f0 18 f0 18 0 a8 0 2b 80 2b 40 18 0 a8 0 18 0 98 ff 98 ff 98 ff 98 ff 98 ff 98 ff 98
  //   ff 98 ff 98 ff 98 ff 98 ff 98 ff 98 ff 98 ff 98 ff 98 ff 98 ff 98 ff 98 ff 98 ff 98 ff 98 ff 98 ff
  //   98 ff 98 ff 98 ff 98 ff 98 ff 98 ff 98 ff 98 ff 98 ff 98 ff 98 ff 98 ff 98 ff 98 ff 98 ff 98 ff 98
  //   ff 98 ff 98 ff 98 ff 98 ff 98 ff 98 ff 98 ff 98 ff 98 ff 98 ff 98 ff 98 ff 98 ff 98 ff 98 ff 98 ff
  //   98 ff 98 ff 98 ff 98 ff 98 ff 98 ff 98 ff 98 ff 98 ff 98 ff 98 ff 98 ff 98 ff 98 ff 98 ff 98 ff 98
  //   ff 98 ff 98 ff 98 ff 98 ff 98 ff 98 ff 98 ff 98 ff 98 ff 98 ff 98 ff 98 ff 98 ff 98 ff 98 ff 98 ff
  //   98 ff 98 ff 98 ff 98 ff 98 ff 98 ff 98 ff 98 ff 98 ff 98 ff 98 ff 98 ff 98 ff 98 ff 98 ff 98 ff 98
  //   ff 98 ff 98 ff 98 ff 98 ff 98 ff 98 ff 98 ff 98 ff 98 ff 98 ff 98 ff 98 ff 98 ff 98 ff 98 ff 98 ff
  //   98 ff 98 ff 98 ff 98 ff 98 ff 98 ff 98 ff 98 ff 98 ff 98 ff 98 ff 98 ff 98 ff 98 ff 98 ff 98 ff 98
  //   ff 98 ff 98 ff 98 ff 98 ff 98 ff 98 ff 98 ff 98 ff 98 ff 98 ff 98 ff 98 ff 98 ff 98 ff 98 ff 98 ff
  //   98 ff 98 ff 98 ff 98 ff 98 ff 98 ff 98 ff 98 ff 98 ff 98 ff 98 ff 98 ff 98 ff 98 ff 98 ff 98 ff 98
  //   ff 98 ff 98 ff 98 ff 98 ff 98 ff 98 ff 98 ff 98 ff 98 ff 98 ff 98 ff 98 ff 98 ff 98 ff 98 ff 98 ff
  //   98 ff 98 ff 98 ff 98 ff 98 ff 98 ff 98 ff 98 ff 98 ff 98 ff 98 ff 98 ff 98 ff 98 ff 98 ff 98 ff 98
  //   ff 98 ff 98 ff 98 ff 98 ff 98 ff 98 ff 98 ff 98 ff 98 ff 98 ff 98 ff 98 ff 98 ff 98 ff 98 ff 98 ff
  //   98 ff 98 ff 98 ff 98 ff 98 ff 98 ff 98 ff 98 ff 98 ff 98 ff 98 ff 98 ff 98 ff 98 ff 98 ff 98 ff 98
  //   ff 98 ff 98 ff 88 fe 32 49 2 18 0 98 fe 18 ff 18 f0 18 0 a8 0 32 4a 3 18 ff 18 f0 18 0 a8 0 32 4a 3
  //   18 ff 18 f0 18 0 a8 0 32 4a 3 18 ff 18 f0 18 0 a8 0 32 4a 3 18 f0 18 0 a8 0 48 0 18 f0 18 0 a8 0 48
  //   0 18 ff 18 0 a8 0 48 0 88 fe a8 0 18 0 a8 0 48 0 a8 0 48
endmodule

module AT28C256_ROM_1 (
  input  A0,
  input  A1,
  input  A2,
  input  A3,
  input  A4,
  input  A5,
  input  A6,
  input  A7,
  input  A8,
  input  A9,
  input  A10,
  input  A11,
  input  A12,
  input  A13,
  input  A14,
  input  nWE,
  input  nOE,
  input  nCE,
  output O0,
  output O1,
  output O2,
  output O3,
  output O4,
  output O5,
  output O6,
  output O7
);

  wire and_1_out;
  wire [7:0] rom_1_data;

  ROM #(.addrWidth(15)) rom_1 (
    .addr({A14, A13, A12, A11, A10, A9, A8, A7, A6, A5, A4, A3, A2, A1, A0}), .data(rom_1_data));
  and and_1 (and_1_out, ~nOE, ~nCE);  // AND_Gate
  assign {O7, O6, O5, O4, O3, O2, O1, O0} = and_1_out ? rom_1_data : 8'bz;  // Controlled_Buffer controlled_buffer_1

  // Notes on the sheet:
  //   contents of rom_1 (hex, n*v repeats v):
  //   0 ee 8 80 80 cf 80 1 80 cf 80 0 4 5 8 9 a 40 50 ff 84 0 50 40 a 0 30 40 8 0 3e 45 50 1 50 f0 0 28 50
  //   0 50 ff a0 90 80 50 40 0 50 0 50 ff 80 1 80 fe a0 90 80 50 40 0 50 0 0 49 50 1 40 20 45 50 ff a0 90
  //   80 50 40 0 0 90 ef 80 a 0 62 80 8 0 69 89 90 1 90 ff 90 ef 0 90 0 90 0 90 ef 0 90 1 90 ff 90 ef 80
  //   20 89 0 99 0 83 8 9 88 0 50 90 80 80 1 90 1 0 73 0 0 73 80 a 0 50 4 48 80 78 0 50 84 80 c 80 f 80 d0
  //   88 0 50 84 80 8 80 f 80 d0 88 0 50 84 80 4 80 f 80 d0 88 0 50 84 80 0 80 f 80 d0 88 0 50 40 0 88 0
  //   c4 80 0 90 4 0 73 0 80 4 90 5 0 73 0 80 ff 90 20 98 80 1 0 cf 98 80 ef 0 aa 0 e8 b8 c9 bc 0 eb 80 1
  //   90 1 a0 1 0 d8 80 1 0 80 0 0 20 0 80 9 90 b 0 84 10 0 10 0 80 3e 0 50 80 20 80 0 80 1 80 2 80 3 80 4
  //   80 5 80 6 80 7 80 8 80 9 80 a 80 b 80 c 80 d 80 e 80 f 80 10 80 11 80 12 80 13 80 14 80 15 80 16 80
  //   17 80 18 80 19 80 1a 80 1b 80 1c 80 1d 80 1e 80 1f 80 20 80 21 80 22 80 23 80 24 80 25 80 26 80 27
  //   80 28 80 29 80 2a 80 2b 80 2c 80 2d 80 2e 80 2f 80 30 80 31 80 32 80 33 80 34 80 35 80 36 80 37 80
  //   38 80 39 80 3a 80 3b 80 3c 80 3d 80 3e 80 3f 80 40 80 41 80 42 80 43 80 44 80 45 80 46 80 47 80 48
  //   80 49 80 4a 80 4b 80 4c 80 4d 80 4e 80 4f 80 50 80 51 80 52 80 53 80 54 80 55 80 56 80 57 80 58 80
  //   59 80 5a 80 5b 80 5c 80 5d 80 5e 80 5f 80 60 80 61 80 62 80 63 80 64 80 65 80 66 80 67 80 68 80 69
  //   80 6a 80 6b 80 6c 80 6d 80 6e 80 6f 80 70 80 71 80 72 80 73 80 74 80 75 80 76 80 77 80 78 80 79 80
  //   7a 80 7b 80 7c 80 7d 80 7e 80 7f 80 80 80 81 80 82 80 83 80 84 80 85 80 86 80 87 80 88 80 89 80 8a
  //   80 8b 80 8c 80 8d 80 8e 80 8f 80 90 80 91 80 92 80 93 80 94 80 95 80 96 80 97 80 98 80 99 80 9a 80
  //   9b 80 9c 80 9d 80 9e 80 9f 80 a0 80 a1 80 a2 80 a3 80 a4 80 a5 80 a6 80 a7 80 a8 80 a9 80 aa 80 ab
  //   80 ac 80 ad 80 ae 80 af 80 b0 80 b1 80 b2 80 b3 80 b4 80 b5 80 b6 80 b7 80 b8 80 b9 80 ba 80 bb 80
  //   bc 80 bd 80 be 80 bf 80 c0 80 c1 80 c2 80 c3 80 c4 80 c5 80 c6 80 c7 80 c8 80 c9 80 ca 80 cb 80 cc
  //   80 cd 80 ce 80 cf 80 d0 80 d1 80 d2 80 d3 80 d4 80 d5 80 d6 80 d7 80 d8 80 d9 80 da 80 db 80 dc 80
  //   dd 80 de 80 df 80 e0 80 e1 80 e2 80 e3 80 e4 80 e5 80 e6 80 e7 80 e8 80 e9 80 ea 80 eb 80 ec 80 ed
  //   80 ee 80 ef 40 fe 44 0 e0 40 0 40 fe 80 0 90 18 a0 4 0 d8 88 0 1d 80 0 90 84 a0 4 0 d8 88 0 25 80 0
  //   90 14 a0 4 0 d8 88 0 2d 80 0 90 88 a0 5 0 d8 88 0 37 80 8d 90 f 0 84 0 fa 80 1c 90 68 0 84 0 fa 80 5
  //   90 fa 0 84 0 fa 80 cf 0 8a 80 a 0 50 0 fa 0 cb 0 fa
endmodule

module AS7C1026B_RAM_1 (
  input  A15,
  input  A14,
  input  A13,
  input  A12,
  input  A11,
  input  A10,
  input  A9,
  input  A8,
  input  A7,
  input  A6,
  input  A5,
  input  A4,
  input  A3,
  input  A2,
  input  A1,
  input  A0,
  input  nCE,
  input  nWE,
  input  nOE,
  input  nLB,
  input  nUB,
  input  IO15,
  input  IO14,
  input  IO13,
  input  IO12,
  input  IO11,
  input  IO10,
  input  IO9,
  input  IO8,
  input  IO7,
  input  IO6,
  input  IO5,
  input  IO4,
  input  IO3,
  input  IO2,
  input  IO1,
  input  IO0,
  output O15,
  output O14,
  output O13,
  output O12,
  output O11,
  output O10,
  output O9,
  output O8,
  output O7,
  output O6,
  output O5,
  output O4,
  output O3,
  output O2,
  output O1,
  output O0
);

  wire and_1_out, not_1_out, not_2_out, not_3_out;
  wire [15:0] controlled_buffer_1_out, ram_1_dout;

  not not_1 (not_1_out, nWE);
  not not_2 (not_2_out, nOE);
  assign controlled_buffer_1_out = not_1_out ? {IO15, IO14, IO13, IO12, IO11, IO10, IO9, IO8, IO7, IO6, IO5, IO4, IO3, IO2, IO1, IO0} : 16'bz;  // Controlled_Buffer controlled_buffer_1
  RAM #(.addrWidth(16), .asyncread("true"), .dataWidth(16), .\type ("nonvolatile")) ram_1 (
    .addr({A15, A14, A13, A12, A11, A10, A9, A8, A7, A6, A5, A4, A3, A2, A1, A0}), .we(not_1_out),
    .oe(not_2_out), .clk(nWE), .din(controlled_buffer_1_out), .dout(ram_1_dout));
  not not_3 (not_3_out, not_1_out);
  and and_1 (and_1_out, not_2_out, not_3_out);
  assign {O15, O14, O13, O12, O11, O10, O9, O8, O7, O6, O5, O4, O3, O2, O1, O0} = and_1_out ? ram_1_dout : 16'bz;  // Controlled_Buffer controlled_buffer_2
endmodule

module registerfile (
  input  CLK,
  input  mask_save,
  input  mask_restore,
  input  [3:0] REG_SEL,
  input  SET,
  input  [7:0] IO_BUSY,
  input  [7:0] IO_INT,
  input  [15:0] data,
  output BUSY,
  output [2:0] INT_ID,
  output INT,
  output [15:0] REG_OUT
);

  wire buf_16b_1_out_0, buf_16b_1_out_1, buf_16b_1_out_2, buf_16b_1_out_3, buf_16b_1_out_4, buf_16b_1_out_5,
       buf_16b_1_out_6, buf_16b_1_out_7, buf_16b_1_out_8, buf_16b_1_out_9, buf_16b_1_out_10,
       buf_16b_1_out_11, buf_16b_1_out_12, buf_16b_1_out_13, buf_16b_1_out_14, buf_16b_1_out_15,
       buf_16b_3_out_0, buf_16b_3_out_1, buf_16b_3_out_2, buf_16b_3_out_3, buf_16b_3_out_4, buf_16b_3_out_5,
       buf_16b_3_out_6, buf_16b_3_out_7, buf_16b_3_out_8, buf_16b_3_out_9, buf_16b_3_out_10,
       buf_16b_3_out_11, buf_16b_3_out_12, buf_16b_3_out_13, buf_16b_3_out_14, buf_16b_3_out_15,
       buf_16b_5_out_0, buf_16b_5_out_1, buf_16b_5_out_2, buf_16b_5_out_3, buf_16b_5_out_4, buf_16b_5_out_5,
       buf_16b_5_out_6, buf_16b_5_out_7, buf_16b_5_out_8, buf_16b_5_out_9, buf_16b_5_out_10,
       buf_16b_5_out_11, buf_16b_5_out_12, buf_16b_5_out_13, buf_16b_5_out_14, buf_16b_5_out_15,
       n7404_2_pin2, n7404_2_pin4, n7404_2_pin6, n7404_2_pin8, n7404_2_pin10, n7404_2_pin12, n7404_3_pin10,
       n7404_3_pin12, n7427_1_pin8, n7427_1_pin11, not_1_out, not_2_out, not_3_out, not_4_out, not_5_out,
       octal_and_1_out_0, octal_and_1_out_1, octal_and_1_out_2, octal_and_1_out_3, octal_and_1_out_4,
       octal_and_1_out_5, octal_and_1_out_6, octal_and_1_out_7, r0_out_0, r0_out_1, r0_out_2, r0_out_3,
       r0_out_4, r0_out_5, r0_out_6, r0_out_7, r0_out_8, r0_out_9, r0_out_10, r0_out_11, r0_out_12,
       r0_out_13, r0_out_14, r0_out_15, r1we, r10_out_0, r10_out_1, r10_out_2, r10_out_3, r10_out_4,
       r10_out_5, r10_out_6, r10_out_7, r10_out_8, r10_out_9, r10_out_10, r10_out_11, r10_out_12, r10_out_13,
       r10_out_14, r10_out_15, r11_out_0, r11_out_1, r11_out_2, r11_out_3, r11_out_4, r11_out_5, r11_out_6,
       r11_out_7, r11_out_8, r11_out_9, r11_out_10, r11_out_11, r11_out_12, r11_out_13, r11_out_14,
       r11_out_15, r12_out_0, r12_out_1, r12_out_2, r12_out_3, r12_out_4, r12_out_5, r12_out_6, r12_out_7,
       r12_out_8, r12_out_9, r12_out_10, r12_out_11, r12_out_12, r12_out_13, r12_out_14, r12_out_15,
       r13_out_0, r13_out_1, r13_out_2, r13_out_3, r13_out_4, r13_out_5, r13_out_6, r13_out_7, r13_out_8,
       r13_out_9, r13_out_10, r13_out_11, r13_out_12, r13_out_13, r13_out_14, r13_out_15, r14_out_0,
       r14_out_1, r14_out_2, r14_out_3, r14_out_4, r14_out_5, r14_out_6, r14_out_7, r14_out_8, r14_out_9,
       r14_out_10, r14_out_11, r14_out_12, r14_out_13, r14_out_14, r14_out_15, r15_out_0, r15_out_1,
       r15_out_2, r15_out_3, r15_out_4, r15_out_5, r15_out_6, r15_out_7, r15_out_8, r15_out_9, r15_out_10,
       r15_out_11, r15_out_12, r15_out_13, r15_out_14, r15_out_15, t74148_1_gs, t74154_1_out_0,
       t74154_1_out_2, t74154_1_out_3, t74154_1_out_4, t74154_1_out_5, t74154_1_out_6, t74154_1_out_7,
       t74154_1_out_8, t74154_1_out_9, t74154_1_out_10, t74154_1_out_11, t74154_1_out_12, t74154_1_out_13,
       t74154_1_out_14, t74154_1_out_15, t74154_2_out_0, t74154_2_out_1, t74154_2_out_2, t74154_2_out_3,
       t74154_2_out_4, t74154_2_out_5, t74154_2_out_6, t74154_2_out_7, t74154_2_out_8, t74154_2_out_9,
       t74154_2_out_10, t74154_2_out_11, t74154_2_out_12, t74154_2_out_13, t74154_2_out_14, t74154_2_out_15;
  wire [15:0] mask_saved, r1_out, r2_out_0, r3_out_0, r4_out_0, r5_out_0, r6_out_0, r7_out_0, r8_out_0,
       r9_out_0;

  not not_1 (not_1_out, SET);
  T74154 t74154_1 (
    .A(REG_SEL[0]), .B(REG_SEL[1]), .C(REG_SEL[2]), .D(REG_SEL[3]), .G1(not_1_out), .G2(1'b0),
    .out_0(t74154_1_out_0), .out_1(r1we), .out_2(t74154_1_out_2), .out_3(t74154_1_out_3),
    .out_4(t74154_1_out_4), .out_5(t74154_1_out_5), .out_6(t74154_1_out_6), .out_7(t74154_1_out_7),
    .out_8(t74154_1_out_8), .out_9(t74154_1_out_9), .out_10(t74154_1_out_10), .out_11(t74154_1_out_11),
    .out_12(t74154_1_out_12), .out_13(t74154_1_out_13), .out_14(t74154_1_out_14), .out_15(t74154_1_out_15));
  // NoConnect on t74154_1_out_0
  _7427 u_7427_1 (
    .pin11(n7427_1_pin11), .pin10(mask_save), .pin9(mask_restore), .pin8(n7427_1_pin8));  // open: pin1, pin2, pin3, pin4, pin5, pin6, pin13, pin12
  _7404 u_7404_1 (
    .pin1(r1we), .pin2(n7427_1_pin11));  // open: pin3, pin4, pin5, pin6, pin13, pin12, pin11, pin10, pin9, pin8
  not not_2 (not_2_out, r1we);
  buf_16b buf_16b_1 (
    .in_8(r1_out[8]), .in_9(r1_out[9]), .in_10(r1_out[10]), .in_11(r1_out[11]), .in_12(r1_out[12]),
    .in_13(r1_out[13]), .in_14(r1_out[14]), .in_15(r1_out[15]), .in_0(r1_out[0]), .in_1(r1_out[1]),
    .in_2(r1_out[2]), .in_3(r1_out[3]), .in_4(r1_out[4]), .in_5(r1_out[5]), .in_6(r1_out[6]),
    .in_7(r1_out[7]), .nOE2(not_2_out), .nOE1(1'b0), .out_8(buf_16b_1_out_8), .out_9(buf_16b_1_out_9),
    .out_10(buf_16b_1_out_10), .out_11(buf_16b_1_out_11), .out_12(buf_16b_1_out_12),
    .out_13(buf_16b_1_out_13), .out_14(buf_16b_1_out_14), .out_15(buf_16b_1_out_15), .out_0(buf_16b_1_out_0),
    .out_1(buf_16b_1_out_1), .out_2(buf_16b_1_out_2), .out_3(buf_16b_1_out_3), .out_4(buf_16b_1_out_4),
    .out_5(buf_16b_1_out_5), .out_6(buf_16b_1_out_6), .out_7(buf_16b_1_out_7));
  buf_16b buf_16b_2 (
    .in_8(data[8]), .in_9(data[9]), .in_10(data[10]), .in_11(data[11]), .in_12(data[12]), .in_13(data[13]),
    .in_14(data[14]), .in_15(data[15]), .in_0(data[0]), .in_1(data[1]), .in_2(data[2]), .in_3(data[3]),
    .in_4(data[4]), .in_5(data[5]), .in_6(data[6]), .in_7(data[7]), .nOE2(r1we), .nOE1(1'b0),
    .out_8(buf_16b_1_out_8), .out_9(buf_16b_1_out_9), .out_10(buf_16b_1_out_10), .out_11(buf_16b_1_out_11),
    .out_12(buf_16b_1_out_12), .out_13(buf_16b_1_out_13), .out_14(buf_16b_1_out_14),
    .out_15(buf_16b_1_out_15), .out_0(buf_16b_1_out_0), .out_1(buf_16b_1_out_1), .out_2(buf_16b_1_out_2),
    .out_3(buf_16b_1_out_3), .out_4(buf_16b_1_out_4), .out_5(buf_16b_1_out_5), .out_6(buf_16b_1_out_6),
    .out_7(buf_16b_1_out_7));
  not not_3 (not_3_out, mask_save);
  not not_4 (not_4_out, mask_restore);
  buf_16b buf_16b_3 (
    .in_8(mask_saved[8]), .in_9(mask_saved[9]), .in_10(mask_saved[10]), .in_11(mask_saved[11]),
    .in_12(mask_saved[12]), .in_13(mask_saved[13]), .in_14(mask_saved[14]), .in_15(mask_saved[15]),
    .in_0(mask_saved[0]), .in_1(mask_saved[1]), .in_2(mask_saved[2]), .in_3(mask_saved[3]),
    .in_4(mask_saved[4]), .in_5(mask_saved[5]), .in_6(mask_saved[6]), .in_7(mask_saved[7]), .nOE2(not_4_out),
    .nOE1(1'b0), .out_8(buf_16b_3_out_8), .out_9(buf_16b_3_out_9), .out_10(buf_16b_3_out_10),
    .out_11(buf_16b_3_out_11), .out_12(buf_16b_3_out_12), .out_13(buf_16b_3_out_13),
    .out_14(buf_16b_3_out_14), .out_15(buf_16b_3_out_15), .out_0(buf_16b_3_out_0), .out_1(buf_16b_3_out_1),
    .out_2(buf_16b_3_out_2), .out_3(buf_16b_3_out_3), .out_4(buf_16b_3_out_4), .out_5(buf_16b_3_out_5),
    .out_6(buf_16b_3_out_6), .out_7(buf_16b_3_out_7));
  buf_16b buf_16b_4 (
    .in_8(data[8]), .in_9(data[9]), .in_10(data[10]), .in_11(data[11]), .in_12(data[12]), .in_13(data[13]),
    .in_14(data[14]), .in_15(data[15]), .in_0(data[0]), .in_1(data[1]), .in_2(data[2]), .in_3(data[3]),
    .in_4(data[4]), .in_5(data[5]), .in_6(data[6]), .in_7(data[7]), .nOE2(mask_restore), .nOE1(1'b0),
    .out_8(buf_16b_3_out_8), .out_9(buf_16b_3_out_9), .out_10(buf_16b_3_out_10), .out_11(buf_16b_3_out_11),
    .out_12(buf_16b_3_out_12), .out_13(buf_16b_3_out_13), .out_14(buf_16b_3_out_14),
    .out_15(buf_16b_3_out_15), .out_0(buf_16b_3_out_0), .out_1(buf_16b_3_out_1), .out_2(buf_16b_3_out_2),
    .out_3(buf_16b_3_out_3), .out_4(buf_16b_3_out_4), .out_5(buf_16b_3_out_5), .out_6(buf_16b_3_out_6),
    .out_7(buf_16b_3_out_7));
  reg_16b reg_16b_1 (
    .in_12(buf_16b_1_out_12), .in_13(buf_16b_1_out_13), .in_14(buf_16b_1_out_14), .in_15(buf_16b_1_out_15),
    .in_0(buf_16b_1_out_0), .in_1(buf_16b_1_out_1), .in_2(buf_16b_1_out_2), .in_3(buf_16b_1_out_3),
    .in_4(buf_16b_1_out_4), .in_5(buf_16b_1_out_5), .in_6(buf_16b_1_out_6), .in_7(buf_16b_1_out_7),
    .in_8(buf_16b_1_out_8), .in_9(buf_16b_1_out_9), .in_10(buf_16b_1_out_10), .in_11(buf_16b_1_out_11),
    .CLK(CLK), .nWE(not_3_out), .out_12(mask_saved[12]), .out_13(mask_saved[13]), .out_14(mask_saved[14]),
    .out_15(mask_saved[15]), .out_0(mask_saved[0]), .out_1(mask_saved[1]), .out_2(mask_saved[2]),
    .out_3(mask_saved[3]), .out_4(mask_saved[4]), .out_5(mask_saved[5]), .out_6(mask_saved[6]),
    .out_7(mask_saved[7]), .out_8(mask_saved[8]), .out_9(mask_saved[9]), .out_10(mask_saved[10]),
    .out_11(mask_saved[11]));
  not not_5 (not_5_out, mask_save);
  buf_16b buf_16b_5 (
    .in_8(1'b0), .in_9(1'b0), .in_10(1'b0), .in_11(1'b0), .in_12(1'b0), .in_13(1'b0), .in_14(1'b0),
    .in_15(1'b0), .in_0(1'b0), .in_1(1'b0), .in_2(1'b0), .in_3(1'b0), .in_4(1'b0), .in_5(1'b0), .in_6(1'b0),
    .in_7(1'b0), .nOE2(not_5_out), .nOE1(1'b0), .out_8(buf_16b_5_out_8), .out_9(buf_16b_5_out_9),
    .out_10(buf_16b_5_out_10), .out_11(buf_16b_5_out_11), .out_12(buf_16b_5_out_12),
    .out_13(buf_16b_5_out_13), .out_14(buf_16b_5_out_14), .out_15(buf_16b_5_out_15), .out_0(buf_16b_5_out_0),
    .out_1(buf_16b_5_out_1), .out_2(buf_16b_5_out_2), .out_3(buf_16b_5_out_3), .out_4(buf_16b_5_out_4),
    .out_5(buf_16b_5_out_5), .out_6(buf_16b_5_out_6), .out_7(buf_16b_5_out_7));
  buf_16b buf_16b_6 (
    .in_8(buf_16b_3_out_8), .in_9(buf_16b_3_out_9), .in_10(buf_16b_3_out_10), .in_11(buf_16b_3_out_11),
    .in_12(buf_16b_3_out_12), .in_13(buf_16b_3_out_13), .in_14(buf_16b_3_out_14), .in_15(buf_16b_3_out_15),
    .in_0(buf_16b_3_out_0), .in_1(buf_16b_3_out_1), .in_2(buf_16b_3_out_2), .in_3(buf_16b_3_out_3),
    .in_4(buf_16b_3_out_4), .in_5(buf_16b_3_out_5), .in_6(buf_16b_3_out_6), .in_7(buf_16b_3_out_7),
    .nOE2(mask_save), .nOE1(1'b0), .out_8(buf_16b_5_out_8), .out_9(buf_16b_5_out_9),
    .out_10(buf_16b_5_out_10), .out_11(buf_16b_5_out_11), .out_12(buf_16b_5_out_12),
    .out_13(buf_16b_5_out_13), .out_14(buf_16b_5_out_14), .out_15(buf_16b_5_out_15), .out_0(buf_16b_5_out_0),
    .out_1(buf_16b_5_out_1), .out_2(buf_16b_5_out_2), .out_3(buf_16b_5_out_3), .out_4(buf_16b_5_out_4),
    .out_5(buf_16b_5_out_5), .out_6(buf_16b_5_out_6), .out_7(buf_16b_5_out_7));
  reg_16b r0 (
    .in_12(IO_INT[4]), .in_13(IO_INT[5]), .in_14(IO_INT[6]), .in_15(IO_INT[7]), .in_0(IO_BUSY[0]),
    .in_1(IO_BUSY[1]), .in_2(IO_BUSY[2]), .in_3(IO_BUSY[3]), .in_4(IO_BUSY[4]), .in_5(IO_BUSY[5]),
    .in_6(IO_BUSY[6]), .in_7(IO_BUSY[7]), .in_8(IO_INT[0]), .in_9(IO_INT[1]), .in_10(IO_INT[2]),
    .in_11(IO_INT[3]), .CLK(CLK), .nWE(1'b0), .out_12(r0_out_12), .out_13(r0_out_13), .out_14(r0_out_14),
    .out_15(r0_out_15), .out_0(r0_out_0), .out_1(r0_out_1), .out_2(r0_out_2), .out_3(r0_out_3),
    .out_4(r0_out_4), .out_5(r0_out_5), .out_6(r0_out_6), .out_7(r0_out_7), .out_8(r0_out_8),
    .out_9(r0_out_9), .out_10(r0_out_10), .out_11(r0_out_11));
  reg_16b r1 (
    .in_12(buf_16b_5_out_12), .in_13(buf_16b_5_out_13), .in_14(buf_16b_5_out_14), .in_15(buf_16b_5_out_15),
    .in_0(buf_16b_5_out_0), .in_1(buf_16b_5_out_1), .in_2(buf_16b_5_out_2), .in_3(buf_16b_5_out_3),
    .in_4(buf_16b_5_out_4), .in_5(buf_16b_5_out_5), .in_6(buf_16b_5_out_6), .in_7(buf_16b_5_out_7),
    .in_8(buf_16b_5_out_8), .in_9(buf_16b_5_out_9), .in_10(buf_16b_5_out_10), .in_11(buf_16b_5_out_11),
    .CLK(CLK), .nWE(n7427_1_pin8), .out_12(r1_out[12]), .out_13(r1_out[13]), .out_14(r1_out[14]),
    .out_15(r1_out[15]), .out_0(r1_out[0]), .out_1(r1_out[1]), .out_2(r1_out[2]), .out_3(r1_out[3]),
    .out_4(r1_out[4]), .out_5(r1_out[5]), .out_6(r1_out[6]), .out_7(r1_out[7]), .out_8(r1_out[8]),
    .out_9(r1_out[9]), .out_10(r1_out[10]), .out_11(r1_out[11]));
  reg_16b r2 (
    .in_12(data[12]), .in_13(data[13]), .in_14(data[14]), .in_15(data[15]), .in_0(data[0]), .in_1(data[1]),
    .in_2(data[2]), .in_3(data[3]), .in_4(data[4]), .in_5(data[5]), .in_6(data[6]), .in_7(data[7]),
    .in_8(data[8]), .in_9(data[9]), .in_10(data[10]), .in_11(data[11]), .CLK(CLK), .nWE(t74154_1_out_2),
    .out_12(r2_out_0[12]), .out_13(r2_out_0[13]), .out_14(r2_out_0[14]), .out_15(r2_out_0[15]),
    .out_0(r2_out_0[0]), .out_1(r2_out_0[1]), .out_2(r2_out_0[2]), .out_3(r2_out_0[3]), .out_4(r2_out_0[4]),
    .out_5(r2_out_0[5]), .out_6(r2_out_0[6]), .out_7(r2_out_0[7]), .out_8(r2_out_0[8]), .out_9(r2_out_0[9]),
    .out_10(r2_out_0[10]), .out_11(r2_out_0[11]));
  reg_16b r3 (
    .in_12(data[12]), .in_13(data[13]), .in_14(data[14]), .in_15(data[15]), .in_0(data[0]), .in_1(data[1]),
    .in_2(data[2]), .in_3(data[3]), .in_4(data[4]), .in_5(data[5]), .in_6(data[6]), .in_7(data[7]),
    .in_8(data[8]), .in_9(data[9]), .in_10(data[10]), .in_11(data[11]), .CLK(CLK), .nWE(t74154_1_out_3),
    .out_12(r3_out_0[12]), .out_13(r3_out_0[13]), .out_14(r3_out_0[14]), .out_15(r3_out_0[15]),
    .out_0(r3_out_0[0]), .out_1(r3_out_0[1]), .out_2(r3_out_0[2]), .out_3(r3_out_0[3]), .out_4(r3_out_0[4]),
    .out_5(r3_out_0[5]), .out_6(r3_out_0[6]), .out_7(r3_out_0[7]), .out_8(r3_out_0[8]), .out_9(r3_out_0[9]),
    .out_10(r3_out_0[10]), .out_11(r3_out_0[11]));
  reg_16b r4 (
    .in_12(data[12]), .in_13(data[13]), .in_14(data[14]), .in_15(data[15]), .in_0(data[0]), .in_1(data[1]),
    .in_2(data[2]), .in_3(data[3]), .in_4(data[4]), .in_5(data[5]), .in_6(data[6]), .in_7(data[7]),
    .in_8(data[8]), .in_9(data[9]), .in_10(data[10]), .in_11(data[11]), .CLK(CLK), .nWE(t74154_1_out_4),
    .out_12(r4_out_0[12]), .out_13(r4_out_0[13]), .out_14(r4_out_0[14]), .out_15(r4_out_0[15]),
    .out_0(r4_out_0[0]), .out_1(r4_out_0[1]), .out_2(r4_out_0[2]), .out_3(r4_out_0[3]), .out_4(r4_out_0[4]),
    .out_5(r4_out_0[5]), .out_6(r4_out_0[6]), .out_7(r4_out_0[7]), .out_8(r4_out_0[8]), .out_9(r4_out_0[9]),
    .out_10(r4_out_0[10]), .out_11(r4_out_0[11]));
  reg_16b r5 (
    .in_12(data[12]), .in_13(data[13]), .in_14(data[14]), .in_15(data[15]), .in_0(data[0]), .in_1(data[1]),
    .in_2(data[2]), .in_3(data[3]), .in_4(data[4]), .in_5(data[5]), .in_6(data[6]), .in_7(data[7]),
    .in_8(data[8]), .in_9(data[9]), .in_10(data[10]), .in_11(data[11]), .CLK(CLK), .nWE(t74154_1_out_5),
    .out_12(r5_out_0[12]), .out_13(r5_out_0[13]), .out_14(r5_out_0[14]), .out_15(r5_out_0[15]),
    .out_0(r5_out_0[0]), .out_1(r5_out_0[1]), .out_2(r5_out_0[2]), .out_3(r5_out_0[3]), .out_4(r5_out_0[4]),
    .out_5(r5_out_0[5]), .out_6(r5_out_0[6]), .out_7(r5_out_0[7]), .out_8(r5_out_0[8]), .out_9(r5_out_0[9]),
    .out_10(r5_out_0[10]), .out_11(r5_out_0[11]));
  reg_16b r6 (
    .in_12(data[12]), .in_13(data[13]), .in_14(data[14]), .in_15(data[15]), .in_0(data[0]), .in_1(data[1]),
    .in_2(data[2]), .in_3(data[3]), .in_4(data[4]), .in_5(data[5]), .in_6(data[6]), .in_7(data[7]),
    .in_8(data[8]), .in_9(data[9]), .in_10(data[10]), .in_11(data[11]), .CLK(CLK), .nWE(t74154_1_out_6),
    .out_12(r6_out_0[12]), .out_13(r6_out_0[13]), .out_14(r6_out_0[14]), .out_15(r6_out_0[15]),
    .out_0(r6_out_0[0]), .out_1(r6_out_0[1]), .out_2(r6_out_0[2]), .out_3(r6_out_0[3]), .out_4(r6_out_0[4]),
    .out_5(r6_out_0[5]), .out_6(r6_out_0[6]), .out_7(r6_out_0[7]), .out_8(r6_out_0[8]), .out_9(r6_out_0[9]),
    .out_10(r6_out_0[10]), .out_11(r6_out_0[11]));
  reg_16b r7 (
    .in_12(data[12]), .in_13(data[13]), .in_14(data[14]), .in_15(data[15]), .in_0(data[0]), .in_1(data[1]),
    .in_2(data[2]), .in_3(data[3]), .in_4(data[4]), .in_5(data[5]), .in_6(data[6]), .in_7(data[7]),
    .in_8(data[8]), .in_9(data[9]), .in_10(data[10]), .in_11(data[11]), .CLK(CLK), .nWE(t74154_1_out_7),
    .out_12(r7_out_0[12]), .out_13(r7_out_0[13]), .out_14(r7_out_0[14]), .out_15(r7_out_0[15]),
    .out_0(r7_out_0[0]), .out_1(r7_out_0[1]), .out_2(r7_out_0[2]), .out_3(r7_out_0[3]), .out_4(r7_out_0[4]),
    .out_5(r7_out_0[5]), .out_6(r7_out_0[6]), .out_7(r7_out_0[7]), .out_8(r7_out_0[8]), .out_9(r7_out_0[9]),
    .out_10(r7_out_0[10]), .out_11(r7_out_0[11]));
  reg_16b r8 (
    .in_12(data[12]), .in_13(data[13]), .in_14(data[14]), .in_15(data[15]), .in_0(data[0]), .in_1(data[1]),
    .in_2(data[2]), .in_3(data[3]), .in_4(data[4]), .in_5(data[5]), .in_6(data[6]), .in_7(data[7]),
    .in_8(data[8]), .in_9(data[9]), .in_10(data[10]), .in_11(data[11]), .CLK(CLK), .nWE(t74154_1_out_8),
    .out_12(r8_out_0[12]), .out_13(r8_out_0[13]), .out_14(r8_out_0[14]), .out_15(r8_out_0[15]),
    .out_0(r8_out_0[0]), .out_1(r8_out_0[1]), .out_2(r8_out_0[2]), .out_3(r8_out_0[3]), .out_4(r8_out_0[4]),
    .out_5(r8_out_0[5]), .out_6(r8_out_0[6]), .out_7(r8_out_0[7]), .out_8(r8_out_0[8]), .out_9(r8_out_0[9]),
    .out_10(r8_out_0[10]), .out_11(r8_out_0[11]));
  reg_16b r9 (
    .in_12(data[12]), .in_13(data[13]), .in_14(data[14]), .in_15(data[15]), .in_0(data[0]), .in_1(data[1]),
    .in_2(data[2]), .in_3(data[3]), .in_4(data[4]), .in_5(data[5]), .in_6(data[6]), .in_7(data[7]),
    .in_8(data[8]), .in_9(data[9]), .in_10(data[10]), .in_11(data[11]), .CLK(CLK), .nWE(t74154_1_out_9),
    .out_12(r9_out_0[12]), .out_13(r9_out_0[13]), .out_14(r9_out_0[14]), .out_15(r9_out_0[15]),
    .out_0(r9_out_0[0]), .out_1(r9_out_0[1]), .out_2(r9_out_0[2]), .out_3(r9_out_0[3]), .out_4(r9_out_0[4]),
    .out_5(r9_out_0[5]), .out_6(r9_out_0[6]), .out_7(r9_out_0[7]), .out_8(r9_out_0[8]), .out_9(r9_out_0[9]),
    .out_10(r9_out_0[10]), .out_11(r9_out_0[11]));
  reg_16b r10 (
    .in_12(data[12]), .in_13(data[13]), .in_14(data[14]), .in_15(data[15]), .in_0(data[0]), .in_1(data[1]),
    .in_2(data[2]), .in_3(data[3]), .in_4(data[4]), .in_5(data[5]), .in_6(data[6]), .in_7(data[7]),
    .in_8(data[8]), .in_9(data[9]), .in_10(data[10]), .in_11(data[11]), .CLK(CLK), .nWE(t74154_1_out_10),
    .out_12(r10_out_12), .out_13(r10_out_13), .out_14(r10_out_14), .out_15(r10_out_15), .out_0(r10_out_0),
    .out_1(r10_out_1), .out_2(r10_out_2), .out_3(r10_out_3), .out_4(r10_out_4), .out_5(r10_out_5),
    .out_6(r10_out_6), .out_7(r10_out_7), .out_8(r10_out_8), .out_9(r10_out_9), .out_10(r10_out_10),
    .out_11(r10_out_11));
  reg_16b r11 (
    .in_12(data[12]), .in_13(data[13]), .in_14(data[14]), .in_15(data[15]), .in_0(data[0]), .in_1(data[1]),
    .in_2(data[2]), .in_3(data[3]), .in_4(data[4]), .in_5(data[5]), .in_6(data[6]), .in_7(data[7]),
    .in_8(data[8]), .in_9(data[9]), .in_10(data[10]), .in_11(data[11]), .CLK(CLK), .nWE(t74154_1_out_11),
    .out_12(r11_out_12), .out_13(r11_out_13), .out_14(r11_out_14), .out_15(r11_out_15), .out_0(r11_out_0),
    .out_1(r11_out_1), .out_2(r11_out_2), .out_3(r11_out_3), .out_4(r11_out_4), .out_5(r11_out_5),
    .out_6(r11_out_6), .out_7(r11_out_7), .out_8(r11_out_8), .out_9(r11_out_9), .out_10(r11_out_10),
    .out_11(r11_out_11));
  reg_16b r12 (
    .in_12(data[12]), .in_13(data[13]), .in_14(data[14]), .in_15(data[15]), .in_0(data[0]), .in_1(data[1]),
    .in_2(data[2]), .in_3(data[3]), .in_4(data[4]), .in_5(data[5]), .in_6(data[6]), .in_7(data[7]),
    .in_8(data[8]), .in_9(data[9]), .in_10(data[10]), .in_11(data[11]), .CLK(CLK), .nWE(t74154_1_out_12),
    .out_12(r12_out_12), .out_13(r12_out_13), .out_14(r12_out_14), .out_15(r12_out_15), .out_0(r12_out_0),
    .out_1(r12_out_1), .out_2(r12_out_2), .out_3(r12_out_3), .out_4(r12_out_4), .out_5(r12_out_5),
    .out_6(r12_out_6), .out_7(r12_out_7), .out_8(r12_out_8), .out_9(r12_out_9), .out_10(r12_out_10),
    .out_11(r12_out_11));
  reg_16b r13 (
    .in_12(data[12]), .in_13(data[13]), .in_14(data[14]), .in_15(data[15]), .in_0(data[0]), .in_1(data[1]),
    .in_2(data[2]), .in_3(data[3]), .in_4(data[4]), .in_5(data[5]), .in_6(data[6]), .in_7(data[7]),
    .in_8(data[8]), .in_9(data[9]), .in_10(data[10]), .in_11(data[11]), .CLK(CLK), .nWE(t74154_1_out_13),
    .out_12(r13_out_12), .out_13(r13_out_13), .out_14(r13_out_14), .out_15(r13_out_15), .out_0(r13_out_0),
    .out_1(r13_out_1), .out_2(r13_out_2), .out_3(r13_out_3), .out_4(r13_out_4), .out_5(r13_out_5),
    .out_6(r13_out_6), .out_7(r13_out_7), .out_8(r13_out_8), .out_9(r13_out_9), .out_10(r13_out_10),
    .out_11(r13_out_11));
  reg_16b r14 (
    .in_12(data[12]), .in_13(data[13]), .in_14(data[14]), .in_15(data[15]), .in_0(data[0]), .in_1(data[1]),
    .in_2(data[2]), .in_3(data[3]), .in_4(data[4]), .in_5(data[5]), .in_6(data[6]), .in_7(data[7]),
    .in_8(data[8]), .in_9(data[9]), .in_10(data[10]), .in_11(data[11]), .CLK(CLK), .nWE(t74154_1_out_14),
    .out_12(r14_out_12), .out_13(r14_out_13), .out_14(r14_out_14), .out_15(r14_out_15), .out_0(r14_out_0),
    .out_1(r14_out_1), .out_2(r14_out_2), .out_3(r14_out_3), .out_4(r14_out_4), .out_5(r14_out_5),
    .out_6(r14_out_6), .out_7(r14_out_7), .out_8(r14_out_8), .out_9(r14_out_9), .out_10(r14_out_10),
    .out_11(r14_out_11));
  reg_16b r15 (
    .in_12(data[12]), .in_13(data[13]), .in_14(data[14]), .in_15(data[15]), .in_0(data[0]), .in_1(data[1]),
    .in_2(data[2]), .in_3(data[3]), .in_4(data[4]), .in_5(data[5]), .in_6(data[6]), .in_7(data[7]),
    .in_8(data[8]), .in_9(data[9]), .in_10(data[10]), .in_11(data[11]), .CLK(CLK), .nWE(t74154_1_out_15),
    .out_12(r15_out_12), .out_13(r15_out_13), .out_14(r15_out_14), .out_15(r15_out_15), .out_0(r15_out_0),
    .out_1(r15_out_1), .out_2(r15_out_2), .out_3(r15_out_3), .out_4(r15_out_4), .out_5(r15_out_5),
    .out_6(r15_out_6), .out_7(r15_out_7), .out_8(r15_out_8), .out_9(r15_out_9), .out_10(r15_out_10),
    .out_11(r15_out_11));
  // Probe on r1_out
  // Probe on r2_out_0
  // Probe on r3_out_0
  // Probe on r4_out_0
  // Probe on r5_out_0
  // Probe on r6_out_0
  // Probe on r7_out_0
  // Probe on r8_out_0
  // Probe on r9_out_0
  running_and_8b running_and_8b_1 (
    .in_0(r0_out_0), .in_1(r0_out_1), .in_2(r0_out_2), .in_3(r0_out_3), .in_4(r0_out_4), .in_5(r0_out_5),
    .in_6(r0_out_6), .in_7(r0_out_7), .result(BUSY));
  octal_and octal_and_1 (
    .in_0(r0_out_8), .in_1(r1_out[8]), .in_2(r0_out_9), .in_3(r1_out[9]), .in_4(r0_out_10),
    .in_5(r1_out[10]), .in_6(r0_out_11), .in_7(r1_out[11]), .in_8(r0_out_12), .in_9(r1_out[12]),
    .in_10(r0_out_13), .in_11(r1_out[13]), .in_12(r0_out_14), .in_13(r1_out[14]), .in_14(r0_out_15),
    .in_15(r1_out[15]), .out_0(octal_and_1_out_0), .out_1(octal_and_1_out_1), .out_2(octal_and_1_out_2),
    .out_3(octal_and_1_out_3), .out_4(octal_and_1_out_4), .out_5(octal_and_1_out_5),
    .out_6(octal_and_1_out_6), .out_7(octal_and_1_out_7));
  buf_16b buf_16b_7 (
    .in_8(r0_out_8), .in_9(r0_out_9), .in_10(r0_out_10), .in_11(r0_out_11), .in_12(r0_out_12),
    .in_13(r0_out_13), .in_14(r0_out_14), .in_15(r0_out_15), .in_0(r0_out_0), .in_1(r0_out_1),
    .in_2(r0_out_2), .in_3(r0_out_3), .in_4(r0_out_4), .in_5(r0_out_5), .in_6(r0_out_6), .in_7(r0_out_7),
    .nOE2(t74154_2_out_0), .nOE1(SET), .out_8(REG_OUT[8]), .out_9(REG_OUT[9]), .out_10(REG_OUT[10]),
    .out_11(REG_OUT[11]), .out_12(REG_OUT[12]), .out_13(REG_OUT[13]), .out_14(REG_OUT[14]),
    .out_15(REG_OUT[15]), .out_0(REG_OUT[0]), .out_1(REG_OUT[1]), .out_2(REG_OUT[2]), .out_3(REG_OUT[3]),
    .out_4(REG_OUT[4]), .out_5(REG_OUT[5]), .out_6(REG_OUT[6]), .out_7(REG_OUT[7]));
  buf_16b buf_16b_8 (
    .in_8(r1_out[8]), .in_9(r1_out[9]), .in_10(r1_out[10]), .in_11(r1_out[11]), .in_12(r1_out[12]),
    .in_13(r1_out[13]), .in_14(r1_out[14]), .in_15(r1_out[15]), .in_0(r1_out[0]), .in_1(r1_out[1]),
    .in_2(r1_out[2]), .in_3(r1_out[3]), .in_4(r1_out[4]), .in_5(r1_out[5]), .in_6(r1_out[6]),
    .in_7(r1_out[7]), .nOE2(t74154_2_out_1), .nOE1(SET), .out_8(REG_OUT[8]), .out_9(REG_OUT[9]),
    .out_10(REG_OUT[10]), .out_11(REG_OUT[11]), .out_12(REG_OUT[12]), .out_13(REG_OUT[13]),
    .out_14(REG_OUT[14]), .out_15(REG_OUT[15]), .out_0(REG_OUT[0]), .out_1(REG_OUT[1]), .out_2(REG_OUT[2]),
    .out_3(REG_OUT[3]), .out_4(REG_OUT[4]), .out_5(REG_OUT[5]), .out_6(REG_OUT[6]), .out_7(REG_OUT[7]));
  buf_16b buf_16b_9 (
    .in_8(r2_out_0[8]), .in_9(r2_out_0[9]), .in_10(r2_out_0[10]), .in_11(r2_out_0[11]), .in_12(r2_out_0[12]),
    .in_13(r2_out_0[13]), .in_14(r2_out_0[14]), .in_15(r2_out_0[15]), .in_0(r2_out_0[0]), .in_1(r2_out_0[1]),
    .in_2(r2_out_0[2]), .in_3(r2_out_0[3]), .in_4(r2_out_0[4]), .in_5(r2_out_0[5]), .in_6(r2_out_0[6]),
    .in_7(r2_out_0[7]), .nOE2(t74154_2_out_2), .nOE1(SET), .out_8(REG_OUT[8]), .out_9(REG_OUT[9]),
    .out_10(REG_OUT[10]), .out_11(REG_OUT[11]), .out_12(REG_OUT[12]), .out_13(REG_OUT[13]),
    .out_14(REG_OUT[14]), .out_15(REG_OUT[15]), .out_0(REG_OUT[0]), .out_1(REG_OUT[1]), .out_2(REG_OUT[2]),
    .out_3(REG_OUT[3]), .out_4(REG_OUT[4]), .out_5(REG_OUT[5]), .out_6(REG_OUT[6]), .out_7(REG_OUT[7]));
  buf_16b buf_16b_10 (
    .in_8(r3_out_0[8]), .in_9(r3_out_0[9]), .in_10(r3_out_0[10]), .in_11(r3_out_0[11]), .in_12(r3_out_0[12]),
    .in_13(r3_out_0[13]), .in_14(r3_out_0[14]), .in_15(r3_out_0[15]), .in_0(r3_out_0[0]), .in_1(r3_out_0[1]),
    .in_2(r3_out_0[2]), .in_3(r3_out_0[3]), .in_4(r3_out_0[4]), .in_5(r3_out_0[5]), .in_6(r3_out_0[6]),
    .in_7(r3_out_0[7]), .nOE2(t74154_2_out_3), .nOE1(SET), .out_8(REG_OUT[8]), .out_9(REG_OUT[9]),
    .out_10(REG_OUT[10]), .out_11(REG_OUT[11]), .out_12(REG_OUT[12]), .out_13(REG_OUT[13]),
    .out_14(REG_OUT[14]), .out_15(REG_OUT[15]), .out_0(REG_OUT[0]), .out_1(REG_OUT[1]), .out_2(REG_OUT[2]),
    .out_3(REG_OUT[3]), .out_4(REG_OUT[4]), .out_5(REG_OUT[5]), .out_6(REG_OUT[6]), .out_7(REG_OUT[7]));
  buf_16b buf_16b_11 (
    .in_8(r4_out_0[8]), .in_9(r4_out_0[9]), .in_10(r4_out_0[10]), .in_11(r4_out_0[11]), .in_12(r4_out_0[12]),
    .in_13(r4_out_0[13]), .in_14(r4_out_0[14]), .in_15(r4_out_0[15]), .in_0(r4_out_0[0]), .in_1(r4_out_0[1]),
    .in_2(r4_out_0[2]), .in_3(r4_out_0[3]), .in_4(r4_out_0[4]), .in_5(r4_out_0[5]), .in_6(r4_out_0[6]),
    .in_7(r4_out_0[7]), .nOE2(t74154_2_out_4), .nOE1(SET), .out_8(REG_OUT[8]), .out_9(REG_OUT[9]),
    .out_10(REG_OUT[10]), .out_11(REG_OUT[11]), .out_12(REG_OUT[12]), .out_13(REG_OUT[13]),
    .out_14(REG_OUT[14]), .out_15(REG_OUT[15]), .out_0(REG_OUT[0]), .out_1(REG_OUT[1]), .out_2(REG_OUT[2]),
    .out_3(REG_OUT[3]), .out_4(REG_OUT[4]), .out_5(REG_OUT[5]), .out_6(REG_OUT[6]), .out_7(REG_OUT[7]));
  buf_16b buf_16b_12 (
    .in_8(r5_out_0[8]), .in_9(r5_out_0[9]), .in_10(r5_out_0[10]), .in_11(r5_out_0[11]), .in_12(r5_out_0[12]),
    .in_13(r5_out_0[13]), .in_14(r5_out_0[14]), .in_15(r5_out_0[15]), .in_0(r5_out_0[0]), .in_1(r5_out_0[1]),
    .in_2(r5_out_0[2]), .in_3(r5_out_0[3]), .in_4(r5_out_0[4]), .in_5(r5_out_0[5]), .in_6(r5_out_0[6]),
    .in_7(r5_out_0[7]), .nOE2(t74154_2_out_5), .nOE1(SET), .out_8(REG_OUT[8]), .out_9(REG_OUT[9]),
    .out_10(REG_OUT[10]), .out_11(REG_OUT[11]), .out_12(REG_OUT[12]), .out_13(REG_OUT[13]),
    .out_14(REG_OUT[14]), .out_15(REG_OUT[15]), .out_0(REG_OUT[0]), .out_1(REG_OUT[1]), .out_2(REG_OUT[2]),
    .out_3(REG_OUT[3]), .out_4(REG_OUT[4]), .out_5(REG_OUT[5]), .out_6(REG_OUT[6]), .out_7(REG_OUT[7]));
  buf_16b buf_16b_13 (
    .in_8(r6_out_0[8]), .in_9(r6_out_0[9]), .in_10(r6_out_0[10]), .in_11(r6_out_0[11]), .in_12(r6_out_0[12]),
    .in_13(r6_out_0[13]), .in_14(r6_out_0[14]), .in_15(r6_out_0[15]), .in_0(r6_out_0[0]), .in_1(r6_out_0[1]),
    .in_2(r6_out_0[2]), .in_3(r6_out_0[3]), .in_4(r6_out_0[4]), .in_5(r6_out_0[5]), .in_6(r6_out_0[6]),
    .in_7(r6_out_0[7]), .nOE2(t74154_2_out_6), .nOE1(SET), .out_8(REG_OUT[8]), .out_9(REG_OUT[9]),
    .out_10(REG_OUT[10]), .out_11(REG_OUT[11]), .out_12(REG_OUT[12]), .out_13(REG_OUT[13]),
    .out_14(REG_OUT[14]), .out_15(REG_OUT[15]), .out_0(REG_OUT[0]), .out_1(REG_OUT[1]), .out_2(REG_OUT[2]),
    .out_3(REG_OUT[3]), .out_4(REG_OUT[4]), .out_5(REG_OUT[5]), .out_6(REG_OUT[6]), .out_7(REG_OUT[7]));
  buf_16b buf_16b_14 (
    .in_8(r7_out_0[8]), .in_9(r7_out_0[9]), .in_10(r7_out_0[10]), .in_11(r7_out_0[11]), .in_12(r7_out_0[12]),
    .in_13(r7_out_0[13]), .in_14(r7_out_0[14]), .in_15(r7_out_0[15]), .in_0(r7_out_0[0]), .in_1(r7_out_0[1]),
    .in_2(r7_out_0[2]), .in_3(r7_out_0[3]), .in_4(r7_out_0[4]), .in_5(r7_out_0[5]), .in_6(r7_out_0[6]),
    .in_7(r7_out_0[7]), .nOE2(t74154_2_out_7), .nOE1(SET), .out_8(REG_OUT[8]), .out_9(REG_OUT[9]),
    .out_10(REG_OUT[10]), .out_11(REG_OUT[11]), .out_12(REG_OUT[12]), .out_13(REG_OUT[13]),
    .out_14(REG_OUT[14]), .out_15(REG_OUT[15]), .out_0(REG_OUT[0]), .out_1(REG_OUT[1]), .out_2(REG_OUT[2]),
    .out_3(REG_OUT[3]), .out_4(REG_OUT[4]), .out_5(REG_OUT[5]), .out_6(REG_OUT[6]), .out_7(REG_OUT[7]));
  buf_16b buf_16b_15 (
    .in_8(r8_out_0[8]), .in_9(r8_out_0[9]), .in_10(r8_out_0[10]), .in_11(r8_out_0[11]), .in_12(r8_out_0[12]),
    .in_13(r8_out_0[13]), .in_14(r8_out_0[14]), .in_15(r8_out_0[15]), .in_0(r8_out_0[0]), .in_1(r8_out_0[1]),
    .in_2(r8_out_0[2]), .in_3(r8_out_0[3]), .in_4(r8_out_0[4]), .in_5(r8_out_0[5]), .in_6(r8_out_0[6]),
    .in_7(r8_out_0[7]), .nOE2(t74154_2_out_8), .nOE1(SET), .out_8(REG_OUT[8]), .out_9(REG_OUT[9]),
    .out_10(REG_OUT[10]), .out_11(REG_OUT[11]), .out_12(REG_OUT[12]), .out_13(REG_OUT[13]),
    .out_14(REG_OUT[14]), .out_15(REG_OUT[15]), .out_0(REG_OUT[0]), .out_1(REG_OUT[1]), .out_2(REG_OUT[2]),
    .out_3(REG_OUT[3]), .out_4(REG_OUT[4]), .out_5(REG_OUT[5]), .out_6(REG_OUT[6]), .out_7(REG_OUT[7]));
  buf_16b buf_16b_16 (
    .in_8(r9_out_0[8]), .in_9(r9_out_0[9]), .in_10(r9_out_0[10]), .in_11(r9_out_0[11]), .in_12(r9_out_0[12]),
    .in_13(r9_out_0[13]), .in_14(r9_out_0[14]), .in_15(r9_out_0[15]), .in_0(r9_out_0[0]), .in_1(r9_out_0[1]),
    .in_2(r9_out_0[2]), .in_3(r9_out_0[3]), .in_4(r9_out_0[4]), .in_5(r9_out_0[5]), .in_6(r9_out_0[6]),
    .in_7(r9_out_0[7]), .nOE2(t74154_2_out_9), .nOE1(SET), .out_8(REG_OUT[8]), .out_9(REG_OUT[9]),
    .out_10(REG_OUT[10]), .out_11(REG_OUT[11]), .out_12(REG_OUT[12]), .out_13(REG_OUT[13]),
    .out_14(REG_OUT[14]), .out_15(REG_OUT[15]), .out_0(REG_OUT[0]), .out_1(REG_OUT[1]), .out_2(REG_OUT[2]),
    .out_3(REG_OUT[3]), .out_4(REG_OUT[4]), .out_5(REG_OUT[5]), .out_6(REG_OUT[6]), .out_7(REG_OUT[7]));
  buf_16b buf_16b_17 (
    .in_8(r10_out_8), .in_9(r10_out_9), .in_10(r10_out_10), .in_11(r10_out_11), .in_12(r10_out_12),
    .in_13(r10_out_13), .in_14(r10_out_14), .in_15(r10_out_15), .in_0(r10_out_0), .in_1(r10_out_1),
    .in_2(r10_out_2), .in_3(r10_out_3), .in_4(r10_out_4), .in_5(r10_out_5), .in_6(r10_out_6),
    .in_7(r10_out_7), .nOE2(t74154_2_out_10), .nOE1(SET), .out_8(REG_OUT[8]), .out_9(REG_OUT[9]),
    .out_10(REG_OUT[10]), .out_11(REG_OUT[11]), .out_12(REG_OUT[12]), .out_13(REG_OUT[13]),
    .out_14(REG_OUT[14]), .out_15(REG_OUT[15]), .out_0(REG_OUT[0]), .out_1(REG_OUT[1]), .out_2(REG_OUT[2]),
    .out_3(REG_OUT[3]), .out_4(REG_OUT[4]), .out_5(REG_OUT[5]), .out_6(REG_OUT[6]), .out_7(REG_OUT[7]));
  buf_16b buf_16b_18 (
    .in_8(r11_out_8), .in_9(r11_out_9), .in_10(r11_out_10), .in_11(r11_out_11), .in_12(r11_out_12),
    .in_13(r11_out_13), .in_14(r11_out_14), .in_15(r11_out_15), .in_0(r11_out_0), .in_1(r11_out_1),
    .in_2(r11_out_2), .in_3(r11_out_3), .in_4(r11_out_4), .in_5(r11_out_5), .in_6(r11_out_6),
    .in_7(r11_out_7), .nOE2(t74154_2_out_11), .nOE1(SET), .out_8(REG_OUT[8]), .out_9(REG_OUT[9]),
    .out_10(REG_OUT[10]), .out_11(REG_OUT[11]), .out_12(REG_OUT[12]), .out_13(REG_OUT[13]),
    .out_14(REG_OUT[14]), .out_15(REG_OUT[15]), .out_0(REG_OUT[0]), .out_1(REG_OUT[1]), .out_2(REG_OUT[2]),
    .out_3(REG_OUT[3]), .out_4(REG_OUT[4]), .out_5(REG_OUT[5]), .out_6(REG_OUT[6]), .out_7(REG_OUT[7]));
  buf_16b buf_16b_19 (
    .in_8(r12_out_8), .in_9(r12_out_9), .in_10(r12_out_10), .in_11(r12_out_11), .in_12(r12_out_12),
    .in_13(r12_out_13), .in_14(r12_out_14), .in_15(r12_out_15), .in_0(r12_out_0), .in_1(r12_out_1),
    .in_2(r12_out_2), .in_3(r12_out_3), .in_4(r12_out_4), .in_5(r12_out_5), .in_6(r12_out_6),
    .in_7(r12_out_7), .nOE2(t74154_2_out_12), .nOE1(SET), .out_8(REG_OUT[8]), .out_9(REG_OUT[9]),
    .out_10(REG_OUT[10]), .out_11(REG_OUT[11]), .out_12(REG_OUT[12]), .out_13(REG_OUT[13]),
    .out_14(REG_OUT[14]), .out_15(REG_OUT[15]), .out_0(REG_OUT[0]), .out_1(REG_OUT[1]), .out_2(REG_OUT[2]),
    .out_3(REG_OUT[3]), .out_4(REG_OUT[4]), .out_5(REG_OUT[5]), .out_6(REG_OUT[6]), .out_7(REG_OUT[7]));
  buf_16b buf_16b_20 (
    .in_8(r13_out_8), .in_9(r13_out_9), .in_10(r13_out_10), .in_11(r13_out_11), .in_12(r13_out_12),
    .in_13(r13_out_13), .in_14(r13_out_14), .in_15(r13_out_15), .in_0(r13_out_0), .in_1(r13_out_1),
    .in_2(r13_out_2), .in_3(r13_out_3), .in_4(r13_out_4), .in_5(r13_out_5), .in_6(r13_out_6),
    .in_7(r13_out_7), .nOE2(t74154_2_out_13), .nOE1(SET), .out_8(REG_OUT[8]), .out_9(REG_OUT[9]),
    .out_10(REG_OUT[10]), .out_11(REG_OUT[11]), .out_12(REG_OUT[12]), .out_13(REG_OUT[13]),
    .out_14(REG_OUT[14]), .out_15(REG_OUT[15]), .out_0(REG_OUT[0]), .out_1(REG_OUT[1]), .out_2(REG_OUT[2]),
    .out_3(REG_OUT[3]), .out_4(REG_OUT[4]), .out_5(REG_OUT[5]), .out_6(REG_OUT[6]), .out_7(REG_OUT[7]));
  buf_16b buf_16b_21 (
    .in_8(r14_out_8), .in_9(r14_out_9), .in_10(r14_out_10), .in_11(r14_out_11), .in_12(r14_out_12),
    .in_13(r14_out_13), .in_14(r14_out_14), .in_15(r14_out_15), .in_0(r14_out_0), .in_1(r14_out_1),
    .in_2(r14_out_2), .in_3(r14_out_3), .in_4(r14_out_4), .in_5(r14_out_5), .in_6(r14_out_6),
    .in_7(r14_out_7), .nOE2(t74154_2_out_14), .nOE1(SET), .out_8(REG_OUT[8]), .out_9(REG_OUT[9]),
    .out_10(REG_OUT[10]), .out_11(REG_OUT[11]), .out_12(REG_OUT[12]), .out_13(REG_OUT[13]),
    .out_14(REG_OUT[14]), .out_15(REG_OUT[15]), .out_0(REG_OUT[0]), .out_1(REG_OUT[1]), .out_2(REG_OUT[2]),
    .out_3(REG_OUT[3]), .out_4(REG_OUT[4]), .out_5(REG_OUT[5]), .out_6(REG_OUT[6]), .out_7(REG_OUT[7]));
  buf_16b buf_16b_22 (
    .in_8(r15_out_8), .in_9(r15_out_9), .in_10(r15_out_10), .in_11(r15_out_11), .in_12(r15_out_12),
    .in_13(r15_out_13), .in_14(r15_out_14), .in_15(r15_out_15), .in_0(r15_out_0), .in_1(r15_out_1),
    .in_2(r15_out_2), .in_3(r15_out_3), .in_4(r15_out_4), .in_5(r15_out_5), .in_6(r15_out_6),
    .in_7(r15_out_7), .nOE2(t74154_2_out_15), .nOE1(SET), .out_8(REG_OUT[8]), .out_9(REG_OUT[9]),
    .out_10(REG_OUT[10]), .out_11(REG_OUT[11]), .out_12(REG_OUT[12]), .out_13(REG_OUT[13]),
    .out_14(REG_OUT[14]), .out_15(REG_OUT[15]), .out_0(REG_OUT[0]), .out_1(REG_OUT[1]), .out_2(REG_OUT[2]),
    .out_3(REG_OUT[3]), .out_4(REG_OUT[4]), .out_5(REG_OUT[5]), .out_6(REG_OUT[6]), .out_7(REG_OUT[7]));
  _7404 u_7404_2 (
    .pin1(octal_and_1_out_3), .pin2(n7404_2_pin2), .pin3(octal_and_1_out_4), .pin4(n7404_2_pin4),
    .pin5(octal_and_1_out_5), .pin6(n7404_2_pin6), .pin13(octal_and_1_out_0), .pin12(n7404_2_pin12),
    .pin11(octal_and_1_out_1), .pin10(n7404_2_pin10), .pin9(octal_and_1_out_2), .pin8(n7404_2_pin8));
  _7404 u_7404_3 (
    .pin13(octal_and_1_out_6), .pin12(n7404_3_pin12), .pin11(octal_and_1_out_7), .pin10(n7404_3_pin10));  // open: pin1, pin2, pin3, pin4, pin5, pin6, pin9, pin8
  T74154 t74154_2 (
    .A(REG_SEL[0]), .B(REG_SEL[1]), .C(REG_SEL[2]), .D(REG_SEL[3]), .G1(1'b0), .G2(1'b0),
    .out_0(t74154_2_out_0), .out_1(t74154_2_out_1), .out_2(t74154_2_out_2), .out_3(t74154_2_out_3),
    .out_4(t74154_2_out_4), .out_5(t74154_2_out_5), .out_6(t74154_2_out_6), .out_7(t74154_2_out_7),
    .out_8(t74154_2_out_8), .out_9(t74154_2_out_9), .out_10(t74154_2_out_10), .out_11(t74154_2_out_11),
    .out_12(t74154_2_out_12), .out_13(t74154_2_out_13), .out_14(t74154_2_out_14), .out_15(t74154_2_out_15));
  T74148 t74148_1 (
    .in_0(n7404_2_pin12), .in_1(n7404_2_pin10), .in_2(n7404_2_pin8), .in_3(n7404_2_pin2),
    .in_4(n7404_2_pin4), .in_5(n7404_2_pin6), .in_6(n7404_3_pin12), .in_7(n7404_3_pin10), .EI(1'b0),
    .A0(INT_ID[0]), .A1(INT_ID[1]), .A2(INT_ID[2]), .GS(t74148_1_gs));  // open: EO
  _7404 u_7404_4 (
    .pin1(t74148_1_gs), .pin2(INT));  // open: pin3, pin4, pin5, pin6, pin13, pin12, pin11, pin10, pin9, pin8

  // Other names for the same wires on the sheet: write_enable = SET
endmodule

module reg_16b (
  input  in_0,
  input  CLK,
  input  in_1,
  input  in_2,
  input  in_3,
  input  in_4,
  input  in_5,
  input  in_6,
  input  nWE,
  input  in_7,
  input  in_8,
  input  in_9,
  input  in_10,
  input  in_11,
  input  in_12,
  input  in_13,
  input  in_14,
  input  in_15,
  output out_0,
  output out_1,
  output out_2,
  output out_3,
  output out_4,
  output out_5,
  output out_6,
  output out_7,
  output out_8,
  output out_9,
  output out_10,
  output out_11,
  output out_12,
  output out_13,
  output out_14,
  output out_15
);

  _74377 u_74377_1 (
    .pin1(nWE), .pin2(out_4), .pin3(in_4), .pin4(in_5), .pin5(out_5), .pin6(out_6), .pin7(in_6), .pin8(in_7),
    .pin9(out_7), .pin19(out_0), .pin18(in_0), .pin17(in_1), .pin16(out_1), .pin15(out_2), .pin14(in_2),
    .pin13(in_3), .pin12(out_3), .pin11(CLK));
  _74377 u_74377_2 (
    .pin1(nWE), .pin2(out_12), .pin3(in_12), .pin4(in_13), .pin5(out_13), .pin6(out_14), .pin7(in_14),
    .pin8(in_15), .pin9(out_15), .pin19(out_8), .pin18(in_8), .pin17(in_9), .pin16(out_9), .pin15(out_10),
    .pin14(in_10), .pin13(in_11), .pin12(out_11), .pin11(CLK));
endmodule

module buf_16b (
  input  in_0,
  input  in_1,
  input  in_2,
  input  in_3,
  input  in_4,
  input  in_5,
  input  in_6,
  input  in_7,
  input  nOE2,
  input  nOE1,
  input  in_8,
  input  in_9,
  input  in_10,
  input  in_11,
  input  in_12,
  input  in_13,
  input  in_14,
  input  in_15,
  output out_0,
  output out_1,
  output out_2,
  output out_3,
  output out_4,
  output out_5,
  output out_6,
  output out_7,
  output out_8,
  output out_9,
  output out_10,
  output out_11,
  output out_12,
  output out_13,
  output out_14,
  output out_15
);

  _74541 u_74541_1 (
    .pin1(nOE1), .pin2(in_0), .pin3(in_1), .pin4(in_2), .pin5(in_3), .pin6(in_4), .pin7(in_5), .pin8(in_6),
    .pin9(in_7), .pin19(nOE2), .pin18(out_0), .pin17(out_1), .pin16(out_2), .pin15(out_3), .pin14(out_4),
    .pin13(out_5), .pin12(out_6), .pin11(out_7));
  _74541 u_74541_2 (
    .pin1(nOE1), .pin2(in_8), .pin3(in_9), .pin4(in_10), .pin5(in_11), .pin6(in_12), .pin7(in_13),
    .pin8(in_14), .pin9(in_15), .pin19(nOE2), .pin18(out_8), .pin17(out_9), .pin16(out_10), .pin15(out_11),
    .pin14(out_12), .pin13(out_13), .pin12(out_14), .pin11(out_15));
endmodule

module running_and_8b (
  input  in_0,
  input  in_1,
  input  in_2,
  input  in_3,
  input  in_4,
  input  in_5,
  input  in_6,
  input  in_7,
  output result
);

  wire n7408_1_pin3, n7408_1_pin6, n7408_1_pin8, n7408_1_pin11, n7408_2_pin3, n7408_2_pin11;

  _7408 u_7408_1 (
    .pin1(in_4), .pin2(in_5), .pin3(n7408_1_pin3), .pin4(in_6), .pin5(in_7), .pin6(n7408_1_pin6),
    .pin13(in_0), .pin12(in_1), .pin11(n7408_1_pin11), .pin10(in_2), .pin9(in_3), .pin8(n7408_1_pin8));
  _7408 u_7408_2 (
    .pin1(n7408_1_pin3), .pin2(n7408_1_pin6), .pin3(n7408_2_pin3), .pin13(n7408_1_pin11),
    .pin12(n7408_1_pin8), .pin11(n7408_2_pin11), .pin10(n7408_2_pin11), .pin9(n7408_2_pin3), .pin8(result));  // open: pin4, pin5, pin6
endmodule

module octal_and (
  input  in_0,
  input  in_1,
  input  in_2,
  input  in_3,
  input  in_4,
  input  in_5,
  input  in_6,
  input  in_7,
  input  in_8,
  input  in_9,
  input  in_10,
  input  in_11,
  input  in_12,
  input  in_13,
  input  in_14,
  input  in_15,
  output out_0,
  output out_1,
  output out_2,
  output out_3,
  output out_4,
  output out_5,
  output out_6,
  output out_7
);

  _7408 u_7408_1 (
    .pin1(in_4), .pin2(in_5), .pin3(out_2), .pin4(in_6), .pin5(in_7), .pin6(out_3), .pin13(in_0),
    .pin12(in_1), .pin11(out_0), .pin10(in_2), .pin9(in_3), .pin8(out_1));
  _7408 u_7408_2 (
    .pin1(in_12), .pin2(in_13), .pin3(out_6), .pin4(in_14), .pin5(in_15), .pin6(out_7), .pin13(in_8),
    .pin12(in_9), .pin11(out_4), .pin10(in_10), .pin9(in_11), .pin8(out_5));
endmodule

module T74148 (
  input  in_0,
  input  in_1,
  input  in_2,
  input  in_3,
  input  in_4,
  input  in_5,
  input  in_6,
  input  in_7,
  input  EI,
  output EO,
  output A0,
  output A1,
  output A2,
  output GS
);

  wire not_2_out, not_3_out, not_4_out, not_5_out, not_7_out, not_9_out, not_10_out, not_11_out, not_12_out,
       priority_encoder_1_en_out, priority_encoder_1_gs;
  wire [2:0] not_6_out, priority_encoder_1_out;

  not not_1 (EO, priority_encoder_1_en_out);
  not not_2 (not_2_out, in_0);
  not not_3 (not_3_out, in_1);
  not not_4 (not_4_out, in_2);
  not not_5 (not_5_out, in_3);
  assign not_6_out = ~priority_encoder_1_out;  // NOT_Gate not_6, 3 bits wide
  Priority_Encoder priority_encoder_1 (
    .in0(not_2_out), .in1(not_3_out), .in2(not_4_out), .in3(not_5_out), .in4(not_7_out), .in5(not_9_out),
    .in6(not_10_out), .in7(not_11_out), .out(priority_encoder_1_out), .en_in(not_12_out),
    .gs(priority_encoder_1_gs), .en_out(priority_encoder_1_en_out));
  not not_7 (not_7_out, in_4);
  not not_8 (GS, priority_encoder_1_gs);
  not not_9 (not_9_out, in_5);
  not not_10 (not_10_out, in_6);
  not not_11 (not_11_out, in_7);
  not not_12 (not_12_out, EI);
  // Transmission_Gate #(.width(3)) transmission_1: pin names not known; wires that end beside it: not_6_out, GS, EO, {A2, A1, A0}
endmodule

module T74154 (
  input  A,
  input  B,
  input  C,
  input  D,
  input  G1,
  input  G2,
  output out_0,
  output out_1,
  output out_2,
  output out_3,
  output out_4,
  output out_5,
  output out_6,
  output out_7,
  output out_8,
  output out_9,
  output out_10,
  output out_11,
  output out_12,
  output out_13,
  output out_14,
  output out_15
);

  wire demultiplexer_1_out0, demultiplexer_1_out1, demultiplexer_1_out2, demultiplexer_1_out3,
       demultiplexer_1_out4, demultiplexer_1_out5, demultiplexer_1_out6, demultiplexer_1_out7,
       demultiplexer_1_out8, demultiplexer_1_out9, demultiplexer_1_out10, demultiplexer_1_out11,
       demultiplexer_1_out12, demultiplexer_1_out13, demultiplexer_1_out14, demultiplexer_1_out15, nor_1_out;

  nor nor_1 (nor_1_out, G1, G2);
  not not_1 (out_0, demultiplexer_1_out0);
  not not_2 (out_1, demultiplexer_1_out1);
  not not_3 (out_2, demultiplexer_1_out2);
  not not_4 (out_3, demultiplexer_1_out3);
  not not_5 (out_4, demultiplexer_1_out4);
  not not_6 (out_5, demultiplexer_1_out5);
  not not_7 (out_6, demultiplexer_1_out6);
  not not_8 (out_7, demultiplexer_1_out7);
  not not_9 (out_8, demultiplexer_1_out8);
  Demultiplexer #(.enable("true"), .select(4)) demultiplexer_1 (
    .out0(demultiplexer_1_out0), .out1(demultiplexer_1_out1), .out2(demultiplexer_1_out2),
    .out3(demultiplexer_1_out3), .out4(demultiplexer_1_out4), .out5(demultiplexer_1_out5),
    .out6(demultiplexer_1_out6), .out7(demultiplexer_1_out7), .out8(demultiplexer_1_out8),
    .out9(demultiplexer_1_out9), .out10(demultiplexer_1_out10), .out11(demultiplexer_1_out11),
    .out12(demultiplexer_1_out12), .out13(demultiplexer_1_out13), .out14(demultiplexer_1_out14),
    .out15(demultiplexer_1_out15), .in(1'b1), .sel({D, C, B, A}), .en(nor_1_out));
  not not_10 (out_9, demultiplexer_1_out9);
  not not_11 (out_10, demultiplexer_1_out10);
  not not_12 (out_11, demultiplexer_1_out11);
  not not_13 (out_12, demultiplexer_1_out12);
  not not_14 (out_13, demultiplexer_1_out13);
  not not_15 (out_14, demultiplexer_1_out14);
  not not_16 (out_15, demultiplexer_1_out15);
endmodule
