// Logisim project master.circ as structural Verilog: 7 circuits, main circuit main
module main (
);

  wire alu_1_fc, alu_1_fo, alu_1_fs, alu_1_fz, button_1_out, CLK, clock_1_out, clock_2_out,
       control_1_mask_restore, control_1_mask_save, control_1_oregwe, io_1_ogpu_clear, io_1_okeyread,
       keyboard_1_avail, registerfile_1_busy, registerfile_1_int, rgb_video_1_p3, s_r_ff_1_q, STOP;
  wire [1:0] GPU_IO_WE;
  wire [2:0] control_1_oioaddr, control_1_omemop, registerfile_1_int_id;
  wire [3:0] control_1_oaluop, control_1_oregid;
  wire [6:0] keyboard_1_data;
  wire [7:0] io_1_obusyassert, io_1_ointasssert, memory_controller_1_gpu_data, rgb_video_1_p4,
       rgb_video_1_p5, rgb_video_1_p6;
  wire [9:8] gpu_1_debug_x, gpu_1_debug_y;
  wire [14:0] memory_controller_1_gpu_addr;
  wire [15:0] control_1_oalubus, control_1_oregbus, GPU_IO, GPU_IO_ADDR, io_1_oled;
  wire [15:8] memory_controller_1_gpu_data_2;

  Clock clock_1 (.out(clock_1_out));
  // RGB_Video #(.cursor("No Cursor"), .height(256), .scale(1), .width(256)) rgb_video_1: pin names not known; wires that end beside it: 1'b0, clock_1_out, rgb_video_1_p3, rgb_video_1_p4, rgb_video_1_p5, rgb_video_1_p6
  GPU gpu_1 (
    .addr(memory_controller_1_gpu_addr), .data(memory_controller_1_gpu_data), .IOWE(GPU_IO_WE),
    .datawe(STOP), .p_clk(CLK), .clk(CLK), .IO_ADDR(GPU_IO_ADDR), .IOi(GPU_IO), .IOo(GPU_IO),
    .DEBUG_x({gpu_1_debug_x, rgb_video_1_p4}), .DEBUG_y({gpu_1_debug_y, rgb_video_1_p5}),
    .DEBUG_WE(rgb_video_1_p3), .color8(rgb_video_1_p6));  // open: HSYNC, VSYNC
  // Probe on memory_controller_1_gpu_addr
  // Probe on {memory_controller_1_gpu_data_2, memory_controller_1_gpu_data}
  Clock clock_2 (.out(clock_2_out));
  TTY tty_1 (.data(memory_controller_1_gpu_data[6:0]), .clk(CLK), .we(STOP), .clr(io_1_ogpu_clear));
  Clock clock_3 (.out(CLK));
  S_R_Flip_Flop s_r_ff_1 (.S(STOP), .clk(clock_2_out), .R(button_1_out), .Q(s_r_ff_1_q));  // open: Qn, preset, reset
  Button button_1 (.out(button_1_out));
  memory_controller memory_controller_1 (
    .MODE(control_1_omemop), .DataBUSin(GPU_IO_ADDR), .CLK(CLK), .GPU_ADDR(memory_controller_1_gpu_addr),
    .GPU_DATA({memory_controller_1_gpu_data_2, memory_controller_1_gpu_data}), .GPU_WE(STOP),
    .DataBUSout(GPU_IO_ADDR));
  control control_1 (
    .ialubus(control_1_oalubus), .ifs(alu_1_fs), .ifo(alu_1_fo), .ifc(alu_1_fc), .ifz(alu_1_fz),
    .imembus(GPU_IO_ADDR), .iregbus(control_1_oregbus), .iint(registerfile_1_int),
    .iintid(registerfile_1_int_id), .ibusy(registerfile_1_busy), .iiobus(GPU_IO), .CLK(CLK),
    .oregwe(control_1_oregwe), .omemop(control_1_omemop), .oioaddr(control_1_oioaddr),
    .oaluop(control_1_oaluop), .oalubus(control_1_oalubus), .omembus(GPU_IO_ADDR),
    .oregbus(control_1_oregbus), .oregid(control_1_oregid), .mask_save(control_1_mask_save),
    .mask_restore(control_1_mask_restore), .oioop(GPU_IO_WE), .oiobus(GPU_IO));
  alu alu_1 (
    .op(control_1_oaluop), .busin(control_1_oalubus), .clk(CLK), .busout(control_1_oalubus), .FC(alu_1_fc),
    .FS(alu_1_fs), .FZ(alu_1_fz), .FO(alu_1_fo));
  IO io_1 (
    .ikeychar(keyboard_1_data), .ikeyaval(keyboard_1_avail), .CLK(CLK), .iioid(control_1_oioaddr),
    .iiocmd(GPU_IO_WE), .iiobus(GPU_IO), .obusyassert(io_1_obusyassert), .ogpu_clear(io_1_ogpu_clear),
    .okeyread(io_1_okeyread), .oled(io_1_oled), .oiobus(GPU_IO), .ointasssert(io_1_ointasssert));
  Keyboard keyboard_1 (.clk(CLK), .re(io_1_okeyread), .clr(1'b0), .avail(keyboard_1_avail), .data(keyboard_1_data));
  registerfile registerfile_1 (
    .regid(control_1_oregid), .mask_restore(control_1_mask_restore), .CLK(CLK), .wr_enable(control_1_oregwe),
    .mask_save(control_1_mask_save), .data_in(control_1_oregbus), .ioint(io_1_ointasssert),
    .iobusy(io_1_obusyassert), .INT_ID(registerfile_1_int_id), .INT(registerfile_1_int),
    .BUSY(registerfile_1_busy), .data_out(control_1_oregbus));
  // LedBar #(.inputtype("row"), .matrixcols(16)) ledbar_1: pin names not known; wires that end beside it: io_1_oled
endmodule

module memory_controller (
  input  [15:0] DataBUSin,
  input  [2:0] MODE,
  input  CLK,
  output [14:0] GPU_ADDR,
  output [15:0] GPU_DATA,
  output GPU_WE,
  output [15:0] DataBUSout
);

  wire and_3_out, not_1_out, output_enable, write_enable;
  wire [15:0] adder_1_out, general_purpose_memory_dout, multiplexer_1_out, multiplexer_2_out, rom_1_data;
  wire [15:15] RegAddr_q;

  not not_1 (not_1_out, output_enable);
  assign GPU_DATA = not_1_out ? DataBUSin : 16'bz;  // Controlled_Buffer controlled_buffer_1
  and and_1 (write_enable, MODE[2], ~MODE[1], ~MODE[0]);  // AND_Gate
  and and_2 (output_enable, MODE[2], MODE[0]);
  Multiplexer #(.width(16)) multiplexer_1 (.in0(GPU_DATA), .in1(adder_1_out), .out(multiplexer_1_out), .sel(MODE[0]));
  Register #(.width(16)) RegAddr (
    .D(multiplexer_1_out), .en(MODE[1]), .clk(CLK), .Q({RegAddr_q[15], GPU_ADDR}));  // open: clr
  Adder #(.width(16)) adder_1 (.a({RegAddr_q[15], GPU_ADDR}), .b(16'h1), .out(adder_1_out));  // open: cin, cout
  and and_3 (and_3_out, RegAddr_q[15], write_enable);
  ROM #(.addrWidth(16), .dataWidth(16)) rom_1 (.addr({RegAddr_q[15], GPU_ADDR}), .data(rom_1_data));
  RAM #(.addrWidth(16), .asyncread("true"), .dataWidth(16), .\type ("nonvolatile")) general_purpose_memory (
    .addr({RegAddr_q[15], GPU_ADDR}), .we(and_3_out), .oe(1'b1), .clk(CLK), .din(GPU_DATA),
    .dout(general_purpose_memory_dout));
  and and_4 (GPU_WE, ~RegAddr_q[15], write_enable);  // AND_Gate
  Multiplexer #(.width(16)) multiplexer_2 (
    .in0(rom_1_data), .in1(general_purpose_memory_dout), .out(multiplexer_2_out), .sel(RegAddr_q[15]));
  assign DataBUSout = output_enable ? multiplexer_2_out : 16'bz;  // Controlled_Buffer controlled_buffer_2

  // Other names for the same wires on the sheet: Data_in[15:0] = GPU_DATA

  // Notes on the sheet:
  //   15 bit
  //   contents of rom_1 (hex, n*v repeats v):
  //   4800 ee c008 6080 8880 fecf 2880 1 9880 fecf d080 b100 c004 c005 c008 c009 c00a 6140 8850 feff 1084
  //   a800 50 3940 a 4900 30 3940 8 4900 3e 9045 2850 1 3950 fff0 4e00 28 1850 ff00 9850 feff d0a0 d090
  //   d080 d050 d040 b100 1850 ff00 9850 feff 1880 1 9880 fefe d0a0 d090 d080 d050 d040 b100 3950 ff00
  //   4900 49 2950 1 1840 20 9045 9850 feff d0a0 d090 d080 d050 d040 b100 0 8890 feef 3980 a 4900 62 3980
  //   8 4900 69 9089 2890 1 2a90 7fff 9890 feef b000 2890 100 2a90 7f00 9890 feef b000 2990 1 2a90 7fff
  //   9890 feef 1880 20 9089 b000 3299 4900 83 c008 c009 8088 a800 50 d090 d080 2880 1 2990 1 4800 73 b000
  //   a800 73 1880 a 4800 50 c004 1048 1880 78 a800 50 1084 2f80 c 2a80 f 2880 fed0 8088 a800 50 1084 2f80
  //   8 2a80 f 2880 fed0 8088 a800 50 1084 2f80 4 2a80 f 2880 fed0 8088 a800 50 1084 2f80 0 2a80 f 2880
  //   fed0 8088 a800 50 d040 b000 3288 4900 c4 1880 f000 1890 4 a800 73 b000 1880 f004 1890 5 a800 73 b000
  //   1880 7fff 1890 20 9098 2980 1 4a00 cf 9098 9880 feef b000 32aa 4900 e8 80b8 80c9 31bc 4a00 eb 2880 1
  //   2890 1 29a0 1 4800 d8 1880 1 b000 1880 0 b000 1820 f000 1880 f009 1890 b a800 84 2b10 8000 2b10 4000
  //   1880 3e a800 50 1880 20 9880 ff00 9880 ff01 9880 ff02 9880 ff03 9880 ff04 9880 ff05 9880 ff06 9880
  //   ff07 9880 ff08 9880 ff09 9880 ff0a 9880 ff0b 9880 ff0c 9880 ff0d 9880 ff0e 9880 ff0f 9880 ff10 9880
  //   ff11 9880 ff12 9880 ff13 9880 ff14 9880 ff15 9880 ff16 9880 ff17 9880 ff18 9880 ff19 9880 ff1a 9880
  //   ff1b 9880 ff1c 9880 ff1d 9880 ff1e 9880 ff1f 9880 ff20 9880 ff21 9880 ff22 9880 ff23 9880 ff24 9880
  //   ff25 9880 ff26 9880 ff27 9880 ff28 9880 ff29 9880 ff2a 9880 ff2b 9880 ff2c 9880 ff2d 9880 ff2e 9880
  //   ff2f 9880 ff30 9880 ff31 9880 ff32 9880 ff33 9880 ff34 9880 ff35 9880 ff36 9880 ff37 9880 ff38 9880
  //   ff39 9880 ff3a 9880 ff3b 9880 ff3c 9880 ff3d 9880 ff3e 9880 ff3f 9880 ff40 9880 ff41 9880 ff42 9880
  //   ff43 9880 ff44 9880 ff45 9880 ff46 9880 ff47 9880 ff48 9880 ff49 9880 ff4a 9880 ff4b 9880 ff4c 9880
  //   ff4d 9880 ff4e 9880 ff4f 9880 ff50 9880 ff51 9880 ff52 9880 ff53 9880 ff54 9880 ff55 9880 ff56 9880
  //   ff57 9880 ff58 9880 ff59 9880 ff5a 9880 ff5b 9880 ff5c 9880 ff5d 9880 ff5e 9880 ff5f 9880 ff60 9880
  //   ff61 9880 ff62 9880 ff63 9880 ff64 9880 ff65 9880 ff66 9880 ff67 9880 ff68 9880 ff69 9880 ff6a 9880
  //   ff6b 9880 ff6c 9880 ff6d 9880 ff6e 9880 ff6f 9880 ff70 9880 ff71 9880 ff72 9880 ff73 9880 ff74 9880
  //   ff75 9880 ff76 9880 ff77 9880 ff78 9880 ff79 9880 ff7a 9880 ff7b 9880 ff7c 9880 ff7d 9880 ff7e 9880
  //   ff7f 9880 ff80 9880 ff81 9880 ff82 9880 ff83 9880 ff84 9880 ff85 9880 ff86 9880 ff87 9880 ff88 9880
  //   ff89 9880 ff8a 9880 ff8b 9880 ff8c 9880 ff8d 9880 ff8e 9880 ff8f 9880 ff90 9880 ff91 9880 ff92 9880
  //   ff93 9880 ff94 9880 ff95 9880 ff96 9880 ff97 9880 ff98 9880 ff99 9880 ff9a 9880 ff9b 9880 ff9c 9880
  //   ff9d 9880 ff9e 9880 ff9f 9880 ffa0 9880 ffa1 9880 ffa2 9880 ffa3 9880 ffa4 9880 ffa5 9880 ffa6 9880
  //   ffa7 9880 ffa8 9880 ffa9 9880 ffaa 9880 ffab 9880 ffac 9880 ffad 9880 ffae 9880 ffaf 9880 ffb0 9880
  //   ffb1 9880 ffb2 9880 ffb3 9880 ffb4 9880 ffb5 9880 ffb6 9880 ffb7 9880 ffb8 9880 ffb9 9880 ffba 9880
  //   ffbb 9880 ffbc 9880 ffbd 9880 ffbe 9880 ffbf 9880 ffc0 9880 ffc1 9880 ffc2 9880 ffc3 9880 ffc4 9880
  //   ffc5 9880 ffc6 9880 ffc7 9880 ffc8 9880 ffc9 9880 ffca 9880 ffcb 9880 ffcc 9880 ffcd 9880 ffce 9880
  //   ffcf 9880 ffd0 9880 ffd1 9880 ffd2 9880 ffd3 9880 ffd4 9880 ffd5 9880 ffd6 9880 ffd7 9880 ffd8 9880
  //   ffd9 9880 ffda 9880 ffdb 9880 ffdc 9880 ffdd 9880 ffde 9880 ffdf 9880 ffe0 9880 ffe1 9880 ffe2 9880
  //   ffe3 9880 ffe4 9880 ffe5 9880 ffe6 9880 ffe7 9880 ffe8 9880 ffe9 9880 ffea 9880 ffeb 9880 ffec 9880
  //   ffed 9880 ffee 9880 ffef 8840 fefe 3244 4900 2e0 1840 0 9840 fefe 1880 ff00 1890 f018 18a0 4 a800 d8
  //   3288 4a00 31d 1880 ff00 1890 f084 18a0 4 a800 d8 3288 4a00 325 1880 ff00 1890 f014 18a0 4 a800 d8
  //   3288 4a00 32d 1880 ff00 1890 f088 18a0 5 a800 d8 3288 4a00 337 1880 f08d 1890 f a800 84 4800 fa 1880
  //   f01c 1890 68 a800 84 4800 fa 1880 ff05 1890 fa a800 84 4800 fa 8880 fecf a800 8a 1880 a a800 50 4800
  //   fa a800 cb 4800 fa 60613*0 74 72 75 65 66 61 6c 73 65 6d 41 4c 55 73 68 20 76 30 2e 31 74 69 6d 65
  //   68 65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
  //   VRAM
  //   ROM
  //   RAM
endmodule

module alu (
  input  clk,
  input  [15:0] busin,
  input  [3:0] op,
  output [15:0] busout,
  output FC,
  output FS,
  output FZ,
  output FO
);

  wire adder_1_cout, and_1_out, and_2_out, comparator_1_eq, comparator_2_eq, out_enable, subtractor_1_bout,
       xnor_1_out, xor_1_out;
  wire [14:0] aluout;
  wire [15:0] A, adder_1_out, and_4_out, B, not_2_out, or_1_out, shifter_1_out, shifter_2_out,
       subtractor_1_out, xor_2_out;

  Comparator #(.width(3)) comparator_1 (.a(op[2:0]), .b(3'b000), .eq(comparator_1_eq));  // open: gt, lt
  Comparator #(.width(3)) comparator_2 (.a(op[2:0]), .b(3'b001), .eq(comparator_2_eq));  // open: gt, lt
  not not_1 (out_enable, op[3]);
  and and_1 (and_1_out, op[3], comparator_1_eq);
  and and_2 (and_2_out, op[3], comparator_2_eq);
  Register #(.width(16)) register_1 (.D(busin), .en(and_1_out), .clk(clk), .Q(A), .clr(1'b0));
  Register #(.width(16)) register_2 (.D(busin), .en(and_2_out), .clk(clk), .Q(B), .clr(1'b0));
  assign busout = out_enable ? {FS, aluout} : 16'bz;  // Controlled_Buffer controlled_buffer_1
  Comparator #(.width(16)) comparator_3 (.a({FS, aluout}), .b({16{1'b0}}), .eq(FZ));  // open: gt, lt
  xnor xnor_1 (xnor_1_out, FS, B[15]);
  xor xor_1 (xor_1_out, A[15], B[15]);
  and and_3 (FO, xnor_1_out, xor_1_out);
  Adder #(.width(16)) adder_1 (.a(A), .b(B), .out(adder_1_out), .cin(1'b0), .cout(adder_1_cout));
  Subtractor #(.width(16)) subtractor_1 (.a(A), .b(B), .out(subtractor_1_out), .bin(1'b0), .bout(subtractor_1_bout));
  assign and_4_out = A & B;  // AND_Gate and_4, 16 bits wide
  assign or_1_out = A | B;  // OR_Gate or_1, 16 bits wide
  assign xor_2_out = A ^ B;  // XOR_Gate xor_2, 16 bits wide
  assign not_2_out = ~A;  // NOT_Gate not_2, 16 bits wide
  Shifter #(.width(16)) shifter_1 (.in(A), .\dist (B[3:0]), .out(shifter_1_out));
  Shifter #(.shift("lr"), .width(16)) shifter_2 (.in(A), .\dist (B[3:0]), .out(shifter_2_out));
  Multiplexer #(.select(3)) multiplexer_1 (
    .in0(adder_1_cout), .in1(subtractor_1_bout), .in2(1'b0), .in3(1'b0), .in4(1'b0), .in5(1'b0), .in6(1'b0),
    .in7(1'b0), .out(FC), .sel(op[2:0]));
  Multiplexer #(.select(3), .width(16)) multiplexer_2 (
    .in0(adder_1_out), .in1(subtractor_1_out), .in2(and_4_out), .in3(or_1_out), .in4(xor_2_out),
    .in5(not_2_out), .in6(shifter_1_out), .in7(shifter_2_out), .out({FS, aluout}), .sel(op[2:0]));

  // Other names for the same wires on the sheet: aluout[15] = FS; bin[15:0] = busin; cout = FC; aluop[2:0] = op[2:0];
  //   regid[2:0] = op[2:0]; regwe = op[3]
endmodule

module control (
  input  CLK,
  input  [15:0] ialubus,
  input  ifs,
  input  ifo,
  input  ifc,
  input  ifz,
  input  [15:0] imembus,
  input  [15:0] iregbus,
  input  iint,
  input  [2:0] iintid,
  input  ibusy,
  input  [15:0] iiobus,
  output [3:0] oaluop,
  output [15:0] oalubus,
  output [2:0] omemop,
  output [15:0] omembus,
  output oregwe,
  output [15:0] oregbus,
  output [3:0] oregid,
  output mask_save,
  output mask_restore,
  output [1:0] oioop,
  output [15:0] oiobus,
  output [2:0] oioaddr
);

  wire and_1_out, and_2_out, and_3_out, and_4_out, and_5_out, and_8_out, c, flwe, instr_load, isimm, isint,
       isjump, isret, isstack, next_instr, not_1_out, not_2_out, not_3_out, not_4_out, not_5_out, not_6_out,
       o, or_1_out, or_2_out, or_3_out, regds, regsrc, s, should_jump, tempregwe, valid, xnor_1_out,
       xnor_2_out, xor_1_out, xor_2_out, z;
  wire [1:0] alumode, alusrc, memsrc;
  wire [2:0] intid_saved;
  wire [3:0] adder_2_out, cycle, flags_saved, multiplexer_5_out, multiplexer_8_out, multiplexer_9_out,
       multiplexer_10_out, opcode;
  wire [7:0] instruction_q;
  wire [15:0] alubus, alubuswrite, iobuswrite, ip, ipnext, membus, membuswrite, multiplexer_1_out,
       multiplexer_2_out, multiplexer_3_out, multiplexer_4_out, multiplexer_11_out, multiplexer_16_out,
       regbuswrite, srctempbus, tempreg;
  wire [23:22] rom_1_data;

  Adder #(.width(16)) adder_1 (.a(ip), .b(16'h1), .out(ipnext), .cin(isimm));  // open: cout
  Multiplexer #(.width(16)) multiplexer_1 (.in0(ipnext), .in1(iobuswrite), .out(multiplexer_1_out), .sel(and_1_out));
  and and_1 (and_1_out, isjump, should_jump);
  not not_1 (not_1_out, oaluop[3]);
  assign alubus = not_1_out ? ialubus : 16'bz;  // Controlled_Buffer controlled_buffer_1
  assign membus = and_5_out ? imembus : 16'bz;  // Controlled_Buffer controlled_buffer_2
  Multiplexer #(.width(16)) multiplexer_2 (.in0(membus), .in1({16{1'b0}}), .out(multiplexer_2_out), .sel(isint));
  Multiplexer #(.width(16)) multiplexer_3 (.in0(multiplexer_1_out), .in1(membus), .out(multiplexer_3_out), .sel(isret));
  Multiplexer #(.width(16)) multiplexer_4 (
    .in0(multiplexer_3_out), .in1({{12{1'b1}}, intid_saved, 1'b0}), .out(multiplexer_4_out), .sel(isint));
  Register #(.width(16)) instruction (
    .D(multiplexer_2_out), .en(instr_load), .clk(CLK), .Q({opcode, isimm, oioaddr, instruction_q}), .clr(1'b0));
  Register #(.width(16)) u_IP (.D(multiplexer_4_out), .en(next_instr), .clk(CLK), .Q(ip), .clr(1'b0));
  xnor xnor_1 (xnor_1_out, s, o);
  xor xor_1 (xor_1_out, s, o);
  xnor xnor_2 (xnor_2_out, s, o);
  xor xor_2 (xor_2_out, s, o);
  Clock clock_1 ();  // open: out
  and and_2 (and_2_out, oioop[0], oioop[1]);
  Pull_Resistor pull_resistor_1 (.node({opcode, isimm, oioaddr, instruction_q}));
  not not_2 (not_2_out, z);
  or or_1 (or_1_out, z, xor_1_out);
  and and_3 (and_3_out, ~z, xnor_2_out);  // AND_Gate
  not not_3 (not_3_out, s);
  not not_4 (not_4_out, c);
  or or_2 (or_2_out, c, z);
  and and_4 (and_4_out, ~c, ~z);  // AND_Gate
  not not_5 (not_5_out, o);
  assign oalubus = oaluop[3] ? alubuswrite : 16'bz;  // Controlled_Buffer controlled_buffer_3
  and and_5 (and_5_out, omemop[0], omemop[2]);
  not not_6 (not_6_out, and_5_out);
  assign omembus = not_6_out ? membuswrite : 16'bz;  // Controlled_Buffer controlled_buffer_4
  assign oregbus = oregwe ? regbuswrite : 16'bz;  // Controlled_Buffer controlled_buffer_5
  assign oiobus = and_2_out ? iobuswrite : 16'bz;  // Controlled_Buffer controlled_buffer_6
  Multiplexer #(.width(4)) multiplexer_5 (
    .in0(instruction_q[7:4]), .in1(instruction_q[3:0]), .out(multiplexer_5_out), .sel(regds));
  Multiplexer #(.select(4)) multiplexer_6 (
    .in0(1'b1), .in1(z), .in2(not_2_out), .in3(xnor_1_out), .in4(or_1_out), .in5(and_3_out), .in6(xor_2_out),
    .in7(o), .in8(ibusy), .in9(s), .in10(not_3_out), .in11(not_4_out), .in12(or_2_out), .in13(and_4_out),
    .in14(c), .in15(not_5_out), .out(should_jump), .sel({opcode[0], oioaddr}));
  Multiplexer #(.width(4)) multiplexer_7 (.in0(multiplexer_5_out), .in1(4'b0010), .out(oregid), .sel(isstack));
  Adder #(.width(4)) adder_2 (.a(cycle), .b(4'b0001), .out(adder_2_out));  // open: cin, cout
  Register #(.width(4)) u_cycle (.D(multiplexer_8_out), .en(1'b1), .clk(CLK), .Q(cycle), .clr(1'b0));
  Multiplexer #(.width(4)) multiplexer_8 (.in0(adder_2_out), .in1(4'b0000), .out(multiplexer_8_out), .sel(next_instr));
  Register #(.width(4)) flags (.D(multiplexer_9_out), .en(or_3_out), .clk(CLK), .Q({z, c, o, s}), .clr(1'b0));
  Multiplexer #(.width(4)) multiplexer_9 (
    .in0({ifz, ifc, ifo, ifs}), .in1(flags_saved), .out(multiplexer_9_out), .sel(mask_restore));
  or or_3 (or_3_out, mask_restore, flwe);
  Register #(.width(16)) u_tempreg (.D(membus), .en(tempregwe), .clk(CLK), .Q(tempreg), .clr(1'b0));
  ROM #(.dataWidth(24)) rom_1 (
    .addr({opcode, cycle}),
    .data({rom_1_data, oioop, isret, isstack, tempregwe, isjump, flwe, omemop, memsrc, instr_load, regsrc, oregwe, regds, alusrc, alumode, valid, next_instr}));
  Pull_Resistor pull_resistor_2 (.node(cycle));
  Multiplexer #(.width(4)) multiplexer_10 (
    .in0({z, c, o, s}), .in1({ifz, ifc, ifo, ifs}), .out(multiplexer_10_out), .sel(flwe));
  Pull_Resistor pull_resistor_3 (.node({rom_1_data, oioop, isret, isstack, tempregwe, isjump, flwe, omemop, memsrc, instr_load, regsrc, oregwe, regds, alusrc, alumode, valid, next_instr}));
  Register #(.width(4)) flags_int (.D(multiplexer_10_out), .en(mask_save), .clk(CLK), .Q(flags_saved), .clr(1'b0));
  Register #(.width(4)) register_1 (
    .D({iint, iintid}), .en(next_instr), .clk(CLK), .Q({isint, intid_saved}), .clr(1'b0));
  Pull_Resistor pull_resistor_4 (.node(iintid));
  and and_6 (mask_save, iint, next_instr);
  and and_7 (mask_restore, isret, next_instr, oioaddr[0]);
  Multiplexer #(.width(16)) multiplexer_11 (.in0(ip), .in1(ipnext), .out(multiplexer_11_out), .sel(isjump));
  Multiplexer #(.width(16)) multiplexer_12 (.in0(iregbus), .in1(membus), .out(iobuswrite), .sel(isimm));
  Multiplexer #(.width(16)) multiplexer_13 (.in0(iregbus), .in1(tempreg), .out(srctempbus), .sel(isimm));
  Multiplexer #(.select(2), .width(4)) multiplexer_14 (
    .in0({1'b0, oioaddr}), .in1({3'b100, regds}), .in2(4'b0000), .in3(4'b0001), .out(oaluop), .sel(alumode));
  Multiplexer #(.select(2), .width(16)) multiplexer_15 (
    .in0(iregbus), .in1(iobuswrite), .in2({16{1'b0}}), .in3(16'h1), .out(alubuswrite), .sel(alusrc));
  Multiplexer #(.width(16)) multiplexer_16 (.in0(alubus), .in1(membus), .out(multiplexer_16_out), .sel(regsrc));
  Multiplexer #(.select(2), .width(16)) multiplexer_17 (
    .in0(iregbus), .in1(iobuswrite), .in2(multiplexer_11_out), .in3(srctempbus), .out(membuswrite),
    .sel(memsrc));
  and and_8 (and_8_out, ~oioop[0], oioop[1]);  // AND_Gate
  Multiplexer #(.width(16)) multiplexer_18 (.in0(multiplexer_16_out), .in1(iiobus), .out(regbuswrite), .sel(and_8_out));

  // Other names for the same wires on the sheet: fs = ifs; fo = ifo; fc = ifc; fz = ifz; regwe = oregwe;
  //   memop[2:0] = omemop; ioop[1:0] = oioop; intid[2:0] = iintid; int = iint; funct[2:0] = oioaddr;
  //   aluop[3:0] = oaluop; busy = ibusy; enter_int = mask_save; iobus[15:0] = iiobus; leave_int = mask_restore;
  //   regbus[15:0] = iregbus; regid[3:0] = oregid; srcbus[15:0] = iobuswrite

  // Notes on the sheet:
  //   MEM
  //   REG
  //   IO
  //   ALU
  //   REGISTERS
  //   JUMPS
  //   contents of rom_1 (hex, n*v repeats v):
  //   2802 7202 40004 25074 4208c 4841 10*1 2802 7202 26 5056 8b 11*1 2802 7202 6 5056 8083 11*1 2802 7202
  //   6 5056 8003 11*1 2802 7202 15043 13*1 2802 7202 15043 13*1 2802 7202 200083 13*1 2802 7202 305043
  //   13*1 2802 7202 25002 2c42 5183 11*1 2802 7202 25002 2c42 4003 11*1 2802 7202 40006 25076 4208e 14802
  //   2802 3002 15103 7*1 2802 7202 42006 76 c508b 11*1 2802 7202 40006 25076 4208e 4c43 10*1 2802 7202
  //   42006 76 4008a 5183 10*1 2802 7202 14*1 2802 7202 14*1
  //   CONTROL SIGNALS
  //   BUSES
endmodule

module registerfile (
  input  [7:0] ioint,
  input  CLK,
  input  [15:0] data_in,
  input  [7:0] iobusy,
  input  wr_enable,
  input  mask_save,
  input  mask_restore,
  input  [3:0] regid,
  output [2:0] INT_ID,
  output INT,
  output BUSY,
  output [15:0] data_out
);

  wire demultiplexer_1_out0, demultiplexer_1_out2, demultiplexer_1_out3, demultiplexer_1_out4,
       demultiplexer_1_out5, demultiplexer_1_out6, demultiplexer_1_out7, demultiplexer_1_out8,
       demultiplexer_1_out9, demultiplexer_1_out10, demultiplexer_1_out11, demultiplexer_1_out12,
       demultiplexer_1_out13, demultiplexer_1_out14, demultiplexer_1_out15, not_1_out, or_1_out, r1we;
  wire [7:0] and_1_out;
  wire [15:0] mask_saved, multiplexer_1_out, multiplexer_2_out, multiplexer_3_out, multiplexer_4_out, r0_out,
       r1_out, r2_q, r3_q, r4_q, r5_q, r6_q, r7_q, r8_q, r9_q, r10_q, r11_q, r12_q, r13_q, r14_q, r15_q;

  Demultiplexer #(.select(4)) demultiplexer_1 (
    .out0(demultiplexer_1_out0), .out1(r1we), .out2(demultiplexer_1_out2), .out3(demultiplexer_1_out3),
    .out4(demultiplexer_1_out4), .out5(demultiplexer_1_out5), .out6(demultiplexer_1_out6),
    .out7(demultiplexer_1_out7), .out8(demultiplexer_1_out8), .out9(demultiplexer_1_out9),
    .out10(demultiplexer_1_out10), .out11(demultiplexer_1_out11), .out12(demultiplexer_1_out12),
    .out13(demultiplexer_1_out13), .out14(demultiplexer_1_out14), .out15(demultiplexer_1_out15),
    .in(wr_enable), .sel(regid));
  Multiplexer #(.width(16)) multiplexer_1 (.in0(r1_out), .in1(data_in), .out(multiplexer_1_out), .sel(r1we));
  // NoConnect on demultiplexer_1_out0
  Register #(.width(16)) mask_storage (.D(multiplexer_1_out), .en(mask_save), .clk(CLK), .Q(mask_saved));  // open: clr
  Multiplexer #(.width(16)) multiplexer_2 (
    .in0(data_in), .in1(mask_saved), .out(multiplexer_2_out), .sel(mask_restore));
  Multiplexer #(.width(16)) multiplexer_3 (
    .in0(multiplexer_2_out), .in1({16{1'b0}}), .out(multiplexer_3_out), .sel(mask_save));
  or or_1 (or_1_out, r1we, mask_save, mask_restore);
  Register #(.width(16)) r0 (.D({ioint, iobusy}), .en(1'b1), .clk(CLK), .Q(r0_out));  // open: clr
  Register #(.width(16)) r1 (.D(multiplexer_3_out), .en(or_1_out), .clk(CLK), .Q(r1_out));  // open: clr
  Register #(.width(16)) r2 (.D(data_in), .en(demultiplexer_1_out2), .clk(CLK), .Q(r2_q));  // open: clr
  Register #(.width(16)) r3 (.D(data_in), .en(demultiplexer_1_out3), .clk(CLK), .Q(r3_q));  // open: clr
  Register #(.width(16)) r4 (.D(data_in), .en(demultiplexer_1_out4), .clk(CLK), .Q(r4_q));  // open: clr
  Register #(.width(16)) r5 (.D(data_in), .en(demultiplexer_1_out5), .clk(CLK), .Q(r5_q));  // open: clr
  Register #(.width(16)) r6 (.D(data_in), .en(demultiplexer_1_out6), .clk(CLK), .Q(r6_q));  // open: clr
  Register #(.width(16)) r7 (.D(data_in), .en(demultiplexer_1_out7), .clk(CLK), .Q(r7_q));  // open: clr
  Register #(.width(16)) r8 (.D(data_in), .en(demultiplexer_1_out8), .clk(CLK), .Q(r8_q));  // open: clr
  Register #(.width(16)) r9 (.D(data_in), .en(demultiplexer_1_out9), .clk(CLK), .Q(r9_q));  // open: clr
  Register #(.width(16)) r10 (.D(data_in), .en(demultiplexer_1_out10), .clk(CLK), .Q(r10_q));  // open: clr
  Register #(.width(16)) r11 (.D(data_in), .en(demultiplexer_1_out11), .clk(CLK), .Q(r11_q));  // open: clr
  Register #(.width(16)) r12 (.D(data_in), .en(demultiplexer_1_out12), .clk(CLK), .Q(r12_q));  // open: clr
  Register #(.width(16)) r13 (.D(data_in), .en(demultiplexer_1_out13), .clk(CLK), .Q(r13_q));  // open: clr
  Register #(.width(16)) r14 (.D(data_in), .en(demultiplexer_1_out14), .clk(CLK), .Q(r14_q));  // open: clr
  Register #(.width(16)) r15 (.D(data_in), .en(demultiplexer_1_out15), .clk(CLK), .Q(r15_q));  // open: clr
  assign data_out = not_1_out ? multiplexer_4_out : 16'bz;  // Controlled_Buffer controlled_buffer_1
  Multiplexer #(.select(4), .width(16)) multiplexer_4 (
    .in0(r0_out), .in1(r1_out), .in2(r2_q), .in3(r3_q), .in4(r4_q), .in5(r5_q), .in6(r6_q), .in7(r7_q),
    .in8(r8_q), .in9(r9_q), .in10(r10_q), .in11(r11_q), .in12(r12_q), .in13(r13_q), .in14(r14_q),
    .in15(r15_q), .out(multiplexer_4_out), .sel(regid));
  not not_1 (not_1_out, wr_enable);
  assign and_1_out = r0_out[15:8] & r1_out[15:8];  // AND_Gate and_1, 8 bits wide
  or or_2 (BUSY, r0_out[0], r0_out[1], r0_out[2], r0_out[3], r0_out[4], r0_out[5], r0_out[6], r0_out[7]);
  Priority_Encoder priority_encoder_1 (
    .in0(and_1_out[7]), .in1(and_1_out[6]), .in2(and_1_out[5]), .in3(and_1_out[4]), .in4(and_1_out[3]),
    .in5(and_1_out[2]), .in6(and_1_out[1]), .in7(and_1_out[0]), .out(INT_ID), .gs(INT));  // open: en_in, en_out

  // Other names for the same wires on the sheet: data_tunnel[15:0] = data_in; reg_num[3:0] = regid; we = wr_enable

  // Notes on the sheet:
  //   necessary to prevent incredibely rare situation
  //   when int happens EXACTLY on mask update
endmodule

module IO (
  input  CLK,
  input  [15:0] iiobus,
  input  [2:0] iioid,
  input  [1:0] iiocmd,
  input  [6:0] ikeychar,
  input  ikeyaval,
  output [15:0] oiobus,
  output [7:0] ointasssert,
  output [7:0] obusyassert,
  output ogpu_clear,
  output okeyread,
  output [15:0] oled
);

  wire and_2_out, and_3_out, and_4_out, and_7_out, isclock, isgpu, iskeyboard, isled, or_2_out, re, we;
  wire [6:0] keyoutput;
  wire [7:0] multiplexer_1_out;
  wire [11:0] adder_1_out, register_2_q;
  wire [15:0] multiplexer_2_out;

  or or_1 (okeyread, and_2_out, and_3_out);
  Register register_1 (.D(multiplexer_1_out), .en(okeyread), .clk(CLK), .Q({ointasssert[6], keyoutput}), .clr(1'b0));
  Multiplexer #(.width(8)) multiplexer_1 (
    .in0({8{1'b0}}), .in1({1'b1, ikeychar}), .out(multiplexer_1_out), .sel(ikeyaval));
  Register #(.width(12)) register_2 (.D(adder_1_out), .en(1'b1), .clk(CLK), .Q(register_2_q), .clr(ointasssert[7]));
  Adder #(.width(12)) adder_1 (.a(register_2_q), .b(12'h1), .out(adder_1_out));  // open: cin, cout
  and and_1 (ogpu_clear, isgpu, we);
  and and_2 (and_2_out, iskeyboard, re);
  and and_3 (and_3_out, ikeyaval, ~ointasssert[6]);  // AND_Gate
  and and_4 (and_4_out, isled, we);
  and and_5 (we, iiocmd[0], iiocmd[1]);
  and and_6 (re, iiocmd[1], ~iiocmd[0]);  // AND_Gate
  Register #(.width(16)) register_3 (.D(iiobus), .en(and_4_out), .clk(CLK), .Q(oled), .clr(1'b0));
  and and_7 (and_7_out, isclock, re);
  Multiplexer #(.select(3), .width(16)) multiplexer_2 (
    .in0({16{1'b0}}), .in1({{9{1'b0}}, keyoutput}), .in2({16{1'b0}}), .in3({16{1'b0}}), .in4({16{1'b0}}),
    .in5({16{1'b0}}), .in6({16{1'b0}}), .in7({16{1'b0}}), .out(multiplexer_2_out), .sel(iioid));
  or or_2 (or_2_out, and_7_out, register_2_q[11]);
  assign oiobus = re ? multiplexer_2_out : 16'bz;  // Controlled_Buffer controlled_buffer_1
  Register #(.width(1)) register_4 (.D(register_2_q[11]), .en(or_2_out), .clk(CLK), .Q(ointasssert[7]), .clr(1'b0));
  Demultiplexer #(.select(3)) demultiplexer_1 (
    .out0(isclock), .out1(iskeyboard), .out2(isgpu), .out7(isled), .in(1'b1), .sel(iioid));  // open: out3, out4, out5, out6

  assign obusyassert = {8{1'b0}};
  assign ointasssert[5:0] = {6{1'b0}};

  // Other names for the same wires on the sheet: keychar[6:0] = ikeychar; iobus[15:0] = iiobus; ioid[2:0] = iioid;
  //   keyaval = ikeyaval; keyread = okeyread; key_present = ointasssert[6]; clockint = ointasssert[7]

  // Notes on the sheet:
  //   GPU interface
  //   clock
  //   CPU interface
  //   keyboard interface
  //   led interface
  //   IO interface
endmodule

module GPU (
  input  p_clk,
  input  clk,
  input  datawe,
  input  [14:0] addr,
  input  [7:0] data,
  input  [1:0] IOWE,
  input  [15:0] IOo,
  input  [15:0] IO_ADDR,
  input  [15:0] IOi,
  output HSYNC,
  output VSYNC,
  output [7:0] color8,
  output [9:0] DEBUG_x,
  output [9:0] DEBUG_y,
  output DEBUG_WE
);

  wire active_col, active_row, active_video, and_3_out, BG_WE, C, c_clk, clr_all_end, clr_all_mode,
       clr_all_start, clr_YY_end, clr_YY_mode, clr_YY_start, comparator_1_eq, comparator_2_eq,
       comparator_3_eq, comparator_4_eq, counter_1_carry, counter_2_carry, counter_3_carry, counter_4_carry,
       counter_5_carry, counter_6_carry, counter_8_carry, d_ff_1_qn, d_ff_2_qn, draw_mode, FG_WE,
       h_back_porch, h_front_porch, h_sync_pulse, IO_RE, IO_WE, LINE_END, or_1_out, or_2_out, or_3_out,
       or_4_out, or_5_out, s_r_ff_3_q, s_r_ff_3_qn, s_r_ff_4_q, s_r_ff_4_qn, s_r_ff_5_qn, s_r_ff_6_qn,
       v_back_porch, v_front_porch, v_sync_pulse;
  wire [2:0] c_col;
  wire [3:0] c_row;
  wire [7:0] BG_C_q, char, col_q, FG_C_q, multiplexer_3_out, multiplexer_5_out, row_q, VRAM_plane2_dout;
  wire [9:3] col;
  wire [9:4] row;
  wire [14:0] addr_t, bit_extender_1_out, bit_extender_2_out, bit_extender_3_out, bit_extender_4_out,
       clr_addr, multiplexer_1_out, multiplexer_2_out, shifter_1_out, shifter_2_out;

  and and_1 (IO_WE, IOWE[1], IOWE[1]);
  and and_2 (IO_RE, IOWE[1], ~IOWE[1]);  // AND_Gate
  Multiplexer #(.width(15)) multiplexer_1 (
    .in0(clr_addr), .in1(multiplexer_2_out), .out(multiplexer_1_out), .sel(draw_mode));
  Multiplexer #(.width(15)) multiplexer_2 (
    .in0(addr_t), .in1({{6{1'b0}}, addr[11:8], addr[4:0]}), .out(multiplexer_2_out), .sel(datawe));
  or or_1 (or_1_out, ~draw_mode, datawe);  // OR_Gate
  Multiplexer #(.width(8)) multiplexer_3 (.in0({8{1'b0}}), .in1(data), .out(multiplexer_3_out), .sel(draw_mode));
  // Probe on multiplexer_3_out
  // Probe on multiplexer_1_out
  RAM #(.addrWidth(15), .asyncread("true")) VRAM_plane0 (
    .addr(multiplexer_1_out), .we(or_1_out), .oe(draw_mode), .clk(c_clk), .din(multiplexer_3_out), .dout(char));
  and and_3 (and_3_out, IO_RE, IO_ADDR[1]);
  assign IOo = and_3_out ? 16'h2 : 16'bz;  // Controlled_Buffer controlled_buffer_1
  and and_4 (FG_WE, IO_WE, comparator_1_eq);
  Comparator comparator_1 (.a(IOi[15:8]), .b(8'h2), .eq(comparator_1_eq));  // open: gt, lt
  and and_5 (BG_WE, IO_WE, comparator_2_eq);
  Comparator comparator_2 (.a(IOi[15:8]), .b(8'h3), .eq(comparator_2_eq));  // open: gt, lt
  and and_6 (clr_all_start, IO_WE, comparator_3_eq);
  Comparator comparator_3 (.a(IOi[15:8]), .b(8'h4), .eq(comparator_3_eq));  // open: gt, lt
  and and_7 (clr_YY_start, IO_WE, comparator_4_eq);
  Comparator comparator_4 (.a(IOi[15:8]), .b(8'h5), .eq(comparator_4_eq));  // open: gt, lt
  Multiplexer multiplexer_4 (.in0(p_clk), .in1(clk), .out(c_clk), .sel(datawe));
  Counter #(.max('h60)) counter_1 (
    .load(1'b0), .count(active_col), .carry(counter_1_carry), .up(1'b1), .clk(p_clk), .clr(LINE_END));  // open: D, Q
  Counter #(.max('h2)) counter_2 (
    .load(1'b0), .count(active_row), .carry(counter_2_carry), .up(1'b1), .clk(LINE_END), .clr(counter_8_carry));  // open: D, Q
  S_R_Flip_Flop s_r_ff_1 (
    .S(counter_1_carry), .clk(p_clk), .R(1'b0), .Q(h_back_porch), .Qn(h_sync_pulse), .preset(1'b0),
    .reset(counter_3_carry));
  S_R_Flip_Flop s_r_ff_2 (
    .S(counter_2_carry), .clk(LINE_END), .R(1'b0), .Q(v_back_porch), .Qn(v_sync_pulse), .preset(1'b0),
    .reset(counter_4_carry));
  Counter #(.max('h30)) counter_3 (
    .load(1'b0), .count(h_back_porch), .carry(counter_3_carry), .up(1'b1), .clk(p_clk), .clr(LINE_END));  // open: D, Q
  Counter #(.max('h1f)) counter_4 (
    .load(1'b0), .count(v_back_porch), .carry(counter_4_carry), .up(1'b1), .clk(LINE_END),
    .clr(counter_8_carry));  // open: D, Q
  // Probe on {char, 1'b0, c_row}
  RAM #(.addrWidth(13), .asyncread("true"), .\type ("nonvolatile")) VRAM_plane2 (
    .addr({char, 1'b0, c_row}), .we(1'b0), .oe(DEBUG_WE), .clk(p_clk),
    .dout({VRAM_plane2_dout[0], VRAM_plane2_dout[1], VRAM_plane2_dout[2], VRAM_plane2_dout[3], VRAM_plane2_dout[4], VRAM_plane2_dout[5], VRAM_plane2_dout[6], VRAM_plane2_dout[7]}));  // open: din
  // Probe on c_col
  // Probe on c_row
  S_R_Flip_Flop s_r_ff_3 (
    .S(counter_3_carry), .clk(p_clk), .R(1'b0), .Q(s_r_ff_3_q), .Qn(s_r_ff_3_qn), .preset(1'b0),
    .reset(counter_5_carry));
  Counter #(.max('h280), .width(10)) counter_5 (
    .load(1'b0), .count(s_r_ff_3_q), .Q({col, c_col}), .carry(counter_5_carry), .up(1'b1), .clk(p_clk),
    .clr(LINE_END));  // open: D
  S_R_Flip_Flop s_r_ff_4 (
    .S(counter_4_carry), .clk(LINE_END), .R(1'b0), .Q(s_r_ff_4_q), .Qn(s_r_ff_4_qn), .preset(1'b0),
    .reset(counter_6_carry));
  Counter #(.max('h1e0), .width(10)) counter_6 (
    .load(1'b0), .count(s_r_ff_4_q), .Q({row, c_row}), .carry(counter_6_carry), .up(1'b1), .clk(LINE_END),
    .clr(counter_8_carry));  // open: D
  or or_2 (or_2_out, clr_all_end, clr_YY_start);
  or or_3 (or_3_out, clr_all_start, clr_YY_end);
  S_R_Flip_Flop s_r_ff_5 (
    .S(counter_5_carry), .clk(p_clk), .R(1'b0), .Q(h_front_porch), .Qn(s_r_ff_5_qn), .preset(1'b0),
    .reset(LINE_END));
  S_R_Flip_Flop s_r_ff_6 (
    .S(counter_6_carry), .clk(LINE_END), .R(1'b0), .Q(v_front_porch), .Qn(s_r_ff_6_qn), .preset(1'b0),
    .reset(counter_8_carry));
  assign bit_extender_1_out = {{10{1'b0}}, col[7:3]};  // Bit_Extender bit_extender_1
  assign bit_extender_2_out = {{10{1'b0}}, row[8:4]};  // Bit_Extender bit_extender_2
  D_Flip_Flop d_ff_1 (.clk(clk), .D(clr_all_start), .Q(clr_all_mode), .Qn(d_ff_1_qn), .preset(1'b0), .reset(or_2_out));
  and and_8 (draw_mode, d_ff_1_qn, d_ff_2_qn);
  D_Flip_Flop d_ff_2 (.clk(clk), .D(clr_YY_start), .Q(clr_YY_mode), .Qn(d_ff_2_qn), .preset(1'b0), .reset(or_3_out));
  Counter #(.max('hf0)) counter_7 (
    .load(1'b0), .count(h_front_porch), .carry(LINE_END), .up(1'b1), .clk(p_clk), .clr(LINE_END));  // open: D, Q
  and and_9 (active_col, s_r_ff_5_qn, s_r_ff_3_qn, h_sync_pulse);
  and and_10 (active_row, v_sync_pulse, s_r_ff_4_qn, s_r_ff_6_qn);
  Counter #(.max('hb), .width(4)) counter_8 (
    .load(1'b0), .count(v_front_porch), .carry(counter_8_carry), .up(1'b1), .clk(LINE_END),
    .clr(counter_8_carry));  // open: D, Q
  Adder #(.width(15)) adder_1 (.a(bit_extender_1_out), .b(shifter_1_out), .out(addr_t), .cin(1'b0));  // open: cout
  Shifter #(.width(15)) shifter_1 (.in(bit_extender_2_out), .\dist (4'b0101), .out(shifter_1_out));
  and and_11 (active_video, s_r_ff_3_qn, s_r_ff_4_qn);
  BitSelector bitselector_1 (.in(VRAM_plane2_dout), .out(C), .sel(c_col));
  // Probe on bit_extender_1_out
  Register BG_C (.D(IOi[7:0]), .en(BG_WE), .clk(clk), .Q(BG_C_q), .clr(1'b0));
  Register FG_C (.D(IOi[7:0]), .en(FG_WE), .clk(clk), .Q(FG_C_q), .clr(1'b0));
  Counter u_col (
    .load(1'b0), .count(or_4_out), .Q(col_q), .carry(clr_YY_end), .up(1'b1), .clk(p_clk), .clr(or_5_out));  // open: D
  or or_4 (or_4_out, clr_all_mode, clr_YY_mode);
  or or_5 (or_5_out, clr_all_start, clr_YY_start);
  Counter u_row (
    .load(clr_YY_mode), .D(IOi[7:0]), .count(clr_YY_end), .Q(row_q), .carry(clr_all_end), .up(1'b1),
    .clk(p_clk), .clr(clr_all_start));
  Multiplexer #(.width(8)) multiplexer_5 (.in0(BG_C_q), .in1(FG_C_q), .out(multiplexer_5_out), .sel(C));
  assign bit_extender_3_out = {{7{1'b0}}, col_q};  // Bit_Extender bit_extender_3
  assign bit_extender_4_out = {{7{1'b0}}, row_q};  // Bit_Extender bit_extender_4
  not not_1 (HSYNC, h_sync_pulse);
  not not_2 (VSYNC, h_sync_pulse);
  Multiplexer #(.width(8)) multiplexer_6 (.in0({8{1'b0}}), .in1(multiplexer_5_out), .out(color8), .sel(active_video));
  Multiplexer #(.width(10)) multiplexer_7 (.in0({10{1'b0}}), .in1({col, c_col}), .out(DEBUG_x), .sel(active_video));
  Multiplexer #(.width(10)) multiplexer_8 (.in0({10{1'b0}}), .in1({row, c_row}), .out(DEBUG_y), .sel(active_video));
  Shifter #(.width(15)) shifter_2 (.in(bit_extender_4_out), .\dist (4'b1000), .out(shifter_2_out));
  Adder #(.width(15)) adder_2 (.a(bit_extender_3_out), .b(shifter_2_out), .out(clr_addr), .cin(1'b0));  // open: cout

  assign IOWE[0] = IOWE[1];

  // Other names for the same wires on the sheet: col[2:0] = c_col; data_in[7:0] = data; ext_w = datawe;
  //   CMD_YY[7:0] = IOi[7:0]; OE = DEBUG_WE; pixel_clk = p_clk; row[3:0] = c_row;
  //   w_addr[8:0] = {addr[11:8], addr[4:0]}

  // Notes on the sheet:
  //   Device Type (2)
  //   Command decoder
  //   hvalues:  0x60, 0x30, 0x280, 0xf0
  //   vvalues:  0x2, 0x1f, 0x1E0, 0xb
  //   add all lines in those  splitters
  //   VGA Synchronization
  //   Character Address Calculation
  //   Operation mode status
  //   clearning counters
  //   proper max: 0x280
  //   proper max: 0x1E0
endmodule
